// Logisim project C74-100 V1.circ as structural Verilog: 2 circuits, main circuit Main
module _6502 (
  input  PHI0,
  input  RDY,
  input  BE,
  input  nRS,
  input  nIRQ,
  input  nNMI,
  input  [7:0] D_IN,
  output R_W,
  output PHI1,
  output PHI2,
  output SYNC,
  output [7:0] D_OUT,
  output [15:0] A_BUS,
  output [7:0] AX_OUT
);

  wire _0_ADX, _0_ADX_D, _0_ALUA, _0_ALUA_D, _0_ALUB, _0_ALUB_D, _0_DOR, _0_DOR_D, _1_ADH, _1_ADH_D, _1_ADL,
       _1_ADL_D, _1_ADL_prime, _1_ALUC_D, _1_CC_ADH, _1_CC_ADL, _1_PC, _1_PC_D, _1_PC_E, _1_Rout_ADH,
       _4BIT_ALU, A7_WB, adder_1_cout, adder_4_cout, ADH_WE, ADL_WE, ADX_WE, ALUA7, ALUB6, ALUB7, ALUC,
       ALUC_q, and_1_out, and_2_out, and_3_out, and_4_out, and_5_out, and_8_out, and_14_out, and_17_out,
       and_18_out, and_19_out, and_20_out, B6, B6_WB, B7, B7_WB, BCD1, BCD2, BCD_WAIT, BRK_FLG, C, C_ALUC_D,
       CF, controlled_buffer_71_out, Cout, Cout_WB, D, d_ff_1_q, d_ff_2_q, d_ff_3_q, d_ff_4_qn, d_ff_6_qn,
       d_ff_7_q, d_ff_8_q, d_ff_8_qn, d_ff_10_q, d_ff_12_q, d_ff_13_q, d_ff_17_q, DB_ALUB, DB_ALUB_D,
       decoder_1_out0, decoder_1_out1, decoder_1_out2, decoder_1_out3, decoder_1_out4, decoder_1_out5,
       decoder_1_out6, decoder_1_out7, decoder_1_out8, decoder_1_out9, decoder_1_out10, decoder_1_out11,
       decoder_1_out12, decoder_1_out13, decoder_1_out14, decoder_1_out15, decoder_2_out0, decoder_2_out1,
       decoder_2_out2, decoder_2_out3, decoder_2_out4, decoder_2_out5, decoder_2_out6, decoder_2_out7,
       decoder_3_out0, decoder_3_out1, decoder_3_out2, decoder_3_out3, decoder_3_out4, decoder_3_out5,
       decoder_3_out6, decoder_3_out7, decoder_4_out0, decoder_4_out1, decoder_4_out2, decoder_4_out3,
       decoder_4_out4, decoder_4_out5, decoder_4_out6, decoder_4_out7, decoder_4_out8, decoder_4_out9,
       decoder_4_out10, decoder_4_out11, decoder_4_out12, decoder_4_out13, decoder_4_out14, decoder_4_out15,
       decoder_5_out0, decoder_5_out1, decoder_5_out2, decoder_5_out3, decoder_5_out4, decoder_5_out5,
       decoder_5_out6, decoder_5_out7, decoder_5_out8, decoder_5_out9, decoder_5_out10, decoder_5_out11,
       decoder_5_out12, decoder_5_out13, decoder_5_out14, decoder_5_out15, decoder_6_out0, decoder_6_out1,
       decoder_6_out2, decoder_6_out3, decoder_6_out4, decoder_6_out5, decoder_6_out6, decoder_6_out7,
       decoder_7_out0, decoder_7_out1, decoder_7_out2, decoder_7_out3, decoder_7_out4, decoder_7_out5,
       decoder_7_out6, decoder_7_out7, decoder_7_out8, decoder_7_out9, decoder_7_out10, decoder_7_out11,
       decoder_7_out12, decoder_7_out13, decoder_7_out14, decoder_7_out15, decoder_8_out0, decoder_8_out1,
       decoder_8_out2, decoder_8_out3, decoder_8_out4, decoder_8_out5, decoder_8_out6, decoder_8_out7,
       decoder_8_out8, decoder_8_out9, decoder_8_out10, decoder_8_out11, decoder_8_out12, decoder_8_out13,
       decoder_8_out14, decoder_8_out15, decoder_9_out0, decoder_9_out1, decoder_9_out2, decoder_9_out3,
       decoder_9_out4, decoder_9_out5, decoder_9_out6, decoder_9_out7, decoder_10_out0, decoder_10_out1,
       decoder_10_out2, decoder_10_out3, decoder_11_out0, decoder_11_out1, decoder_11_out2, decoder_11_out3,
       decoder_11_out4, decoder_11_out5, decoder_11_out6, decoder_11_out7, DF, EXIT_BTF, FetchOperand_SW, I,
       IF, multiplexer_4_out, multiplexer_8_out, multiplexer_9_out, multiplexer_10_out, multiplexer_11_out,
       multiplexer_12_out, multiplexer_13_out, multiplexer_22_out, multiplexer_23_out, multiplexer_24_out,
       multiplexer_25_out, multiplexer_26_out, multiplexer_27_out, multiplexer_28_out, multiplexer_39_out,
       multiplexer_40_out, multiplexer_41_out, multiplexer_45_out, multiplexer_46_out, multiplexer_47_out,
       multiplexer_48_out, multiplexer_52_out, multiplexer_53_out, multiplexer_56_out, multiplexer_57_out,
       multiplexer_58_out, multiplexer_59_out, multiplexer_60_out, multiplexer_61_out, multiplexer_62_out,
       multiplexer_63_out, multiplexer_65_out, N, nA_ALUA, nA_ALUA_D, nA_DOR, nA_DOR_D, nA_W, nA_WE, nAD_T,
       nADD_ALU, nADD_D_ALU, nADDR_ALU, nADH_1_DOR, nADH_1_DOR_D, nADL_1_ALUA, nADL_1_ALUA_D, nADL_ALUA,
       nand_2_out, nand_3_out, nand_4_out, nand_5_out, nand_9_out, nand_10_out, nand_11_out, nand_12_out,
       nand_13_out, nand_14_out, nAND_ALU, nB_ALUA, nB_ALUA_D, nB_DOR, nB_W, nB_WE, nBCD1, nBCD2, nBCD_ALU,
       nBIT_ALU, nBIT_WB, nC, nCF_W, nCF_WE, nCGL_ADL, nCLD, nCLD_WB, nCout_WB, nD, nDB_ADH, nDB_ADL,
       nDB_ADL_D, nDB_ADX, nDB_ALUB, nDB_ALUB_D, nDBR_ADX, nDBR_ALUB, nDBR_DOR, nDBR_W, nDBR_WE, nDF_W,
       nDF_WE, nDH_ADH, nDH_ADH_D, nDH_ALUA, nDH_DOR, nDH_W, nDH_WE, nEND, nEXIT_CC, NF, nFetchOpcode_SW,
       nFF_ADH, nFF_ALUA, nFF_ALUB, nFF_ALUB_D, nIF_W, nIF_WE, nINT_CLR, nINT_ON, nIRQ_PND, nIRQB, nML,
       nML_WR, nN, nNEXT, nNF_W, nNF_WE, nNMI_PND, nNMOS, nNONE_FLG, nNZ_FLG, nNZC_FLG, nNZCV_FLG, nNZV_FLG,
       NONE_W, nOPCODE_FLG, nor_1_out, nor_3_out, nor_11_out, nor_12_out, nor_13_out, nor_14_out, nOR_ALU,
       not_1_out, not_2_out, not_3_out, not_4_out, not_5_out, not_6_out, not_7_out, not_8_out, not_9_out,
       not_10_out, not_11_out, not_12_out, not_13_out, not_14_out, not_15_out, not_16_out, not_17_out,
       not_19_out, not_20_out, not_21_out, not_22_out, not_23_out, not_24_out, not_41_out, not_42_out,
       not_43_out, not_44_out, not_45_out, not_46_out, not_79_out, not_80_out, not_95_out, not_96_out,
       not_97_out, not_98_out, not_99_out, not_103_out, not_104_out, not_147_out, not_156_out, not_157_out,
       not_158_out, not_159_out, not_160_out, not_164_out, not_165_out, not_166_out, not_167_out,
       not_168_out, not_169_out, not_170_out, not_171_out, not_172_out, not_173_out, not_174_out,
       not_175_out, not_176_out, not_177_out, not_178_out, not_179_out, not_180_out, not_181_out,
       not_183_out, not_184_out, not_185_out, not_186_out, not_187_out, not_188_out, not_189_out,
       not_190_out, not_191_out, not_192_out, not_193_out, not_194_out, not_195_out, not_196_out,
       not_197_out, not_198_out, not_199_out, not_200_out, not_201_out, not_202_out, not_203_out,
       not_204_out, not_205_out, not_206_out, not_207_out, not_208_out, not_209_out, not_210_out,
       not_211_out, not_212_out, not_213_out, not_214_out, not_215_out, not_216_out, not_217_out,
       not_218_out, not_219_out, not_220_out, not_221_out, not_222_out, not_223_out, not_224_out,
       not_225_out, not_226_out, not_227_out, not_228_out, not_229_out, not_230_out, not_231_out,
       not_232_out, not_233_out, not_234_out, not_235_out, not_236_out, not_237_out, not_238_out,
       not_239_out, not_240_out, not_241_out, not_242_out, not_243_out, not_244_out, not_245_out,
       not_246_out, not_247_out, not_248_out, not_249_out, not_250_out, not_251_out, not_252_out,
       not_253_out, not_254_out, not_255_out, not_256_out, not_257_out, not_258_out, not_260_out,
       not_261_out, not_262_out, not_263_out, not_264_out, not_265_out, nP_ALUA, nP_DOR, nP_DOR_D, nP_VAL,
       nPBAC, nPBR_ADX, nPBR_DOR, nPBR_DOR_D, nPBR_W, nPBR_WE, nPC_Rout_ADH, nPCH_ADH, nPCH_ADH_P, nPCH_ALUA,
       nPCH_CC_ADH, nPCH_DOR, nPCL_ADL, nPCL_ADL_prime, nPCL_CC_ADL, nPCL_DOR, nR_ADL, nR_ALUB, nR_DOR,
       nREPEAT, nREPEAT_CS, nRES_PND, nRout_ADH, nRout_ADH_P, nRout_ADL, nRout_ADX, nRout_ALUA, nRout_DOR,
       nSE_ALUB, nSEI_CLD_FLG, nSH_ADH, nSH_ADH_D, nSH_ALUA, nSH_W, nSH_WE, nSHL_ALU, nSHR_ALU, nSO, nSP_ADL,
       nSP_ADL_D, nSP_ALUA, nSP_ALUA_D, nSP_W, nSP_WE, nSTP, nSTP_EN, nT_ADH, nT_ADL, nV, nVF_W, nVF_WE,
       nWAI, nX_ALUA, nX_ALUA_D, nX_DOR, nX_DOR_D, nX_W, nX_WE, nXCE, nXH_ALUA, nXH_DOR, nXH_W, nXH_WE,
       nXOR_ALU, nY_ALUA, nY_ALUA_D, nY_DOR, nY_DOR_D, nY_W, nY_WE, nYH_ALUA, nYH_DOR, nYH_W, nYH_WE, nZ,
       nZ16, nZ_FLG, nZF_W, nZF_WE, or_3_out, or_4_out, or_6_out, or_7_out, or_8_out, or_9_out, or_10_out,
       or_14_out, P_VAL, PHI11, PHI22, R_W_t, RDY_Flop_qn, RES_PND, SEI, SEI_WB, SF, SF_WB, STP_Flop_q,
       V_PRE, VF, WAI, WE, WE_ADH_D, WE_ADL_D, WE_ADL_prime, WE_ADX_D, WE_D, WE_E, xor_1_out, xor_2_out,
       xor_3_out, xor_5_out, Y6, Y6_WB, Y7, Y7_WB, ZF;
  wire [0:0] A_B_q, ALUC_2_q;
  wire [1:0] ALUC_MX, ALUOP_MX, END_MX, multiplexer_14_out;
  wire [2:0] ADX_MX, ALUB_MX, FLG_MX;
  wire [3:0] adder_3_out, adder_4_out, adder_5_out, ADH_MX, ADL_MX, ALUA_MX, DOR_MX, multiplexer_2_out,
       not_47_out, not_65_out, not_84_out, Q, Q_Counter_q, Save_Q_q, WB_MX;
  wire [5:0] ALUB_q;
  wire [6:0] ALUA_q, not_25_out, not_123_out, rom_2_data;
  wire [6:1] multiplexer_49_out, P;
  wire [7:0] A_q, adder_1_out, adder_2_out, ADH, ADH_q, ADL, ADL_q, ADX, ADX_q, ALUA, ALUA_2_q, ALUB,
       ALUB_2_q, and_12_out, and_16_out, B_q, bit_extender_1_out, DB, DBR_q, DH_q, DOR, DOR_q,
       multiplexer_1_out, not_182_out, OP, OP_IN, or_13_out, PBR_q, PCH_q, PCL_q, R, RF, RFout, Rout, SP_q,
       TH_q, TL_q, X_q, XH_q, xor_4_out, Y_q, YH_q;
  wire [7:3] MIR_2_q;
  wire [7:5] multiplexer_42_out;
  wire [7:7] and_7_out, FTM_q, not_259_out;
  wire [14:0] Synch_RAM_2_q, Synch_RAM_q;
  wire [15:15] RTM_q;
  wire [31:0] and_11_out, rom_1_data;

  Multiplexer #(.enable("false"), .width(8)) multiplexer_1 (
    .in0(OP), .in1(OP_IN), .out(multiplexer_1_out), .sel(not_1_out));
  not not_1 (not_1_out, nEND);
  not not_2 (not_2_out, nRS);
  Register #(.width(15)) Synch_RAM (.D({3'b100, multiplexer_1_out, Q}), .Q(Synch_RAM_q), .clk(PHI11));  // open: en, clr
  Register #(.width(15)) Synch_RAM_2 (
    .D({3'b100, multiplexer_1_out, Q}), .Q(Synch_RAM_2_q), .clk(PHI11));  // open: en, clr
  not not_3 (not_3_out, RDY);
  not not_4 (not_4_out, not_3_out);
  not not_5 (not_5_out, nREPEAT_CS);
  and and_1 (and_1_out, nIRQ_PND, nNMI_PND, nRES_PND);
  D_Flip_Flop #(.enable("true")) d_ff_1 (.clk(PHI1), .D(not_2_out), .Q(d_ff_1_q));  // open: Qn, preset, en, reset
  D_Flip_Flop #(.enable("true")) d_ff_2 (.clk(PHI11), .D(nML_WR), .Q(d_ff_2_q));  // open: Qn, preset, en, reset
  D_Flip_Flop #(.enable("true")) d_ff_3 (.clk(PHI11), .D(d_ff_2_q), .Q(d_ff_3_q));  // open: Qn, preset, en, reset
  ROM #(.addrWidth(15), .dataWidth(32)) rom_1 (.addr(Synch_RAM_q), .data(rom_1_data));
  ROM #(.addrWidth(15), .dataWidth(4)) rom_2 (.addr(Synch_RAM_q), .data(rom_2_data[3:0]));
  ROM #(.addrWidth(15), .dataWidth(32)) rom_3 (
    .addr(Synch_RAM_2_q),
    .data({_0_ALUA_D, nA_ALUA_D, nX_ALUA_D, nY_ALUA_D, nSP_ALUA_D, nADL_1_ALUA_D, nB_ALUA_D, nDB_ALUB_D, DB_ALUB_D, _0_ALUB_D, nFF_ALUB_D, _1_ALUC_D, C_ALUC_D, _1_ADL_D, nSP_ADL_D, nDB_ADL_D, WE_ADL_D, _1_ADH_D, nSH_ADH_D, nDH_ADH_D, WE_ADH_D, _0_ADX_D, WE_ADX_D, _1_PC_D, _0_DOR_D, nA_DOR_D, nX_DOR_D, nY_DOR_D, nADH_1_DOR_D, nP_DOR_D, nPBR_DOR_D, WE_D}));
  ROM #(.addrWidth(15), .dataWidth(4)) rom_4 (.addr(Synch_RAM_2_q), .data({EXIT_BTF, rom_2_data[6:4]}));
  not not_6 (not_6_out, nSTP_EN);
  nand nand_1 (nREPEAT, not_5_out, Cout_WB);
  not not_7 (not_7_out, nWAI);
  nand nand_2 (nand_2_out, not_7_out, and_2_out);
  and and_2 (and_2_out, nIRQB, nNMI_PND, nRES_PND);
  or or_1 (nINT_ON, and_1_out, nEND);
  D_Flip_Flop #(.enable("true")) d_ff_4 (.clk(PHI1), .D(d_ff_1_q), .Qn(d_ff_4_qn));  // open: Q, preset, en, reset
  not not_8 (not_8_out, d_ff_1_q);
  and and_3 (and_3_out, not_8_out, nINT_CLR);
  and and_4 (and_4_out, nRES_PND, nINT_CLR);
  not not_9 (not_9_out, PHI0);
  nand nand_3 (nand_3_out, not_6_out, nRES_PND);
  and and_5 (and_5_out, BCD_WAIT, RDY_Flop_qn);
  assign WAI = nand_2_out ? 1'b0 : 1'bz;  // Controlled_Buffer controlled_buffer_1
  D_Flip_Flop #(.enable("true")) d_ff_5 (
    .clk(d_ff_4_qn), .D(1'b1), .Q(RES_PND), .Qn(nRES_PND), .reset(not_10_out));  // open: preset, en
  not not_10 (not_10_out, and_3_out);
  not not_11 (not_11_out, nCGL_ADL);
  and and_6 (nML, d_ff_2_q, nML_WR, d_ff_3_q);
  not not_12 (not_12_out, not_9_out);
  D_Flip_Flop #(.enable("true")) STP_Flop (.clk(PHI1), .D(nand_3_out), .Q(STP_Flop_q));  // open: Qn, preset, en, reset
  D_Flip_Flop RDY_Flop (
    .clk(PHI2), .D(and_5_out), .Qn(RDY_Flop_qn), .preset(not_13_out), .reset(not_14_out));  // open: Q
  not not_13 (not_13_out, not_4_out);
  not not_14 (not_14_out, nRES_PND);
  D_Flip_Flop #(.enable("true")) d_ff_6 (
    .clk(and_4_out), .D(1'b0), .Qn(d_ff_6_qn), .preset(not_11_out));  // open: Q, en, reset
  not not_15 (not_15_out, nNMI);
  and and_7 (and_7_out[7], 1'b1, nFetchOpcode_SW);
  not not_16 (not_16_out, nEND);
  and and_8 (and_8_out, PHI1, d_ff_6_qn);
  D_Flip_Flop #(.enable("true")) d_ff_7 (.clk(PHI1), .D(not_15_out), .Q(d_ff_7_q));  // open: Qn, preset, en, reset
  D_Flip_Flop #(.enable("true")) d_ff_8 (
    .clk(PHI2), .D(not_17_out), .Q(d_ff_8_q), .Qn(d_ff_8_qn));  // open: preset, en, reset
  not not_17 (not_17_out, nSO);
  not not_18 (nNMOS, 1'b1);
  nand nand_4 (nand_4_out, 1'b1, not_12_out);
  nand nand_5 (nand_5_out, not_12_out, STP_Flop_q);
  Counter #(.max('hf), .width(4)) Q_Counter (
    .load(not_16_out), .D(4'b0001), .count(nREPEAT), .Q(Q_Counter_q), .clk(PHI11));  // open: carry, clr
  not not_19 (not_19_out, nSTP);
  D_Flip_Flop #(.enable("true")) d_ff_9 (.Qn(BRK_FLG), .preset(not_20_out), .reset(not_21_out));  // open: clk, D, Q, en
  not not_20 (not_20_out, nINT_ON);
  not not_21 (not_21_out, nINT_CLR);
  D_Flip_Flop #(.enable("true")) d_ff_10 (.clk(and_8_out), .D(d_ff_7_q), .Q(d_ff_10_q));  // open: Qn, preset, en, reset
  buf xor_1 (xor_1_out, d_ff_8_qn);  // XOR_Gate
  buf xor_2 (xor_2_out, xor_1_out);  // XOR_Gate
  assign DB = R_W_t ? D_IN : 8'bz;  // Controlled_Buffer controlled_buffer_2
  assign D_OUT = nor_1_out ? DB : 8'bz;  // Controlled_Buffer controlled_buffer_3
  nor nor_1 (nor_1_out, R_W_t, not_22_out, PHI1);
  not not_22 (not_22_out, BE);
  and and_9 (PHI1, 1'b1, nand_4_out);
  nand nand_6 (PHI2, nand_4_out, 1'b1);
  and and_10 (PHI11, RDY_Flop_qn, nand_5_out);
  nand nand_7 (PHI22, nand_5_out, RDY_Flop_qn);
  Register #(.width(4)) Save_Q (.D(Q_Counter_q), .Q(Save_Q_q), .clk(PHI11));  // open: en, clr
  Multiplexer #(.width(4)) multiplexer_2 (
    .in0(Save_Q_q), .in1(Q_Counter_q), .out(multiplexer_2_out), .sel(nREPEAT));  // open: en
  nand nand_8 (nSTP_EN, not_19_out, nRES_PND);
  D_Flip_Flop #(.enable("true")) d_ff_11 (
    .clk(d_ff_10_q), .D(1'b1), .Qn(nNMI_PND), .reset(not_23_out));  // open: Q, preset, en
  not not_23 (not_23_out, and_4_out);
  buf xor_3 (xor_3_out, xor_2_out);  // XOR_Gate
  assign and_11_out = rom_1_data & {32{and_7_out[7]}};  // AND_Gate and_11, 32 bits wide
  assign and_12_out = {EXIT_BTF, rom_2_data} & {8{and_7_out[7]}};  // AND_Gate and_12, 8 bits wide
  // Probe on DB
  // Probe on multiplexer_2_out
  D_Flip_Flop #(.enable("true")) d_ff_12 (.clk(PHI1), .D(nIRQ), .Q(d_ff_12_q));  // open: Qn, preset, en, reset
  buf buffer_1 (nIRQB, d_ff_12_q);
  and and_13 (V_PRE, d_ff_8_q, xor_3_out);
  Register #(.width(32)) MIR (
    .D(and_11_out), .en(nREPEAT),
    .Q({ALUA_MX, ALUB_MX, _1_PC_E, ALUC_MX, END_MX, ADL_MX, ADH_MX, ADX_MX, WE_E, DOR_MX, WB_MX}), .clk(PHI11));  // open: clr
  Register MIR_2 (
    .D(and_12_out), .en(nREPEAT), .Q({MIR_2_q[7], _4BIT_ALU, ALUOP_MX, MIR_2_q[3], FLG_MX}), .clk(PHI11));  // open: clr
  Multiplexer #(.width(4)) multiplexer_3 (.in0(4'b0000), .in1(multiplexer_2_out), .out(Q), .sel(nEND));  // open: en
  D_Flip_Flop #(.enable("true")) d_ff_13 (
    .clk(PHI1), .D(d_ff_12_q), .Q(d_ff_13_q), .reset(not_24_out));  // open: Qn, preset, en
  not not_24 (not_24_out, nRES_PND);
  or or_2 (nIRQ_PND, I, d_ff_13_q);
  or or_3 (or_3_out, FetchOperand_SW, BCD1);
  not not_25 (not_25_out[0], decoder_1_out0);
  not not_26 (not_25_out[1], decoder_1_out1);
  not not_27 (not_25_out[2], decoder_1_out2);
  not not_28 (not_25_out[3], decoder_1_out3);
  not not_29 (not_25_out[4], decoder_1_out4);
  not not_30 (nP_ALUA, decoder_1_out5);
  not not_31 (not_25_out[5], decoder_1_out6);
  not not_32 (nRout_ALUA, decoder_1_out7);
  not not_33 (nADL_ALUA, decoder_1_out8);
  not not_34 (nPCH_ALUA, decoder_1_out9);
  not not_35 (nFF_ALUA, decoder_1_out10);
  not not_36 (not_25_out[6], decoder_1_out11);
  not not_37 (nXH_ALUA, decoder_1_out12);
  not not_38 (nYH_ALUA, decoder_1_out13);
  not not_39 (nDH_ALUA, decoder_1_out14);
  not not_40 (nSH_ALUA, decoder_1_out15);
  Decoder #(.select(4)) decoder_1 (
    .out0(decoder_1_out0), .out1(decoder_1_out1), .out2(decoder_1_out2), .out3(decoder_1_out3),
    .out4(decoder_1_out4), .out5(decoder_1_out5), .out6(decoder_1_out6), .out7(decoder_1_out7),
    .out8(decoder_1_out8), .out9(decoder_1_out9), .out10(decoder_1_out10), .out11(decoder_1_out11),
    .out12(decoder_1_out12), .out13(decoder_1_out13), .out14(decoder_1_out14), .out15(decoder_1_out15),
    .sel(ALUA_MX), .en(not_41_out));
  not not_41 (not_41_out, FetchOperand_SW);
  Decoder #(.select(3)) decoder_2 (
    .out0(decoder_2_out0), .out1(decoder_2_out1), .out2(decoder_2_out2), .out3(decoder_2_out3),
    .out4(decoder_2_out4), .out5(decoder_2_out5), .out6(decoder_2_out6), .out7(decoder_2_out7),
    .sel(ALUB_MX), .en(not_42_out));
  not not_42 (not_42_out, or_3_out);
  Decoder #(.select(3)) decoder_3 (
    .out0(decoder_3_out0), .out1(decoder_3_out1), .out2(decoder_3_out2), .out3(decoder_3_out3),
    .out4(decoder_3_out4), .out5(decoder_3_out5), .out6(decoder_3_out6), .out7(decoder_3_out7),
    .sel({_4BIT_ALU, ALUOP_MX}), .en(not_43_out));
  not not_43 (not_43_out, FetchOperand_SW);
  Decoder #(.select(4)) decoder_4 (
    .out0(decoder_4_out0), .out1(decoder_4_out1), .out2(decoder_4_out2), .out3(decoder_4_out3),
    .out4(decoder_4_out4), .out5(decoder_4_out5), .out6(decoder_4_out6), .out7(decoder_4_out7),
    .out8(decoder_4_out8), .out9(decoder_4_out9), .out10(decoder_4_out10), .out11(decoder_4_out11),
    .out12(decoder_4_out12), .out13(decoder_4_out13), .out14(decoder_4_out14), .out15(decoder_4_out15),
    .sel(ADL_MX), .en(not_44_out));
  not not_44 (not_44_out, FetchOperand_SW);
  Decoder #(.select(4)) decoder_5 (
    .out0(decoder_5_out0), .out1(decoder_5_out1), .out2(decoder_5_out2), .out3(decoder_5_out3),
    .out4(decoder_5_out4), .out5(decoder_5_out5), .out6(decoder_5_out6), .out7(decoder_5_out7),
    .out8(decoder_5_out8), .out9(decoder_5_out9), .out10(decoder_5_out10), .out11(decoder_5_out11),
    .out12(decoder_5_out12), .out13(decoder_5_out13), .out14(decoder_5_out14), .out15(decoder_5_out15),
    .sel(ADH_MX), .en(not_45_out));
  not not_45 (not_45_out, FetchOperand_SW);
  not not_46 (not_46_out, nP_VAL);
  not not_47 (not_47_out[0], decoder_2_out0);
  not not_48 (not_47_out[1], decoder_2_out1);
  not not_49 (not_47_out[2], decoder_2_out2);
  not not_50 (not_47_out[3], decoder_2_out3);
  not not_51 (nSE_ALUB, decoder_2_out4);
  not not_52 (nDBR_ALUB, decoder_2_out5);
  not not_53 (nR_ALUB, decoder_2_out6);
  not not_54 (nZ16, decoder_2_out7);
  not not_55 (nADD_ALU, decoder_3_out0);
  not not_56 (nOR_ALU, decoder_3_out1);
  not not_57 (nXOR_ALU, decoder_3_out2);
  not not_58 (nBIT_ALU, decoder_3_out3);
  not not_59 (nAND_ALU, decoder_3_out4);
  not not_60 (nADD_D_ALU, decoder_3_out5);
  not not_61 (nSHL_ALU, decoder_3_out6);
  not not_62 (nSHR_ALU, decoder_3_out7);
  not not_63 (_1_ADL_prime, decoder_4_out0);
  not not_64 (WE_ADL_prime, decoder_4_out1);
  not not_65 (not_65_out[0], decoder_4_out2);
  not not_66 (nPCL_ADL_prime, decoder_4_out3);
  not not_67 (nRout_ADL, decoder_4_out4);
  not not_68 (nCGL_ADL, decoder_4_out5);
  not not_69 (not_65_out[1], decoder_4_out6);
  not not_70 (nR_ADL, decoder_4_out7);
  not not_71 (nT_ADL, decoder_4_out8);
  not not_72 (nPCL_CC_ADL, decoder_4_out9);
  not not_73 (_1_CC_ADL, decoder_4_out10);
  // NOT_Gate not_74 has open pins: in=decoder_4_out11, out=open
  // NOT_Gate not_75 has open pins: in=decoder_4_out12, out=open
  // NOT_Gate not_76 has open pins: in=decoder_4_out13, out=open
  // NOT_Gate not_77 has open pins: in=decoder_4_out14, out=open
  // NOT_Gate not_78 has open pins: in=decoder_4_out15, out=open
  not not_79 (not_79_out, decoder_5_out0);
  not not_80 (not_80_out, decoder_5_out1);
  not not_81 (nDB_ADH, decoder_5_out2);
  not not_82 (nPCH_ADH_P, decoder_5_out3);
  not not_83 (nRout_ADH_P, decoder_5_out4);
  not not_84 (not_84_out[0], decoder_5_out5);
  not not_85 (not_84_out[1], decoder_5_out6);
  not not_86 (nFF_ADH, decoder_5_out7);
  not not_87 (nT_ADH, decoder_5_out8);
  not not_88 (nPCH_CC_ADH, decoder_5_out9);
  not not_89 (_1_CC_ADH, decoder_5_out10);
  not not_90 (_1_Rout_ADH, decoder_5_out11);
  not not_91 (nPC_Rout_ADH, decoder_5_out12);
  not not_92 (nXCE, decoder_5_out13);
  not not_93 (nWAI, decoder_5_out14);
  not not_94 (nSTP, decoder_5_out15);
  Decoder #(.select(3)) decoder_6 (
    .out0(decoder_6_out0), .out1(decoder_6_out1), .out2(decoder_6_out2), .out3(decoder_6_out3),
    .out4(decoder_6_out4), .out5(decoder_6_out5), .out6(decoder_6_out6), .out7(decoder_6_out7), .sel(ADX_MX),
    .en(not_95_out));
  not not_95 (not_95_out, FetchOperand_SW);
  not not_96 (not_96_out, FetchOperand_SW);
  Decoder #(.select(4)) decoder_7 (
    .out0(decoder_7_out0), .out1(decoder_7_out1), .out2(decoder_7_out2), .out3(decoder_7_out3),
    .out4(decoder_7_out4), .out5(decoder_7_out5), .out6(decoder_7_out6), .out7(decoder_7_out7),
    .out8(decoder_7_out8), .out9(decoder_7_out9), .out10(decoder_7_out10), .out11(decoder_7_out11),
    .out12(decoder_7_out12), .out13(decoder_7_out13), .out14(decoder_7_out14), .out15(decoder_7_out15),
    .sel(WB_MX), .en(not_96_out));
  Decoder #(.select(4)) decoder_8 (
    .out0(decoder_8_out0), .out1(decoder_8_out1), .out2(decoder_8_out2), .out3(decoder_8_out3),
    .out4(decoder_8_out4), .out5(decoder_8_out5), .out6(decoder_8_out6), .out7(decoder_8_out7),
    .out8(decoder_8_out8), .out9(decoder_8_out9), .out10(decoder_8_out10), .out11(decoder_8_out11),
    .out12(decoder_8_out12), .out13(decoder_8_out13), .out14(decoder_8_out14), .out15(decoder_8_out15),
    .sel(DOR_MX), .en(not_97_out));
  not not_97 (not_97_out, FetchOperand_SW);
  not not_98 (not_98_out, FetchOperand_SW);
  Decoder #(.select(3)) decoder_9 (
    .out0(decoder_9_out0), .out1(decoder_9_out1), .out2(decoder_9_out2), .out3(decoder_9_out3),
    .out4(decoder_9_out4), .out5(decoder_9_out5), .out6(decoder_9_out6), .out7(decoder_9_out7), .sel(FLG_MX),
    .en(not_98_out));
  Decoder #(.select(2)) decoder_10 (
    .out0(decoder_10_out0), .out1(decoder_10_out1), .out2(decoder_10_out2), .out3(decoder_10_out3),
    .sel(OP[7:6]));  // open: en
  Multiplexer multiplexer_4 (.in0(_1_ALUC_D), .in1(C), .out(multiplexer_4_out), .sel(C_ALUC_D));  // open: en
  not not_99 (not_99_out, decoder_6_out0);
  not not_100 (nDBR_ADX, decoder_6_out1);
  not not_101 (nPBR_ADX, decoder_6_out2);
  not not_102 (multiplexer_14_out[1], decoder_6_out3);
  not not_103 (not_103_out, decoder_6_out4);
  not not_104 (not_104_out, decoder_6_out5);
  not not_105 (nDB_ADX, decoder_6_out6);
  not not_106 (nINT_CLR, decoder_6_out7);
  not not_107 (NONE_W, decoder_7_out0);
  not not_108 (nA_W, decoder_7_out1);
  not not_109 (nX_W, decoder_7_out2);
  not not_110 (nY_W, decoder_7_out3);
  not not_111 (nSP_W, decoder_7_out4);
  not not_112 (nPBR_W, decoder_7_out5);
  not not_113 (nDBR_W, decoder_7_out6);
  not not_114 (nSH_W, decoder_7_out7);
  not not_115 (nDH_W, decoder_7_out8);
  not not_116 (nB_W, decoder_7_out9);
  not not_117 (nXH_W, decoder_7_out10);
  not not_118 (nYH_W, decoder_7_out11);
  // NOT_Gate not_119 has open pins: in=decoder_7_out12, out=open
  not not_120 (nAD_T, decoder_7_out13);
  not not_121 (nP_VAL, decoder_7_out14);
  not not_122 (nPBAC, decoder_7_out15);
  not not_123 (not_123_out[0], decoder_8_out0);
  not not_124 (not_123_out[1], decoder_8_out1);
  not not_125 (not_123_out[2], decoder_8_out2);
  not not_126 (not_123_out[3], decoder_8_out3);
  not not_127 (nDH_DOR, decoder_8_out4);
  not not_128 (not_123_out[5], decoder_8_out5);
  not not_129 (nR_DOR, decoder_8_out6);
  not not_130 (nRout_DOR, decoder_8_out7);
  not not_131 (nPCL_DOR, decoder_8_out8);
  not not_132 (nPCH_DOR, decoder_8_out9);
  not not_133 (nDBR_DOR, decoder_8_out10);
  not not_134 (not_123_out[4], decoder_8_out11);
  not not_135 (nB_DOR, decoder_8_out12);
  not not_136 (nXH_DOR, decoder_8_out13);
  not not_137 (nYH_DOR, decoder_8_out14);
  not not_138 (not_123_out[6], decoder_8_out15);
  not not_139 (nEND, decoder_11_out0);
  not not_140 (nNEXT, decoder_11_out1);
  not not_141 (nEXIT_CC, decoder_11_out2);
  not not_142 (nREPEAT_CS, decoder_11_out3);
  // NOT_Gate not_143 has open pins: in=decoder_11_out4, out=open
  // NOT_Gate not_144 has open pins: in=decoder_11_out5, out=open
  // NOT_Gate not_145 has open pins: in=decoder_11_out6, out=open
  // NOT_Gate not_146 has open pins: in=decoder_11_out7, out=open
  Decoder #(.select(3)) decoder_11 (
    .out0(decoder_11_out0), .out1(decoder_11_out1), .out2(decoder_11_out2), .out3(decoder_11_out3),
    .out4(decoder_11_out4), .out5(decoder_11_out5), .out6(decoder_11_out6), .out7(decoder_11_out7),
    .sel({1'b0, END_MX}), .en(not_147_out));
  not not_147 (not_147_out, FetchOperand_SW);
  nor nor_2 (nNF_W, not_46_out, nor_3_out);
  nor nor_3 (nor_3_out, FetchOperand_SW, not_156_out);
  not not_148 (nNONE_FLG, decoder_9_out0);
  not not_149 (nOPCODE_FLG, decoder_9_out1);
  not not_150 (nSEI_CLD_FLG, decoder_9_out2);
  not not_151 (nZ_FLG, decoder_9_out3);
  not not_152 (nNZ_FLG, decoder_9_out4);
  not not_153 (nNZC_FLG, decoder_9_out5);
  not not_154 (nNZCV_FLG, decoder_9_out6);
  not not_155 (nNZV_FLG, decoder_9_out7);
  not not_156 (not_156_out, FLG_MX[2]);
  not not_157 (not_157_out, decoder_10_out0);
  not not_158 (not_158_out, decoder_10_out1);
  not not_159 (not_159_out, decoder_10_out2);
  not not_160 (not_160_out, decoder_10_out3);
  not not_161 (SF, nOPCODE_FLG);
  Multiplexer #(.select(3)) multiplexer_5 (
    .in0(ALUC_MX[0]), .in1(ALUC_MX[0]), .in2(C), .in3(Cout), .in4(multiplexer_4_out),
    .in5(multiplexer_4_out), .in6(multiplexer_4_out), .in7(multiplexer_4_out), .out(ALUC),
    .sel({FetchOperand_SW, ALUC_MX}));  // open: en
  Multiplexer multiplexer_6 (.in0(_1_PC_E), .in1(_1_PC_D), .out(_1_PC), .sel(FetchOperand_SW));  // open: en
  Multiplexer multiplexer_7 (.in0(WE_E), .in1(WE_D), .out(WE), .sel(FetchOperand_SW));  // open: en
  not not_162 (SYNC, nEND);
  nor nor_4 (nZF_W, not_46_out, nand_9_out);
  nor nor_5 (nCF_W, not_46_out, nand_10_out);
  nand nand_9 (nand_9_out, nZ_FLG, or_4_out);
  or or_4 (or_4_out, not_156_out, FetchOperand_SW);
  not not_163 (SEI, nSEI_CLD_FLG);
  or or_5 (nCLD, nSEI_CLD_FLG, 1'b1);
  nor nor_6 (nVF_W, not_46_out, nand_11_out);
  nand nand_10 (nand_10_out, nNZC_FLG, nNZCV_FLG, or_6_out);
  nand nand_11 (nand_11_out, nNZCV_FLG, nNZV_FLG, or_7_out);
  or or_6 (or_6_out, nOPCODE_FLG, not_157_out);
  or or_7 (or_7_out, nOPCODE_FLG, not_159_out);
  nor nor_7 (nIF_W, not_46_out, nand_12_out);
  nor nor_8 (nDF_W, not_46_out, nand_13_out);
  nand nand_12 (nand_12_out, nSEI_CLD_FLG, or_8_out);
  or or_8 (or_8_out, nOPCODE_FLG, not_158_out);
  or or_9 (or_9_out, nOPCODE_FLG, not_160_out);
  Multiplexer #(.enable("false")) multiplexer_8 (.in0(Cout_WB), .in1(1'b0), .out(multiplexer_8_out), .sel(not_104_out));
  Multiplexer #(.enable("false")) multiplexer_9 (
    .in0(nCout_WB), .in1(1'b1), .out(multiplexer_9_out), .sel(not_104_out));
  nand nand_13 (nand_13_out, or_9_out, nCLD);
  Multiplexer #(.enable("false")) multiplexer_10 (
    .in0(nCout_WB), .in1(multiplexer_11_out), .out(multiplexer_10_out), .sel(nPCL_CC_ADL));
  Multiplexer #(.enable("false")) multiplexer_11 (
    .in0(nCout_WB), .in1(nPCL_CC_ADL), .out(multiplexer_11_out), .sel(_1_CC_ADL));
  Multiplexer #(.enable("false")) multiplexer_12 (.in0(Cout_WB), .in1(1'b1), .out(multiplexer_12_out), .sel(_1_CC_ADL));
  Multiplexer #(.enable("false")) multiplexer_13 (
    .in0(Cout_WB), .in1(1'b1), .out(multiplexer_13_out), .sel(nPCL_CC_ADL));
  Multiplexer #(.enable("false")) multiplexer_14 (
    .in0(multiplexer_8_out), .in1(1'b1), .out(multiplexer_14_out[0]), .sel(not_99_out));
  Multiplexer #(.enable("false")) multiplexer_15 (
    .in0(1'b0), .in1(multiplexer_9_out), .out(nRout_ADX), .sel(not_103_out));
  Multiplexer #(.width(7)) multiplexer_16 (
    .in0(not_123_out), .in1({nADH_1_DOR_D, nP_DOR_D, nPBR_DOR_D, nY_DOR_D, nX_DOR_D, nA_DOR_D, _0_DOR_D}),
    .out({nADH_1_DOR, nP_DOR, nPBR_DOR, nY_DOR, nX_DOR, nA_DOR, _0_DOR}), .sel(FetchOperand_SW));  // open: en
  Multiplexer #(.width(7)) multiplexer_17 (
    .in0(not_25_out),
    .in1({nB_ALUA_D, nADL_1_ALUA_D, nSP_ALUA_D, nY_ALUA_D, nX_ALUA_D, nA_ALUA_D, _0_ALUA_D}),
    .out({nB_ALUA, nADL_1_ALUA, nSP_ALUA, nY_ALUA, nX_ALUA, nA_ALUA, _0_ALUA}), .sel(FetchOperand_SW));  // open: en
  Multiplexer #(.width(4)) multiplexer_18 (
    .in0(not_47_out), .in1({nFF_ALUB_D, _0_ALUB_D, DB_ALUB_D, nDB_ALUB_D}),
    .out({nFF_ALUB, _0_ALUB, DB_ALUB, nDB_ALUB}), .sel(FetchOperand_SW));  // open: en
  Multiplexer #(.enable("false")) multiplexer_19 (
    .in0(1'b0), .in1(multiplexer_10_out), .out(not_65_out[2]), .sel(WE_ADL_prime));
  Multiplexer #(.enable("false")) multiplexer_20 (
    .in0(1'b0), .in1(multiplexer_12_out), .out(not_65_out[3]), .sel(_1_ADL_prime));
  Multiplexer #(.enable("false")) multiplexer_21 (
    .in0(1'b0), .in1(multiplexer_13_out), .out(nPCL_ADL), .sel(nPCL_ADL_prime));
  Multiplexer #(.enable("false")) multiplexer_22 (
    .in0(1'b0), .in1(nPCH_CC_ADH), .out(multiplexer_22_out), .sel(_1_CC_ADH));
  Multiplexer #(.enable("false")) multiplexer_23 (
    .in0(nCout_WB), .in1(multiplexer_24_out), .out(multiplexer_23_out), .sel(nPC_Rout_ADH));
  Multiplexer #(.enable("false")) multiplexer_24 (
    .in0(nCout_WB), .in1(1'b1), .out(multiplexer_24_out), .sel(_1_Rout_ADH));
  Multiplexer #(.enable("false")) multiplexer_25 (
    .in0(Cout_WB), .in1(multiplexer_26_out), .out(multiplexer_25_out), .sel(_1_CC_ADH));
  Multiplexer #(.enable("false")) multiplexer_26 (
    .in0(Cout_WB), .in1(1'b1), .out(multiplexer_26_out), .sel(_1_Rout_ADH));
  Multiplexer #(.enable("false")) multiplexer_27 (
    .in0(Cout_WB), .in1(multiplexer_28_out), .out(multiplexer_27_out), .sel(nPC_Rout_ADH));
  Multiplexer #(.enable("false")) multiplexer_28 (
    .in0(Cout_WB), .in1(1'b1), .out(multiplexer_28_out), .sel(nPCH_CC_ADH));
  Multiplexer #(.width(2)) multiplexer_29 (
    .in0(multiplexer_14_out), .in1({WE_ADX_D, _0_ADX_D}), .out({_0_ADX, ADX_WE}), .sel(FetchOperand_SW));  // open: en
  Multiplexer #(.enable("false")) multiplexer_30 (
    .in0(nCout_WB), .in1(multiplexer_22_out), .out(not_84_out[2]), .sel(not_80_out));
  Multiplexer #(.enable("false")) multiplexer_31 (
    .in0(1'b0), .in1(multiplexer_23_out), .out(nRout_ADH), .sel(nRout_ADH_P));
  Multiplexer #(.enable("false")) multiplexer_32 (
    .in0(1'b0), .in1(multiplexer_25_out), .out(not_84_out[3]), .sel(not_79_out));
  Multiplexer #(.enable("false")) multiplexer_33 (
    .in0(1'b0), .in1(multiplexer_27_out), .out(nPCH_ADH), .sel(nPCH_ADH_P));
  Multiplexer #(.width(4)) multiplexer_34 (
    .in0(not_65_out), .in1({_1_ADL_D, WE_ADL_D, nSP_ADL_D, nDB_ADL_D}),
    .out({_1_ADL, ADL_WE, nSP_ADL, nDB_ADL}), .sel(FetchOperand_SW));  // open: en
  Multiplexer #(.width(4)) multiplexer_35 (
    .in0(not_84_out), .in1({_1_ADH_D, WE_ADH_D, nDH_ADH_D, nSH_ADH_D}),
    .out({_1_ADH, ADH_WE, nDH_ADH, nSH_ADH}), .sel(FetchOperand_SW));  // open: en
  not not_164 (not_164_out, BE);
  or or_10 (or_10_out, R_W_t, not_164_out);
  // Probe on Rout
  // Probe on Rout
  // Probe on DB
  // Probe on R
  // Probe on DB
  // Probe on R
  not not_165 (not_165_out, or_10_out);
  assign DB = not_165_out ? DOR_q : 8'bz;  // Controlled_Buffer controlled_buffer_4
  Multiplexer #(.width(8)) multiplexer_36 (.in0({8{1'b0}}), .in1(DB), .out(OP_IN), .sel(nINT_ON));  // open: en
  not not_166 (not_166_out, nA_WE);
  not not_167 (not_167_out, nB_WE);
  not not_168 (not_168_out, nX_WE);
  not not_169 (not_169_out, nXH_WE);
  not not_170 (not_170_out, nY_WE);
  not not_171 (not_171_out, nYH_WE);
  not not_172 (not_172_out, nSP_WE);
  not not_173 (not_173_out, nAD_T);
  not not_174 (not_174_out, _1_PC);
  not not_175 (not_175_out, _1_PC);
  not not_176 (not_176_out, nSH_WE);
  not not_177 (not_177_out, nDH_WE);
  not not_178 (not_178_out, nDBR_WE);
  not not_179 (not_179_out, nDBR_WE);
  not not_180 (not_180_out, nAD_T);
  // Probe on OP_IN
  not not_181 (not_181_out, nEND);
  assign not_182_out = ~DB;  // NOT_Gate not_182, 8 bits wide
  assign bit_extender_1_out = {{7{ALUB7}}, ALUB7};  // Bit_Extender bit_extender_1
  not not_183 (not_183_out, nA_ALUA);
  Register A (.D(R), .en(not_166_out), .Q(A_q), .clk(PHI22));  // open: clr
  not not_184 (not_184_out, nA_DOR);
  not not_185 (not_185_out, nB_ALUA);
  Register B (.D(R), .en(not_167_out), .Q(B_q), .clk(PHI22));  // open: clr
  not not_186 (not_186_out, nB_DOR);
  not not_187 (not_187_out, nX_ALUA);
  Register X (.D(R), .en(not_168_out), .Q(X_q), .clk(PHI22));  // open: clr
  not not_188 (not_188_out, nX_DOR);
  not not_189 (not_189_out, nXH_ALUA);
  Register XH (.D(R), .en(not_169_out), .Q(XH_q), .clk(PHI22));  // open: clr
  not not_190 (not_190_out, nXH_DOR);
  not not_191 (not_191_out, nY_ALUA);
  Register Y (.D(R), .en(not_170_out), .Q(Y_q), .clk(PHI22));  // open: clr
  not not_192 (not_192_out, nY_DOR);
  not not_193 (not_193_out, nYH_ALUA);
  Register YH (.D(R), .en(not_171_out), .Q(YH_q), .clk(PHI22));  // open: clr
  not not_194 (not_194_out, nYH_DOR);
  not not_195 (not_195_out, nSP_ALUA);
  Register SP (.D(R), .en(not_172_out), .Q(SP_q), .clk(PHI22));  // open: clr
  not not_196 (not_196_out, nSP_ADL);
  not not_197 (not_197_out, nRout_ALUA);
  not not_198 (not_198_out, nT_ADL);
  Register TL (.D(ADL), .en(not_173_out), .Q(TL_q), .clk(PHI11));  // open: clr
  not not_199 (not_199_out, nP_ALUA);
  not not_200 (not_200_out, nP_DOR);
  not not_201 (not_201_out, _0_ALUA);
  not not_202 (not_202_out, nPCL_DOR);
  Register PCL (.D(adder_1_out), .en(not_174_out), .Q(PCL_q), .clk(PHI11));  // open: clr
  not not_203 (not_203_out, nPCL_ADL);
  not not_204 (not_204_out, nRout_ADL);
  not not_205 (not_205_out, nR_ADL);
  not not_206 (not_206_out, nDB_ADL);
  not not_207 (not_207_out, nDB_ADH);
  not not_208 (not_208_out, nRout_ADH);
  not not_209 (not_209_out, nPCH_ALUA);
  Register PCH (.D(adder_2_out), .en(not_175_out), .Q(PCH_q), .clk(PHI11));  // open: clr
  not not_210 (not_210_out, nPCH_DOR);
  not not_211 (not_211_out, nPCH_ADH);
  not not_212 (not_212_out, nFF_ADH);
  not not_213 (not_213_out, nSH_ALUA);
  not not_214 (not_214_out, nSH_ADH);
  not not_215 (not_215_out, nDH_DOR);
  not not_216 (not_216_out, nDH_ALUA);
  Register DH (.D(R), .en(not_177_out), .Q(DH_q), .clk(PHI22));  // open: clr
  not not_217 (not_217_out, nDH_ADH);
  not not_218 (not_218_out, nDBR_ALUB);
  Register DBR (.D(R), .en(not_178_out), .Q(DBR_q), .clk(PHI22));  // open: clr
  not not_219 (not_219_out, nDBR_DOR);
  not not_220 (not_220_out, nDBR_ADX);
  not not_221 (not_221_out, nDBR_DOR);
  Register PBR (.D(R), .en(not_179_out), .Q(PBR_q), .clk(PHI22));  // open: clr
  not not_222 (not_222_out, nDBR_ADX);
  not not_223 (not_223_out, _0_ADX);
  assign ADX = not_223_out ? {8{1'b0}} : 8'bz;  // Controlled_Buffer controlled_buffer_5
  not not_224 (not_224_out, nRout_ADX);
  assign ADX = not_224_out ? Rout : 8'bz;  // Controlled_Buffer controlled_buffer_6
  assign ADX = not_225_out ? DB : 8'bz;  // Controlled_Buffer controlled_buffer_7
  not not_225 (not_225_out, nDB_ADX);
  not not_226 (not_226_out, nT_ADH);
  Register TH (.D(ADH), .en(not_180_out), .Q(TH_q), .clk(PHI11));  // open: clr
  Register IR (.D(OP_IN), .en(not_181_out), .Q(OP), .clk(PHI11));  // open: clr
  not not_227 (not_227_out, nR_ALUB);
  assign ALUB = not_227_out ? R : 8'bz;  // Controlled_Buffer controlled_buffer_8
  not not_228 (not_228_out, nDB_ALUB);
  assign ALUB = not_228_out ? DB : 8'bz;  // Controlled_Buffer controlled_buffer_9
  not not_229 (not_229_out, DB_ALUB);
  assign ALUB = not_229_out ? not_182_out : 8'bz;  // Controlled_Buffer controlled_buffer_10
  not not_230 (not_230_out, nSE_ALUB);
  assign ALUB = not_230_out ? bit_extender_1_out : 8'bz;  // Controlled_Buffer controlled_buffer_11
  not not_231 (not_231_out, _0_ALUB);
  assign ALUB = not_231_out ? {8{1'b0}} : 8'bz;  // Controlled_Buffer controlled_buffer_12
  not not_232 (not_232_out, nFF_ALUB);
  assign ALUB = not_232_out ? {8{1'b1}} : 8'bz;  // Controlled_Buffer controlled_buffer_13
  not not_233 (not_233_out, nFF_ALUA);
  assign ALUA = not_233_out ? {8{1'b1}} : 8'bz;  // Controlled_Buffer controlled_buffer_14
  // Probe on ALUA
  assign ALUA = not_183_out ? A_q : 8'bz;  // Controlled_Buffer controlled_buffer_15
  assign DOR = not_184_out ? A_q : 8'bz;  // Controlled_Buffer controlled_buffer_16
  assign ALUA = not_185_out ? B_q : 8'bz;  // Controlled_Buffer controlled_buffer_17
  assign DOR = not_186_out ? B_q : 8'bz;  // Controlled_Buffer controlled_buffer_18
  assign ALUA = not_187_out ? X_q : 8'bz;  // Controlled_Buffer controlled_buffer_19
  assign DOR = not_188_out ? X_q : 8'bz;  // Controlled_Buffer controlled_buffer_20
  assign ALUA = not_189_out ? XH_q : 8'bz;  // Controlled_Buffer controlled_buffer_21
  assign DOR = not_190_out ? XH_q : 8'bz;  // Controlled_Buffer controlled_buffer_22
  assign ALUA = not_191_out ? Y_q : 8'bz;  // Controlled_Buffer controlled_buffer_23
  assign DOR = not_192_out ? Y_q : 8'bz;  // Controlled_Buffer controlled_buffer_24
  assign ALUA = not_193_out ? YH_q : 8'bz;  // Controlled_Buffer controlled_buffer_25
  assign DOR = not_194_out ? YH_q : 8'bz;  // Controlled_Buffer controlled_buffer_26
  assign ALUA = not_195_out ? SP_q : 8'bz;  // Controlled_Buffer controlled_buffer_27
  assign ADL = not_196_out ? SP_q : 8'bz;  // Controlled_Buffer controlled_buffer_28
  assign ADL = not_234_out ? {{5{1'b1}}, nNMI_PND, nRES_PND, 1'b0} : 8'bz;  // Controlled_Buffer controlled_buffer_29
  not not_234 (not_234_out, nCGL_ADL);
  assign ALUA = not_197_out ? Rout : 8'bz;  // Controlled_Buffer controlled_buffer_30
  assign ADL = not_198_out ? TL_q : 8'bz;  // Controlled_Buffer controlled_buffer_31
  assign ALUA = not_199_out ? {N, P[6], 1'b1, BRK_FLG, D, I, P[1], C} : 8'bz;  // Controlled_Buffer controlled_buffer_32
  assign DOR = not_200_out ? {N, P[6], 1'b1, BRK_FLG, D, I, P[1], C} : 8'bz;  // Controlled_Buffer controlled_buffer_33
  assign ALUA = not_201_out ? {8{1'b0}} : 8'bz;  // Controlled_Buffer controlled_buffer_34
  not not_235 (not_235_out, nR_DOR);
  assign DOR = not_235_out ? R : 8'bz;  // Controlled_Buffer controlled_buffer_35
  not not_236 (not_236_out, nRout_DOR);
  assign DOR = not_236_out ? Rout : 8'bz;  // Controlled_Buffer controlled_buffer_36
  not not_237 (not_237_out, _0_DOR);
  assign DOR = not_237_out ? {8{1'b0}} : 8'bz;  // Controlled_Buffer controlled_buffer_37
  assign DOR = not_202_out ? PCL_q : 8'bz;  // Controlled_Buffer controlled_buffer_38
  assign ADL = not_203_out ? PCL_q : 8'bz;  // Controlled_Buffer controlled_buffer_39
  assign ADL = not_204_out ? Rout : 8'bz;  // Controlled_Buffer controlled_buffer_40
  assign ADL = not_205_out ? R : 8'bz;  // Controlled_Buffer controlled_buffer_41
  assign ADL = not_206_out ? DB : 8'bz;  // Controlled_Buffer controlled_buffer_42
  assign ADH = not_207_out ? DB : 8'bz;  // Controlled_Buffer controlled_buffer_43
  assign ADH = not_208_out ? Rout : 8'bz;  // Controlled_Buffer controlled_buffer_44
  assign ALUA = not_209_out ? PCH_q : 8'bz;  // Controlled_Buffer controlled_buffer_45
  assign DOR = not_210_out ? PCH_q : 8'bz;  // Controlled_Buffer controlled_buffer_46
  assign ADH = not_211_out ? PCH_q : 8'bz;  // Controlled_Buffer controlled_buffer_47
  assign ADH = not_212_out ? {8{1'b1}} : 8'bz;  // Controlled_Buffer controlled_buffer_48
  assign ALUA = not_213_out ? 8'h1 : 8'bz;  // Controlled_Buffer controlled_buffer_49
  assign ADH = not_214_out ? 8'h1 : 8'bz;  // Controlled_Buffer controlled_buffer_50
  assign DOR = not_215_out ? DH_q : 8'bz;  // Controlled_Buffer controlled_buffer_51
  assign ALUA = not_216_out ? DH_q : 8'bz;  // Controlled_Buffer controlled_buffer_52
  assign ADH = not_217_out ? DH_q : 8'bz;  // Controlled_Buffer controlled_buffer_53
  assign ALUB = not_218_out ? DBR_q : 8'bz;  // Controlled_Buffer controlled_buffer_54
  assign DOR = not_219_out ? DBR_q : 8'bz;  // Controlled_Buffer controlled_buffer_55
  assign ADX = not_220_out ? DBR_q : 8'bz;  // Controlled_Buffer controlled_buffer_56
  assign DOR = not_221_out ? PBR_q : 8'bz;  // Controlled_Buffer controlled_buffer_57
  assign ADX = not_222_out ? PBR_q : 8'bz;  // Controlled_Buffer controlled_buffer_58
  assign ADH = not_226_out ? TH_q : 8'bz;  // Controlled_Buffer controlled_buffer_59
  // Probe on ALUB
  // Probe on ALUA
  // Probe on DOR
  // Probe on ADL
  // Probe on DOR
  // Probe on ADH
  // Probe on ADX
  assign ALUA = not_238_out ? adder_1_out : 8'bz;  // Controlled_Buffer controlled_buffer_60
  assign ADL = not_239_out ? adder_1_out : 8'bz;  // Controlled_Buffer controlled_buffer_61
  assign ALUA = not_240_out ? ADL_q : 8'bz;  // Controlled_Buffer controlled_buffer_62
  assign ADH = not_241_out ? adder_2_out : 8'bz;  // Controlled_Buffer controlled_buffer_63
  assign DOR = not_242_out ? adder_2_out : 8'bz;  // Controlled_Buffer controlled_buffer_64
  not not_238 (not_238_out, nADL_1_ALUA);
  not not_239 (not_239_out, _1_ADL);
  not not_240 (not_240_out, nADL_ALUA);
  not not_241 (not_241_out, _1_ADH);
  not not_242 (not_242_out, nADH_1_DOR);
  Multiplexer #(.enable("false")) multiplexer_37 (.in0(DB[6]), .in1(ALUB[6]), .out(B6), .sel(DB_ALUB));
  Multiplexer #(.enable("false")) multiplexer_38 (.in0(DB[7]), .in1(ALUB[7]), .out(B7), .sel(DB_ALUB));
  // Probe on ADL
  // Probe on ADH
  Register u_DOR (.D(DOR), .Q(DOR_q), .clk(PHI11));  // open: en, clr
  Register u_ADL (.D(ADL), .en(ADL_WE), .Q(ADL_q), .clk(PHI11));  // open: clr
  Register u_ADH (.D(ADH), .en(ADH_WE), .Q(ADH_q), .clk(PHI11));  // open: clr
  not not_243 (not_243_out, nRES_PND);
  Register u_ADX (.D(ADX), .en(ADX_WE), .Q(ADX_q), .clk(PHI11));  // open: clr
  Adder adder_1 (.a({8{1'b0}}), .b(ADL_q), .out(adder_1_out), .cin(1'b1), .cout(adder_1_cout));
  Adder adder_2 (.a(ADH_q), .b({8{1'b0}}), .out(adder_2_out), .cin(adder_1_cout));  // open: cout
  D_Flip_Flop #(.enable("true")) d_ff_14 (.clk(PHI11), .D(WE), .Qn(R_W_t), .reset(not_243_out));  // open: Q, preset, en
  assign A_BUS[7:0] = BE ? ADL_q : 8'bz;  // Controlled_Buffer controlled_buffer_65
  assign A_BUS[15:8] = BE ? ADH_q : 8'bz;  // Controlled_Buffer controlled_buffer_66
  assign R_W = BE ? R_W_t : 1'bz;  // Controlled_Buffer controlled_buffer_67
  // Probe on A_BUS
  assign AX_OUT = BE ? ADX_q : 8'bz;  // Controlled_Buffer controlled_buffer_68
  // Probe on AX_OUT
  or or_11 (nBCD_ALU, nADD_D_ALU, not_244_out);
  not not_244 (not_244_out, D);
  and and_14 (and_14_out, BCD_WAIT, nBCD2);
  D_Flip_Flop #(.enable("true")) d_ff_15 (.clk(PHI1), .D(and_14_out), .Q(BCD2), .Qn(nBCD2));  // open: preset, en, reset
  and and_15 (nADDR_ALU, nADD_ALU, nADD_D_ALU);
  nor nor_9 (BCD_WAIT, nADD_D_ALU, not_244_out);
  or or_12 (nBCD1, nBCD_ALU, BCD2);
  nor nor_10 (BCD1, nBCD_ALU, BCD2);
  not not_245 (not_245_out, OP[7]);
  nand nand_14 (nand_14_out, D, _4BIT_ALU);
  // Probe on ALUA
  // Probe on ALUB
  assign ALUB = not_246_out ? {1'b0, multiplexer_49_out, 1'b0} : 8'bz;  // Controlled_Buffer controlled_buffer_69
  not not_246 (not_246_out, nBCD1);
  // Probe on {1'b0, multiplexer_49_out, 1'b0}
  Register #(.width(1)) u_ALUC (.D(ALUC), .Q(ALUC_q), .clk(PHI1));  // open: en, clr
  Register u_ALUA (.D(ALUA), .Q({ALUA7, ALUA_q}), .clk(PHI1));  // open: en, clr
  Register u_ALUB (.D(ALUB), .Q({Y7, Y6, ALUB_q}), .clk(PHI1));  // open: en, clr
  Register #(.width(1)) ALUC_2 (.D(ALUC), .Q(ALUC_2_q[0]), .clk(PHI1));  // open: en, clr
  Register ALUA_2 (.D(ALUA), .Q(ALUA_2_q), .clk(PHI1));  // open: en, clr
  Register ALUB_2 (.D(ALUB), .Q(ALUB_2_q), .clk(PHI1));  // open: en, clr
  Register #(.width(2)) ALUB6__7 (.D({B7, B6}), .Q({ALUB7, ALUB6}), .clk(PHI1));  // open: en, clr
  Multiplexer #(.select(2)) multiplexer_39 (
    .in0(OP[7]), .in1(ALUB_q[5]), .in2(not_245_out), .in3(not_245_out), .out(multiplexer_39_out),
    .sel({Y6, ALUA7}));  // open: en
  Multiplexer multiplexer_40 (.in0(multiplexer_39_out), .in1(1'b0), .out(multiplexer_40_out), .sel(OP[7]));  // open: en
  Multiplexer multiplexer_41 (.in0(1'b0), .in1(multiplexer_39_out), .out(multiplexer_41_out), .sel(OP[7]));  // open: en
  Multiplexer multiplexer_42 (
    .in0(ALUB_q[5]), .in1(multiplexer_39_out), .out(multiplexer_42_out[5]), .sel(BCD2));  // open: en
  Multiplexer multiplexer_43 (.in0(Y6), .in1(multiplexer_40_out), .out(multiplexer_42_out[6]), .sel(BCD2));  // open: en
  Multiplexer multiplexer_44 (.in0(Y7), .in1(multiplexer_41_out), .out(multiplexer_42_out[7]), .sel(BCD2));  // open: en
  // Probe on {ALUA7, ALUA_q}
  // Probe on {multiplexer_42_out, ALUB_q[4:0]}
  Adder #(.width(4)) adder_3 (.a(ALUA_2_q[7:4]), .b(4'b0000), .out(adder_3_out), .cin(ALUB_q[1]));  // open: cout
  // Probe on {adder_3_out, ALUA_2_q[3:0]}
  assign or_13_out = ALUA_2_q | ALUB_2_q;  // OR_Gate or_13, 8 bits wide
  assign and_16_out = ALUA_2_q & ALUB_2_q;  // AND_Gate and_16, 8 bits wide
  assign xor_4_out = ALUA_2_q ^ ALUB_2_q;  // XOR_Gate xor_4, 8 bits wide
  Adder #(.width(4)) adder_4 (.a(ALUA_q[3:0]), .b(ALUB_q[3:0]), .out(adder_4_out), .cin(ALUC_q), .cout(adder_4_cout));
  Multiplexer #(.enable("false")) multiplexer_45 (
    .in0(1'b0), .in1(adder_4_cout), .out(multiplexer_45_out), .sel(nand_14_out));
  Adder #(.width(4)) adder_5 (
    .a({ALUA7, ALUA_q[6:4]}), .b({multiplexer_42_out, ALUB_q[4]}), .out(adder_5_out),
    .cin(multiplexer_45_out), .cout(multiplexer_49_out[6]));
  assign multiplexer_49_out[4] = not_247_out ? multiplexer_46_out : 1'bz;  // Controlled_Buffer controlled_buffer_70
  Multiplexer #(.select(3)) multiplexer_46 (
    .in0(1'b0), .in1(1'b0), .in2(1'b0), .in3(1'b0), .in4(1'b0), .in5(not_245_out), .in6(not_245_out),
    .in7(not_245_out), .out(multiplexer_46_out), .sel(adder_4_out[3:1]), .en(not_247_out));
  not not_247 (not_247_out, adder_4_cout);
  assign controlled_buffer_71_out = not_248_out ? multiplexer_47_out : 1'bz;  // Controlled_Buffer controlled_buffer_71
  Multiplexer #(.select(3)) multiplexer_47 (
    .in0(1'b1), .in1(1'b1), .in2(1'b1), .in3(1'b1), .in4(1'b1), .in5(OP[7]), .in6(OP[7]), .in7(OP[7]),
    .out(multiplexer_47_out), .sel(adder_4_out[3:1]), .en(not_248_out));
  not not_248 (not_248_out, adder_4_cout);
  not not_249 (not_249_out, multiplexer_39_out);
  assign multiplexer_49_out[4] = adder_4_cout ? 1'b1 : 1'bz;  // Controlled_Buffer controlled_buffer_72
  assign controlled_buffer_71_out = adder_4_cout ? 1'b0 : 1'bz;  // Controlled_Buffer controlled_buffer_73
  Multiplexer multiplexer_48 (
    .in0(multiplexer_39_out), .in1(not_249_out), .out(multiplexer_48_out), .sel(OP[7]));  // open: en
  Multiplexer multiplexer_49 (
    .in0(multiplexer_49_out[4]), .in1(controlled_buffer_71_out), .out(multiplexer_49_out[1]), .sel(OP[7]));  // open: en
  Multiplexer multiplexer_50 (
    .in0(multiplexer_49_out[4]), .in1(1'b0), .out(multiplexer_49_out[2]), .sel(OP[7]));  // open: en
  Multiplexer multiplexer_51 (
    .in0(1'b0), .in1(controlled_buffer_71_out), .out(multiplexer_49_out[3]), .sel(OP[7]));  // open: en
  Multiplexer multiplexer_52 (
    .in0(multiplexer_49_out[4]), .in1(1'b1), .out(multiplexer_52_out), .sel(OP[7]));  // open: en
  Multiplexer multiplexer_53 (
    .in0(1'b1), .in1(controlled_buffer_71_out), .out(multiplexer_53_out), .sel(OP[7]));  // open: en
  // Probe on or_13_out
  // Probe on and_16_out
  // Probe on {adder_5_out, adder_4_out}
  Multiplexer #(.select(3)) multiplexer_54 (
    .in0(multiplexer_49_out[6]), .in1(multiplexer_49_out[6]), .in2(or_13_out[7]), .in3(or_13_out[0]),
    .in4(multiplexer_49_out[6]), .in5(multiplexer_48_out), .in6(or_13_out[7]), .in7(or_13_out[0]),
    .out(Cout), .sel({D, ALUOP_MX}));  // open: en
  // Probe on {or_13_out[6:0], ALUC_2_q[0]}
  // Probe on {ALUC_2_q[0], or_13_out[7:1]}
  // Probe on xor_4_out
  Multiplexer #(.select(3)) multiplexer_55 (
    .in0(OP[7]), .in1(multiplexer_52_out), .in2(1'b1), .in3(1'b1), .in4(1'b1), .in5(1'b1), .in6(1'b1),
    .in7(multiplexer_53_out), .out(multiplexer_49_out[5]), .sel(adder_5_out[2:0]));  // open: en
  and and_17 (and_17_out, nAND_ALU, nBIT_ALU);
  not not_250 (not_250_out, nADDR_ALU);
  assign Rout = not_250_out ? {adder_5_out, adder_4_out} : 8'bz;  // Controlled_Buffer controlled_buffer_74
  assign Rout = not_251_out ? {or_13_out[6:0], ALUC_2_q[0]} : 8'bz;  // Controlled_Buffer controlled_buffer_75
  not not_251 (not_251_out, nSHL_ALU);
  assign Rout = not_252_out ? {ALUC_2_q[0], or_13_out[7:1]} : 8'bz;  // Controlled_Buffer controlled_buffer_76
  not not_252 (not_252_out, nSHR_ALU);
  assign Rout = not_253_out ? or_13_out : 8'bz;  // Controlled_Buffer controlled_buffer_77
  not not_253 (not_253_out, nOR_ALU);
  assign Rout = not_254_out ? and_16_out : 8'bz;  // Controlled_Buffer controlled_buffer_78
  not not_254 (not_254_out, and_17_out);
  assign Rout = not_255_out ? xor_4_out : 8'bz;  // Controlled_Buffer controlled_buffer_79
  not not_255 (not_255_out, nXOR_ALU);
  assign RFout = not_256_out ? {adder_3_out, ALUA_2_q[3:0]} : 8'bz;  // Controlled_Buffer controlled_buffer_80
  not not_256 (not_256_out, or_14_out);
  or or_14 (or_14_out, nNMOS, nBCD_ALU);
  assign RFout = not_257_out ? Rout : 8'bz;  // Controlled_Buffer controlled_buffer_81
  not not_257 (not_257_out, not_256_out);
  not not_258 (not_258_out, multiplexer_49_out[6]);
  Multiplexer #(.select(2)) multiplexer_56 (
    .in0(multiplexer_49_out[6]), .in1(not_258_out), .in2(1'b1), .in3(1'b1), .out(multiplexer_56_out),
    .sel({nEXIT_CC, ALUB7}));  // open: en
  Multiplexer multiplexer_57 (.in0(nN), .in1(N), .out(multiplexer_57_out), .sel(OP[5]));  // open: en
  Multiplexer multiplexer_58 (
    .in0(multiplexer_57_out), .in1(multiplexer_59_out), .out(multiplexer_58_out), .sel(OP[6]));  // open: en
  Multiplexer multiplexer_59 (.in0(nV), .in1(P[6]), .out(multiplexer_59_out), .sel(OP[5]));  // open: en
  Multiplexer multiplexer_60 (.in0(nC), .in1(C), .out(multiplexer_60_out), .sel(OP[5]));  // open: en
  Multiplexer multiplexer_61 (
    .in0(multiplexer_60_out), .in1(multiplexer_62_out), .out(multiplexer_61_out), .sel(OP[6]));  // open: en
  Multiplexer multiplexer_62 (.in0(nZ), .in1(P[1]), .out(multiplexer_62_out), .sel(OP[5]));  // open: en
  Multiplexer multiplexer_63 (
    .in0(multiplexer_58_out), .in1(multiplexer_61_out), .out(multiplexer_63_out), .sel(OP[7]));  // open: en
  // Probe on Rout
  // Probe on RFout
  not not_259 (not_259_out[7], nP_VAL);
  Multiplexer multiplexer_64 (
    .in0(multiplexer_56_out), .in1(multiplexer_63_out), .out(nFetchOpcode_SW), .sel(EXIT_BTF));  // open: en
  Register u_R (.D(Rout), .Q(R), .clk(PHI11));  // open: en, clr
  Register u_RF (.D(RFout), .Q(RF), .clk(PHI11));  // open: en, clr
  Register FTM (
    .D({{2{not_259_out[7]}}, nNF_W, nVF_W, nDF_W, nIF_W, nZF_W, nCF_W}),
    .Q({FTM_q[7], P_VAL, nNF_WE, nVF_WE, nDF_WE, nIF_WE, nZF_WE, nCF_WE}), .clk(PHI11));  // open: en, clr
  Register #(.width(16)) RTM (
    .D({3'b000, SF, nBIT_ALU, nYH_W, nXH_W, nB_W, nDH_W, nSH_W, nDBR_W, nPBR_W, nSP_W, nY_W, nX_W, nA_W}),
    .Q({{3{RTM_q[15]}}, SF_WB, nBIT_WB, nYH_WE, nXH_WE, nB_WE, nDH_WE, nSH_WE, nDBR_WE, nPBR_WE, nSP_WE, nY_WE, nX_WE, nA_WE}),
    .clk(PHI11));  // open: en, clr
  Register A_B (
    .D({nCLD, SEI, Y7, Y6, ALUB7, ALUB6, {2{ALUA7}}}),
    .Q({nCLD_WB, SEI_WB, Y7_WB, Y6_WB, B7_WB, B6_WB, A7_WB, A_B_q[0]}), .clk(PHI11));  // open: en, clr
  D_Flip_Flop d_ff_16 (.clk(PHI11), .D(Cout), .Q(Cout_WB), .Qn(nCout_WB));  // open: preset, reset
  D_Flip_Flop #(.enable("true")) d_ff_17 (
    .clk(PHI11), .D(nFetchOpcode_SW), .Q(d_ff_17_q));  // open: Qn, preset, en, reset
  and and_18 (and_18_out, d_ff_17_q, nEND);
  D_Flip_Flop #(.enable("true")) d_ff_18 (
    .clk(PHI11), .D(and_18_out), .Qn(FetchOperand_SW));  // open: Q, preset, en, reset
  and and_19 (and_19_out, A7_WB, Y7_WB);
  nor nor_11 (nor_11_out, A7_WB, Y7_WB);
  xor xor_5 (xor_5_out, Y7_WB, Y6_WB);
  nor nor_12 (nor_12_out, RF[0], RF[1], RF[2]);
  nor nor_13 (nor_13_out, RF[3], RF[4], RF[5]);
  nor nor_14 (nor_14_out, RF[6], RF[7], RF[7]);
  or or_15 (IF, RF[2], SEI_WB);
  Multiplexer multiplexer_65 (.in0(and_19_out), .in1(nor_11_out), .out(multiplexer_65_out), .sel(RF[7]));  // open: en
  and and_20 (and_20_out, nor_12_out, nor_13_out, nor_14_out);
  Multiplexer multiplexer_66 (.in0(and_20_out), .in1(RF[1]), .out(ZF), .sel(P_VAL));  // open: en
  Multiplexer #(.select(3)) multiplexer_67 (
    .in0(B6_WB), .in1(multiplexer_65_out), .in2(1'b0), .in3(RF[6]), .in4(1'b0), .in5(RF[6]), .in6(1'b0),
    .in7(xor_5_out), .out(VF), .sel({P_VAL, SF_WB, nBIT_WB}));  // open: en
  Multiplexer multiplexer_68 (.in0(B7_WB), .in1(RF[7]), .out(NF), .sel(nBIT_WB));  // open: en
  and and_21 (DF, RF[3], nCLD_WB);
  Multiplexer #(.select(2)) multiplexer_69 (
    .in0(Cout_WB), .in1(RF[0]), .in2(RF[0]), .in3(RF[0]), .out(CF), .sel({P_VAL, SF_WB}));  // open: en
  not not_260 (not_260_out, nCF_WE);
  not not_261 (not_261_out, nZF_WE);
  not not_262 (not_262_out, nIF_WE);
  not not_263 (not_263_out, nDF_WE);
  not not_264 (not_264_out, nVF_WE);
  not not_265 (not_265_out, nNF_WE);
  D_Flip_Flop #(.enable("true")) d_ff_19 (.clk(PHI2), .D(CF), .Q(C), .Qn(nC), .en(not_260_out));  // open: preset, reset
  D_Flip_Flop #(.enable("true")) d_ff_20 (
    .clk(PHI2), .D(ZF), .Q(P[1]), .Qn(nZ), .en(not_261_out));  // open: preset, reset
  D_Flip_Flop #(.enable("true")) d_ff_21 (.clk(PHI2), .D(IF), .Q(I), .en(not_262_out));  // open: Qn, preset, reset
  D_Flip_Flop #(.enable("true")) d_ff_22 (.clk(PHI2), .D(DF), .Q(D), .Qn(nD), .en(not_263_out));  // open: preset, reset
  D_Flip_Flop #(.enable("true")) d_ff_23 (
    .clk(PHI2), .D(VF), .Q(P[6]), .Qn(nV), .en(not_264_out));  // open: preset, reset
  D_Flip_Flop #(.enable("true")) d_ff_24 (.clk(PHI2), .D(NF), .Q(N), .Qn(nN), .en(not_265_out));  // open: preset, reset
  // Probe on {N, P[6], 1'b1, BRK_FLG, D, I, P[1], C}
  // Probe on {N, P[6], 1'b1, BRK_FLG, D, I, P[1], C}
  // also tied to GND on the sheet: RTM_q[15]

  // Other names for the same wires on the sheet: ALUOP_MX[2] = _4BIT_ALU; AX_BUS[7:0] = AX_OUT; nRES = nRS;
  //   nIR_WE = nEND; nSYNC = nEND; P (some bits) = {N, BRK_FLG, D, I, C}; Z = P[1]; V = P[6]; R_W_Pin = R_W

  // Notes on the sheet:
  //   OPCODE (From IR)
  //   74CBTLV3257
  //   From WAI / STP below
  //   From ALU
  //   From ADH.MX
  //   74UC14
  //   74UC14
  //   From END.MX
  //   74UC14
  //   REPEAT (if CS)
  //   Inhibit Q, Inhibit MIR
  //   ML Detector
  //   contents of rom_1 (hex, n*v repeats v):
  //   compressed eJztXVly5LgO/Mcp9N1fWqtax3G53Pc/wpPEFStBeXriTYQnYsLtKnEDwSTITMHP57RO0z4Oz+sf
  //   v9M/tnHYpu35GNdhGs//jl/X+fz5dfy//xrhuW3r43H8Mh3P1w9MUyzxmqZlWcdpWK/f96OmX6n+
  //   /ajA2+JV7Phle1S1A699PmufwgPnc8d/z3FYY235m1f8Brb06Fm/0evl+vr85T1M7+tfV9npcXZr
  //   HM+f01kqtJufPn6+00ie66fd+TDGs45j/Nvxy2u8nq0eWQ+rv7arA/jTYX1Oj+25HoPcTlOOVVVX
  //   59fDkocpocM6Q7LOftYfyxtGmstj1FhDNBZwY52jjjZaiY1YG3CZdt+/krtN61XHaYAlOeE7tfl6
  //   P9fQl+Xj40M1eSo3vVPXl4+X3vrp9Nv5NW/wnOPZ7P8u+uejOQNnRw/bpdXWmoL4mNdfx2C+UOk7
  //   eez0TrNhmi/8MgaPzYVf7cKnMWVffoVhr/HTJ1yfTo/oWzcMeBle7ZxgyOl6/ip6Pn21tozHw8yl
  //   uT3Ptj7H0Bb4mlqvnu9rweA1Ll/IEDhH53Mg7lg77Zjr/1oz9PKGCmLFVRgq2C7TUehlzYTuTaWO
  //   yxSQnWNh+DoyfN29/urH15FtPWUkYdTh26/QhQS4QNxRctLncws1nXMylUGvsfBvCoi59+FnNs2s
  //   oiuzb64Mm+o76Dr+s+jKDG6jK2s9W9WLriNB1wokDXtTKBU6j6BUtndyTeiFUm2Vpi6aUKpY7vWU
  //   vPRPAEDyaaobWN3MWlMb1UcZOIcGcHJvrYFz8I26Wnzp57mGj/V8LeXh94bQbA076Y3AdX4UGGwF
  //   QQmaNimoBAx6aZOOG9f7Xfat8ycCPWiBnhJvh9jwleLticSGYpg5BNDbh9fX5/Vt2IRRfLomq20Y
  //   6LQBiwFiY+DQFSAOCMKgE8KEiK8rQBwQhMGNAPFaAhGSLqvei/mg7U4mUIERrjSByio8ZW98pxBk
  //   wd4IrxTz5m10rZZUXMzXr1twXx3MrLCOolPbZBY6KeFthU7jFdAmnNnSeGYbjfY06W9hFvYxRkrB
  //   os9k0Uf8RzHiGrpTYh9SL16iFy6jLfSaAa0zgIFsdwBZit6AA5k54hwdhMla46Tt8akp9P8VJsmF
  //   Z3z/GKe6Q7/TTKH94wSxstwqIFwQwqkGE4GwabizZQaEqr2kWA78QCiYHwwglFpnsRwIQKj1P8Vy
  //   zzE7ZBVmLQgaVRvMxTHB55gWJL4M2zQhUS08CX4dEfEVn1qCx3yJsdwBSdOcbDoSp1zPtmc5hDN7
  //   pJ19W0aUz75mU+KBQwbFELocJnjRedv3d6lkTZ5+At4TldmRAx2fvgnOAa9/Tc9+ckxMPhIGfE7B
  //   W+3jO0ToSxz+q97Zykn5mlNxpgPMf1T75RqxaFmk0SQwWsQeLansLI1uwUGXNKjgWD3Hxd9j9JhJ
  //   MrMUavGnrg3TPiTK4x0ToCyxcWar61vNVuHbOZZltpJxYywDTrWSs+LbPJ/lIEW32lTcJd+XISfK
  //   7haWxDXlBVPplPc1LD8u1B4OazR6IqYhlcdjyQJouRjBUuyKGMPHyub46ceQ8eFhlp1/kW/R+l3o
  //   t0pYlMtW7S8cP1LUAVqdwWdeZGLjLZVyd3U9S8at3II9gAQw2rh5/KKRMUpdVX9mKarRhv/NoEaw
  //   Jg9qXIc7M6ZReo+vpyqrMduSp+RDH4hPUdv+tUOeecb6I7pdBLsZ8KcsNME3PpVtzjsQ+3EhkLE6
  //   jrooQRStHFDlc3LcZCoLoY6Wt/DY8iaXbKe5Z3TQ+EIAZRS9pvj4dhK/PTd5vey52D/S+ePj8uMr
  //   pvv9O2M4utw0792VVuL9zSaFPqL5PkOURJzk8Jyv7IwJVBa1TQQ9pu3SU8kOoNmBhBIUsmIjwBrp
  //   uFOHDFnLM7id6CkcsZ77p9q250Zdq2CvJ/wIPkOhsYT8l10QFrWMfT3FnA5sYxs36tFSfOyOC3W1
  //   bLmm+kyXKjO5ND1m8s+YbunofUD6QW6rajwC2gtuMeGy6iPgkcdLxesqc8QuNCt85JKO3Yt0Hpbg
  //   DHLYoZc93WRW8CyGVHrh6+stuBYxkMCN2XBGGgE0us+AZ2R/e83k4mkZy4VmdUm1VrgzWwsGCoaZ
  //   BsuP4bE3VhWDMHXIN3jBY67SqV/0Dw5irwuDlNZdKKb1/4Kxx1Wcoxe6SopVgGrm8JjsYv10oGYi
  //   Fx2oFxavlEKfPuJTcwo0r2qvJoDdJAUI3N9FLHCOtNYKJDDY5cBM9QAObTBd0KQa1QQ2y9mCMVoS
  //   NyADihK3tuBCUcW0W0wXP6bETaF7ks7luv92irhkiZvCRrYkLt9hI5OwRZe4KYqLJHEDW+LmEACC
  //   JXFrGB/YxX3TWAVsoZPBxHeiSycTSR6HFnHJlG0EYg3e2yds43bP13JtrwdF2NYwfIJfgWsy3bRG
  //   X2jbe9bcFqiabehVs8ne6uoSiHcTPg0bv5UxXZZJ2CAry25K2HDIdUPCFivYhhsSNmBKGL+EDVz4
  //   adz+qY00JWzQA6hMwga4yh4JG8jo6ZOwPVvq1JaErStUpeipqJi+rVz77wrXbKhs6NYa1gre0qVW
  //   yzWGWwrRML5m/xocMu+hwoIzWppawjTj7lAF31qYpmM0tIVpBMqCaRxKIj+UqcK0QRSmKVhGhRzp
  //   grAI08AnTBOBCbJPNAfOgckabxuY4F5YR3CsTVmowMQr2InTqJEaE/nhSK1hS+iBH8bgtOGHTTY+
  //   g3QqzpzRoIw1Pp2ZgjU/MrPsUT8ys/+MzMwpFzNQ0KUuq14cuSEuq7CoX1yWrApOcZnmj+DRliXr
  //   vLB18OJSDglL8B2qJINIxFo6MhJmvdKWI5mFQl+KQrHvgQ/6VPfWd9SWeIxwmlQ8VrhXSTyWgCjV
  //   sP2qn8FYVj0jXpfpYrE8X1fRGhzGHo1YJfpZaPd82jBcpqEJCzuN8/x1fjuJwjIpyhGbEvQYXUow
  //   PDpwKcCIRcT7JUMEKE0bNPs8/1JkXlA7SkvdtdatCJousnblmohgR3UD5MJ5SQKPPtL61m/h5rAM
  //   WnKthMn18XAJVmodduoiMxJ3CsFDu8Nx3coHmHpMbikWHZQq1DLeuKGjJCJPW3nWc37pO758+/QS
  //   5qmhtxLsF780Bj2rVQTzgbGlt70kqgeaVpvpQkAelIvvnw86wqaJZ60C5B5e2gIFKvqK79FBFSF3
  //   W16yLBvRC1zr+J7+qVswgFsBNCgEhaLOIlo9vfUlq52E/udriy6Vk2e0hsqJCzN6rl2j2ohbSkYH
  //   /PRQPy0owTVtEyu/1yGZpW0qAKBOsaltUpns1q2HtUzkSw/VVuzOI8qXBr98KcyxqyXCGvotIhwA
  //   DMdWEScfJf8drRLp1hVu3NIoCdfyXRol6VY+bhKiNGmg0qRyWojSJB1wLLmQIUlqLIaWJEkOR5T3
  //   fFVpEapFEIBbjzdOHLZYiwuRoECNJETS9V5hZ3UaV6Z3oOlI6vUDGEYyrh9i0FSrjozUJ+yIkMmQ
  //   sUYisyNUwOA1mAhEpjP+HY1RvdFM3oYGyV4VRVSv6ik4HlchbPV1GC8U7zfSfk9uuxZbHkTqmsru
  //   VMe3U4Su9bP6zc5zBYYIaENnU/lQNLFjlzLAWTo60XF1vB8H1dsq+/5BrSNcpQavz91O0op2airS
  //   ySsfhm4sfBkquE6dlsowluM1FDRiDDpCApLLSoBsjd3GlN1YQ1bel8XzAjW8lNdkp+lDNEH9bgnL
  //   CYUH0cTDMtkmahB7RvkM9GeAquUzgpcL+DCS+08UXqRbYBE1tGBHaHfS95mYzik3y2FEzd5USEAi
  //   arFCIXFdFKWLH0QEyO99yTYK/W6AiOvlWhVEqtsUyVYmhpSypq0cOepuYAhe0QhD7OxJdcKTuiYv  hCBJSh+EDCp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
  //   contents of rom_2 (hex, n*v repeats v):
  //   compressed eJztWEuS6yAM3OsUXmcVA8aZ+1/sBYSkbsBvLjCVqpnEfPRrdYOv1/tIx1m+/8r3c176O73e0n+3
  //   gXy8j/b3PPHp9f2ct66TVG0DG8q5rZRYCcNyqaH2JPtQtt19r1ONS98iTRYk5r2/X87j/Axn2Fr/
  //   cqMzaXGmzM6kjznTwri/H5sjS/CHBi9rXvrvW25wxGdcwwDFrwYo/rBNBjB2idg50+KxP0TAcYvG
  //   rTH9ACKETFqtY5/ygckPGV3Lmww8uuoAUGhFxaMabuW8rMhop0rVqfX76RG0LxxBf5Jsn2RPKJS2
  //   T5goY04zIX1ytlVjQ+mh0D461PYBcPriXkt1IhdwU3Pn22cvQism1vBIyWLI7xnt98dMeF18TkVc
  //   4yrhZolVUib4wj5RMJwhDgVEgIRJAvh/DSzNPZEQ+iubXbxxTqvLZ3zpHe4Q8kJ3YqGd+xBlglsn
  //   2T7zUKA0u/VsNa7mxg2roj/cqEbeDdS0GHCTFB61AYUnjlEPr8H3JAgZ1o2KqAkioxdONUuCbXEk
  //   N4Bl1cnQ4dEW7XNb45TZqY6JvVhFcVCstqSsBMY6pmJlSsNi1QDhWOZek41YfTfZiNWKZ2+ytMXz
  //   6sw1o5PESp2ZxUqLvhGrjY6pWH3lai9W3cDKNRHX+XqUGRZqodg36eQILuwvIpS9WEV/YbiRiUms
  //   KKPP5U334g+LVU+jgDc5YYo2YtV0YytWEQGKlSJlI1atv1axemMbLV0pG7EyIjidGCznQ7sz6Z5F
  //   JChV3RGrn5BQeXYt3/dY8gN5FJSfHFuCSEyiJrMGGZyvrUKddlb7DcrTUnIMWziUfMxn+5PhsXur
  //   788rhCiSeU0HDyMECRniGVaXZaHAxB6sr/CSowBNHB0CJK6CIUBUEhCgHtROflQtZCM+XnbSE/NC
  //   /DGzfttKIX5MEBcUHiAjFh7QvjHDV1yIUkd7wjpKoppnH1NuGAhNAYRWgpZ5mhnMmFUDJgAn3Rpw
  //   HFx9vvxoMOPPBMQaw1ZewEoyOGpwPs2Urfv6UHYLrKcG4W2iuGdfMAqzt4tCFlMRhQTTvmdPZXa/
  //   BD0JpZ0djhvQ6mncssxspj0hv87nzbO4S4zDjvFaxrGiCyCjDeG62UDigGw/uFZysBIgsFfwjiGY
  //   w2rdfDuLUWlTUi/zcty+/Zr9iSrCsT4OsgD1Egmeb+dBJnWarzQWvxHBEynPJ4lYVJ8bZjpz7Z0u
  //   sQLuD72+13STdhCMI/t8kIxjVNots9P2GLWxzr4yVAI15qIG+tJzpimjmclxB2boQAncFbs+sOPV
  //   U173i/Sq+whWQ17ZgBXvBoOCwX8Z+xD5xuuplXyf2j8XnwlcWh3hodcr+UKLM/ne0cYL+ToO62ui
  //   LeePBy5Vnt2Rr71O2pGvX9j4DJLAgrf/Jgqhs5Yl+vakPEUhO/Id2hGJBvKNm1CmQ9Zwarx2e/Q0
  //   7AEkD3+btpJvvP5ZyTfGVvKN1z2DLQnPBIhKqayes8GfwxD4OVGvnZnHOiPeooNwSA7uxBtbIBda
  //   uOAZVuYsI6rj12/dsKz7vRv29mrs6cfgDibmwwc2nQ4CdGbGUPStC4wpZQKPWgwXxaA8GocEWx7u
  //   CrFoCKrt+QlQFBuzE16dFxit+nuUFW9SKZ+Etxgz9gyvJY6uwBiJavTHnhDFH3v+secfe/6x5wCa  /AO58uVy
  //   contents of rom_3 (hex, n*v repeats v):
  //   compressed eJztXcF22zgMvOMrfO5ps23j9nNiS/r/T1glWcmSCHAGAGU7sXvqi2RaIsHBABjCw/H8u3sbusOv
  //   H8PQH4+/h/5w7Pufp/OxP8x/mf/zZ7zr89+hm+56nT8pfy+Xh/DAw+vnXbL45MvL5fppOL32b+Mo
  //   xx/ax4/D2+fl4kvkMty/yv2X9zj8ZS/Lx2uOT6S80svPxTPbb764TU7D2/hHdNv7M33eZszQNM/y
  //   ZzH35WX0cX2CZb78e/Hxfxbr92a+q7YA43hDdQGmy9bXvRZPK3+W1nKuWUsH5mK6LsDYTOPZrOfL
  //   r8uL92AiR7NirGEyGgFGM32bbhRd+TCyfJjO/fHVu4zfPsLB+JDGdQVNNkbw8XHDJGcbsCzaxATD
  //   JH33I5AAVjIczXVWn44Dk3e7GLD5yPztCA3468KjyYFFE8W69aXg0MSyQwVNHHAhLJwg36X71ONw
  //   tuHkgOHkzODEcKR80AyMaEOj6yqeCPr4aLWj3zWXGZCT0Qo2O2g5kRBNZp9QbMSNl46BToSIaJxg
  //   tQ1J0Bg6a/VlbSQftKdDRMX8UlFvCxGSy3q0ISQXjGhGSFT6VLeeeyYmiH8WNFac1qGvCw05IYoi
  //   M6TEKMrobasEiuQoQ2U2ROUccY4iPLwgljDCy8lw0xt4ITjJjO7mDnRTkpWXbkRJFPPOUBJoOMkI
  //   BnHjUPyboySKVcnm2TxcxNrZOS4CQyOvf0GZE+dwCrBsJ3Fcwb4GLApQnAbavD/u79jxEc/pC4tS
  //   13ziMwBwOl9GRRnN2NIkRcwGVZavClIak5NkKI0GQaJGPcbb9mg2/rcYg+v03Br39W1HWop9m4vS
  //   AjIxgzYd3qj+sf6MOOfC5CzvJvdSvizLg5Zvbadg9fUFKMWN5swA8TmXJPx8jYiKTrrw8KM40Fgs
  //   NQ9uTiWXbikwTtTbaKZj+BVE2ND4/XC0qLEHechdk0eeG0ZUPZXdl9N2Ri23xLAmIQl1M3oTCrDi
  //   7MaIUXLsZl5HVBnJ5XwtbKTQxZpJWCn02cONkr0duQf68Y+/HDOpjsKFUwl+IuT9dDy+ZrFkzfD1
  //   dOowy6kaH1etllZkxCjwNihHSy5bo4KJlZfNcRUhwcQ0no2XkGS2RgUTzcA153+TQvSkS1m6rrDg
  //   pVCCpAQvZukmKngBNCdUZ5oEL2CR+Ro1YzKs4GVhE9JM8LJfNGRqJVLhUCPFiwW3TYIhW9rFeS9f
  //   fQkgBYLanOIF4lhE8QJFclGWomzEDEsxqJg330EmeznFy/zt6eTsnZWXeDi5Zn0pxVjY+pKJJ1u+
  //   YxiEr8wUTHOTgGJnirySl00QvHFSEcnLxRdafjqGOq0kL6t9mJa8bHRySclLLCiiMSRVkkQYkU2h
  //   cIqpe6Ymn8uvVlEz1IRcHxpkn9IXjqw8pS9PbnIl7YsJKBsOjKbSp4WBqdoQkmBdrvPwB0QW33Ac
  //   0kAUnyQwypJUAEaVwGyqLz7lyyrbunUZumdxCl74jexbCBqnvON9iUNHXdC9W5FF7xwPODyvYMaS
  //   1UUVM0uzRqXEbEWbSNNU4qJ9zxHYOZcm5wjIYes6GKmumpsNr+YnqnrxYhaLQex4X4wckayalsmQ
  //   4+0cjlU/XT3e0ACdV5zai85QhFOUuwEkVadVpwlx7cy2QHxTycy6HH1kksSlUmYFbPvE7/cqmLFk
  //   Iw+gmDE282eeB1F5MhqDtDUQjYmjBlUKZzZIclu9DIckoptwKnQvZTJrJLHUMeDQgF8dsx+pubJa
  //   JlnL/spyGTbBg/kSYzDde2H4ZL0SL4YOnnVK94uxy1vBkS9JH9L7zXoaK0fqRCwU3tVeONA6Ruoo
  //   o7KZoM4/THPQeNaWMdHHcAIs+ljOfrIcKwY+V1e4CCQAdsNcBOBNKWYzi2vauCvjEdFDsOeebIPd
  //   impc2SBSVbNXqgWQRRJQoD6TNMeyPr4xiIHI3cTzu5LIL0M7jCNNkudY3zfxHCDeIF9/3ifO+xHy
  //   mMCdKXVJIcNZp0mdDWeCp7yAPgZ9nFXf2AIKJlPs3S3RDjR6EieMO+9ERq2W1SXBVf+zgZtd+s08
  //   Jth4O9B8CXYzB+Mm+9klHA+gjmiwgVAH8B1bml4oc/REHku4baVOFXikflsMeCQgIz6ZCCSlenhD
  //   eGr4T5/IfkzI+d78hj0YxTKcbLI4yHCi0p1GkgxvGqfoU0Nhl3a/AkqLAgDwAIgdFaoeHQvr7Kiq
  //   oaid6q6DCxIJth6vkeWx4h2AVUGf3LquDouetSoDbNjAtVJgVWM2vw7BcnvxTghYuU43JVlikYE1
  //   63Q2SXftAKC8x7hVOyTp9Xz0qg2yKMdRGo3XBqn4o548VHlcupN2CduICzYGvRiiq2BGGSKpXmSx
  //   x1pquhWOpQqim1Yg5mrtmCo2xbHGiWVNU0l9UaPQyVJd18AxrngvnGdkx6+oDUExyoByAm2ySMmG
  //   pEivlYvk8EFUX78cfiqj0NPm9BbczqlkUrhzjlZwF/WqNwf5RBwVccKkZy/EaXIMLIc47LGtfQDn
  //   qQoqreWpCnKP11oVZL7fI6qCSPAuW/BkWr65SaEerfjhCamGdD267bCoXjxRQmNM4rUAJ9uLp6oa
  //   2hbRasgTTzzTyEDmEy1kiJ6zMN83k/6JI41328WYEaufph10bTRvDx8vOSQfcuYzMaSqV5mJfLhL
  //   ZQTMxaky0kbLxWel8vwEy3fVOpryA5sJlRF6YeduS4JT/PgpT5PEAU6c9cQPY9pJC1+Kus6WwBw6
  //   uwI1tpjw3CUlkHw1b9OUKipGqiaS3GKkxWhNVZC+0lZVjDTzKJ1l+cVIbWiWqarfqb4fC+DoAr93
  //   23hpVjigoxJK5C5xd1lo/EsTXqIVIk5uZg47okV/hIt8XWcjIrAYXP8haHjOBkSqQkkHrKhCiQXT
  //   qx03sbjQXv0Wc4EhO31eSVO4H5FpeJmiXd30uPZDbpiKnUKBHItsR4QqOTpraFeoy/ArN0atgBmk
  //   tn0ipdu0I6JZUBqjHjl51QCjIsIC8ukS/YvubuYQ5gG1DimAAhQoph7PNF9Tc2BJ3ZM6RWgCb9rQ
  //   yAtOILnVXHjZLoRct36Nqp70LZfPtFPCS3Lyih5IZtRhOUxPy4AGWSyXfJ/riUSnDzk0QtzACTMk
  //   aAVT7d7uSPspoPamVt8s1Q6CEhasr3SarngIUZ8mmsACm6TeRylOslIKqmPtJSuxar0Tga6osr+p
  //   Fnr8VayyMpJDYXW9NikbhZXu3ZztCvQDeSjKZxVWLP7xeNYmfWUqVFOh4aSwgq0+nHhWcerxmqE7
  //   XKoqrJT8Bkuq9NMtcVL17Mu0HS1ZGWR387Mvk+f52pQKv3ffApJpRfs0iVoY9E7BtYiWW8SgSqxE
  //   nyNvFmqyl2gjp6ZZKFtiJY2Y0Syx0hbZ/StqD5+F4gR64YYFSbqkb5FYMqqH3cWcv2QfRSd27nL6
  //   T9gCJtbvKdhjRZNYpWp76IhNG6m6cBIrC6gKiZU4Ui5hnpXMSPFIyPEmEwmdxT3APK4f0VWYjjui
  //   s+1Sf1vvmb77SJx7qXmD/lBrIVsIuxYSK1FnOd8WyiFfqEuslF+sdShZrvWLbl6uxW6KsPlZ4+3a
  //   Gzxc4SOnzxu7YcOjclhAYkUa5iol4TUc2N0gJ8FSKKBLjlDbolF+hWLqnZRYdEMo9Qf7LFJV+azb
  //   UV5LleBlac/s1cCFcq5OZJzEin06TmIFUOBOZg5hGveTcQ8tauB+PM5ycOeKsXh1MHsTtG8iaiAl
  //   VuyWy6faY/pP3bNFf2ZO6qZ1H4dxOInVQws+qxIr4SRWFpI9BZ8JKoVS7W0kCXfWWsFboaYTWJ8S  K+PH/a7bW0H+AwxxY5Q=
  //   contents of rom_4 (hex, n*v repeats v):
  //   compressed eJzVVzmSJCEM9PMV2GsNZ1X//2ML6EBSM+YaGxUxQ5dOhDJFlZ8/PynPp7y8yGUuCnJqqaT1N2eS
  //   ILe5GPPJjxiNtZi6KqpLedvBW7MKpnWXN0v0pvwRJ1UEgxdTwm7YWYnxVLUs3bVoTTJYfyFGyRo1
  //   1t3ZtuWYyzA3hv17pVLns23mm7D5pbM331YA3XwxVuRHrbr4MZvWSFsw5E12sW0A1dm7XYs2fk+U
  //   3/CZzELuMy7r+fBipYUnPeR5i3hBfpaovUY5PVM9N3ljNrMC7M1sgbp79hGK8YrUOYAmMcpXAPGz
  //   U+/zWaljLz78RhxS4bZIFpQ6OHWrTCez35jU9+8qAnX30OJU4oi21VTfqfsANQRo2kqryfCm0hUA
  //   irkfbkhtZ8ECBdfuzdykGwRFlNtrdOCVu/ixYHMBNKRDqqLMpXVQNkJal0Qb9W8pZYcuT5dicaQR
  //   z7RWLrkeZSXVynWGNkQ4P+QqAn9+M4AYnzjr2Hbk+uPjZAQeJB7BhckmlwUetCR3eJDZ8MuajwaH
  //   B+0pksDwoCfVEuOdExIvrUfyzOK2W4YQHkTgQWUnWHoJmz88qCIEHlQRLA/aTR+m3IthmfISG5YH
  //   X16sfgyJdknU82ASHkTgQYU4LA8mQT8CDybhQRR3gmqzBZYHA+N2l81UPzw4DJlsP44HtZfhmWdE
  //   8HgKX1DwqQuOwKmrjeAIlgdPJQ7ExIp4ED2kbgN4HkzKgziUZJpvMwpTlNIlt+vLHPTFfz2wn2U2
  //   fAFMGMhynw2FbC46YrqZ4xaj0cj/jewQZoeSHczccmSHnr7ITo/RHpKSHTGakh2fDXRGqTuKQwM4
  //   y7DNArCZK0GH61WeU5uBWoK2CKQStH85VHbILn62raLzRCJ5pQZoGxk4aoJlNtopHD4mHtqRKphf
  //   7A4a7aBJsEqN6DTl9mWzF04SpsvlZkeynflM+DEqcFknLhxRDiqVgvEoxLFJAvyyfZzKIJlJUHiG
  //   SlDARCIGxDgUCKM6GXEPNxp3JM9Cm9KUPfZl+5hf0tI2JWlNqos2oU2pgwON6mSd7NgZs0Xmzleu
  //   UBDrOOVPkHj70HvPY5u4fYwaLOC76V647lUWcB8f1pZSkO59na1Lr1HvBJKAjPNhz6E2ewC1nCYS
  //   kONWeSkyV55vVK7kcolin44G8AVsrjgcDaRDAwjalgaQDzObQlJLXvBNN1tOqNHsbIaXxheg6FNI
  //   sgjoZPxT6vrS4R827YP/98hauuHfMZckwfhXu+909avnhn/wJeGGf/BNwibIsgKG+g3/Ek/wPw7Y
  //   CribbvgHXwhu+BeCCvh/j0y60ONfSeHzx+J/kKw7Zx7/0G8m7lVD/RkBj/zPda3g3qrEifU6mcV8
  //   tHssbka9+PxHQDfV/AXorrawXv57oMtFys77OI3tvPd4jzcDi3exu+E92lm8w817j3e4ee/xDjfv
  //   Pd4duALewXP7hnclgQvexe6Gd413wTvcvPd4x60ZGe/q84J3WAqKeEeY9x7vCsoL3uEvqw7vEM0L
  //   3hE6ttzsLngPPj3eIbf/G95BeE83vAtgb3gPVyqHdzCXspe/47uphQ==
  //   INTERRUPT DETECT
  //   RESET CONTROL
  //   DECODE ROM (36 Bits)
  //   74UC14
  //   To MIR
  //   To IR
  //   MICROCODE ROMS
  //   EXECUTE ROM (36 Bits)
  //   CONFIGURATION (tbd)
  //   PINOUT
  //   SEQUENCER / STATE (Q) CONTROL
  //   CLOCK MANAGEMENT
  //   74UC14
  //   Q STATE REGISTER
  //   WAI / STP
  //   NMI CONTROL
  //   74UC14
  //   FETCH STAGE
  //   74LVC161
  //   From ADH.MX
  //   From ADX.MX
  //   BREAK FLAG
  //   SO Pin
  //   74CBTLV3257
  //   To P Register
  //   IRQ CONTROL
  //   Select NMOS if E flag is on
  //   To CLOK MANAGEMENT above
  //   Decode Pipeline Register (MIR)
  //   NMOS does not clear D flag on an interurpt
  //   Ungated Internal Clocks
  //   Gated Internal Clocks
  //   Q.RESET
  //   74CBTLV3257
  //   To Control Muxes
  //   To Control ROMs
  //   To Microinstruction Decoders
  //   To Microinstruction Decoders
  //   From ALU
  //   From Configuration
  //   74LVC138
  //   74LVC138
  //   74LVC138
  //   74LVC138 x 2
  //   74LVC138 x 2
  //   ALUA.MX
  //   ALUB.MX
  //   ALU.MX
  //   /+1.ADH'
  //   74LVC138
  //   From DECODE ROM
  //   74LVC138
  //   74LVC138
  //   74AUC2G53
  //   To ALU
  //   ADH.WE
  //   From DECODE ROM
  //   74LVC138 x 2
  //   74LVC138 x 2
  //   74LVC138
  //   ALUC.MX
  //   74CBTLV3251
  //   ADL.MX
  //   WE.ADL'
  //   /+1.CC.ADL (+1 to ADL if Carry clear)
  //   /+1.ADL'
  //   /PCL.CC.ADL (PCL to ADL if Carry clear)
  //   /PCL.ADL'
  //   ADH.MX
  //   ADX.MX
  //   PC.MX
  //   74CBTLV3257
  //   WE.MX
  //   74CBTLV3257
  //   WB.MX
  //   DOR.MX
  //   From DECODEROM
  //   END.MX
  //   SYNC Pin
  //   FLG.MX
  //   To WB Pipeline Register
  //   (PCL to ADL if Carry Clear)
  //   (+1 to ADL if Carry Clear)
  //   From WB Register
  //   /Rout.CS.ADX (Rout to ADX if Carry set)
  //   From WB Register
  //   From DECODE ROM
  //   Load IR
  //   To WB Pipeline Register
  //   DECODE STAGE
  //   From DECODE ROM
  //   From DECODE ROM
  //   From WB Register
  //   From WB Register
  //   /SH.ADH
  //   /+1.Rout.ADH (+1 to ADH if crry clear, Rout to ADH if carry set)
  //   /PC.Rout.ADH (PC to ADH if Carry clear, Rout to ADH if Carry set)
  //   /Rout.ADH'
  //   /+1.Rout.ADH (+1 to ADH if crry clear, Rout to ADH if carry set)
  //   /+1.CC.ADH (+1 to ADH if Carry clear)
  //   /+1.ADH'
  //   /PCH.CC.ADH
  //   /PC.Rout.ADH (PC to ADH if Carry clear, Rout to ADH if Carry set)
  //   /PCH.ADH'
  //   WE.ADX
  //   /0.ADX
  //   /Rout.ADX
  //   /Rout.CS.ADX
  //   /DH.ADH
  //   From WB Register
  //   From WB Register
  //   74AUC2G53
  //   74AUC2G53
  //   CONTROL MUX
  //   74CBTLV3257
  //   CONTROL MUX
  //   74CBTLV3257
  //   /DB.ADL
  //   /SP.ADL
  //   74AUC2G53
  //   74AUC2G53
  //   74AUC2G53
  //   74AUC2G53
  //   CONTROL MUX
  //   74CBTLV3257
  //   74AUC2G53
  //   74AUC2G53
  //   74AUC2G53
  //   74AUC2G53
  //   CONTROL MUX
  //   74CBTLV3257
  //   From DECODE ROM
  //   ADH.WE
  //   /+1.ADH
  //   CONTROL MUX
  //   74CBTLV3257
  //   From DECODE ROM
  //   CONTROL MUX
  //   74CBTLV3257
  //   FIX: Bus Management
  //   DOR should drive only in PHI2
  //   (Implement bus management for all other buses)
  //   Reset IR
  //   74CBTLV3257
  //   REGISTER FILE
  //   74CBTLV3245
  //   Select pre-inverter ALUB
  //   To Microcode ROMs
  //   74CBTLV3257
  //   To ALU
  //   Execute Pipeline Register
  //   ALU Control
  //   From ALU.MX
  //   SBC
  //   ADC
  //   4-bit ALU
  //   (AUB Pre-Inverter)
  //   C8
  //   BCDLC
  //   BCD.DET.HI
  //   BCD.ADJ.LO
  //   Execute Pipeline Register
  //   SBC
  //   (For V Flag) To WB Register 
  //   (For V Flag) To WB Register
  //   '3253 - BCD.DET.HI.AUX
  //   BCDHC
  //   SBC
  //   '2G53 BCD.SEL.HI
  //   BCDHC
  //   '2G53 BCD.SEL.HI
  //   BCDLC
  //   C8
  //   NMOS BCD Flag 4-bit Adder
  //   (INH)
  //   FET ADDER
  //   '2G53
  //   ADC
  //   C8
  //   C4
  //   BCD.DETECT.LO
  //   74CBTLV3251
  //   SBC
  //   Result for NMOS BCD Flags
  //   SBC
  //   EXECUTE STAGE
  //   ALU
  //   74CBTLV3251
  //   BCDLC
  //   SBC
  //   /BCDLC
  //   ASL / ROL
  //   LSR / ROR
  //   '3257 - BCD.SEL.LO
  //   BCD.DETECT.HI
  //   '3257 - BCD.SEL.ADJ
  //   Cout Select
  //   74CBTLV3251
  //   '3251 - BCD.DET.HI
  //   C8
  //   Opcode[5..7]
  //   Exit.CC
  //   74CBTLV3253
  //   BranchTest
  //   74AUC2G53
  //   74AUC2G53
  //   Result for Flags
  //   74AUC2G53
  //   From FLG.MX
  //   From WB.MX
  //   From ALU
  //   Exit.BTF
  //   74AUC2G53
  //   /Branch Exit
  //   WriteBack Pipeline Register
  //   FetchOpcode
  //   To MIR
  //   To Decoders
  //   FetchOperand
  //   V FLAG
  //   Z FLAG
  //   I FLAG
  //   74AUC2G53
  //   74AUC2G53
  //   Flags Logic
  //   74CBTLV3251
  //   C FLAG
  //   D FLAG
  //   WRITEBACK STAGE
  //   N FLAG
  //   74AUC2G53
  //   74CBTLV3253
  //   Status Register (P)
endmodule

module Main (
  input  RDY,
  input  BE
);

  wire BANK0, BANK1, BANK2, BANK3, IRQ_out, NMI_out, not_1_out, not_2_out, not_3_out, not_4_out, PHI0_out,
       PHI1, PHI2, R_W, RES_out, SYNC;
  wire [7:0] AX_BUS, D_BUS;
  wire [15:0] A_BUS;

  Clock PHI0 (.out(PHI0_out));
  Button RES (.out(RES_out));
  Button IRQ (.out(IRQ_out));
  Button NMI (.out(NMI_out));
  _6502 u_6502_1 (
    .A_BUS(A_BUS), .AX_OUT(AX_BUS), .D_OUT(D_BUS), .R_W(R_W), .PHI1(PHI1), .PHI2(PHI2), .SYNC(SYNC),
    .PHI0(PHI0_out), .RDY(1'b1), .BE(1'b1), .nRS(not_1_out), .nIRQ(not_2_out), .nNMI(not_3_out), .D_IN(D_BUS));
  not not_1 (not_1_out, RES_out);
  not not_2 (not_2_out, IRQ_out);
  not not_3 (not_3_out, NMI_out);
  // Probe on A_BUS
  not not_4 (not_4_out, R_W);
  RAM #(.addrWidth(16), .databus("bidir"), .trigger("high")) ram_1 (.addr(A_BUS), .data(D_BUS));  // open: we, oe, clk
  Decoder #(.select(2)) decoder_1 (
    .out0(BANK0), .out1(BANK1), .out2(BANK2), .out3(BANK3), .sel(AX_BUS[1:0]));  // open: en
  // Probe on D_BUS

  // Other names for the same wires on the sheet: BANK_SEL[1:0] = AX_BUS[1:0]

  // Notes on the sheet:
  //   Copyright Drass, 2020
  //   All rights reserved
  //   6502 Minimalist Computer
endmodule
