// Logisim project HCT.circ as structural Verilog: 6 circuits, main circuit HCT138
module HCT138 (
  input  A,
  input  B,
  input  C,
  input  G1,
  input  nG2A,
  input  nG2B,
  output Y0,
  output Y1,
  output Y2,
  output Y3,
  output Y4,
  output Y5,
  output Y6,
  output Y7
);

  wire buffer_1_out, buffer_2_out, buffer_3_out, buffer_4_out, nand_1_out, nand_2_out, nand_3_out,
       nand_4_out, nand_5_out, nand_6_out, nand_7_out, nand_8_out, nand_9_out, not_1_out, not_2_out,
       not_3_out, not_4_out, not_5_out;

  buf buffer_1 (buffer_1_out, A);
  buf buffer_2 (buffer_2_out, B);
  buf buffer_3 (buffer_3_out, C);
  buf buffer_4 (buffer_4_out, G1);
  not not_1 (not_1_out, nG2A);
  not not_2 (not_2_out, nG2B);
  not not_3 (not_3_out, buffer_1_out);
  not not_4 (not_4_out, buffer_2_out);
  not not_5 (not_5_out, buffer_3_out);
  nand nand_1 (nand_1_out, buffer_4_out, not_1_out, not_2_out);
  nand nand_2 (nand_2_out, not_3_out, not_4_out, not_5_out);
  nand nand_3 (nand_3_out, buffer_1_out, not_4_out, not_5_out);
  nand nand_4 (nand_4_out, not_3_out, buffer_2_out, not_5_out);
  nand nand_5 (nand_5_out, buffer_1_out, buffer_2_out, not_5_out);
  nand nand_6 (nand_6_out, not_3_out, not_4_out, buffer_3_out);
  nand nand_7 (nand_7_out, buffer_1_out, not_4_out, buffer_3_out);
  nand nand_8 (nand_8_out, not_3_out, buffer_2_out, buffer_3_out);
  nand nand_9 (nand_9_out, buffer_1_out, buffer_2_out, buffer_3_out);
  or or_1 (Y0, nand_2_out, nand_1_out);
  or or_2 (Y1, nand_3_out, nand_1_out);
  or or_3 (Y2, nand_4_out, nand_1_out);
  or or_4 (Y3, nand_5_out, nand_1_out);
  or or_5 (Y4, nand_6_out, nand_1_out);
  or or_6 (Y5, nand_7_out, nand_1_out);
  or or_7 (Y6, nand_8_out, nand_1_out);
  or or_8 (Y7, nand_9_out, nand_1_out);
endmodule

module HCT377 (
  input  [7:0] D,
  input  nE,
  input  CP,
  output [7:0] Q
);

  wire and_1_out, and_2_out, and_3_out, and_4_out, and_5_out, and_6_out, and_7_out, and_8_out, and_9_out,
       and_10_out, and_11_out, and_12_out, and_13_out, and_14_out, and_15_out, and_16_out, not_1_out,
       not_2_out, or_1_out, or_2_out, or_3_out, or_4_out, or_5_out, or_6_out, or_7_out, or_8_out;

  not not_1 (not_1_out, nE);
  not not_2 (not_2_out, CP);
  and and_1 (and_1_out, Q[0], ~not_1_out);  // AND_Gate
  and and_2 (and_2_out, not_1_out, D[0]);
  and and_3 (and_3_out, Q[1], ~not_1_out);  // AND_Gate
  and and_4 (and_4_out, not_1_out, D[1]);
  and and_5 (and_5_out, Q[2], ~not_1_out);  // AND_Gate
  and and_6 (and_6_out, not_1_out, D[2]);
  and and_7 (and_7_out, Q[3], ~not_1_out);  // AND_Gate
  and and_8 (and_8_out, not_1_out, D[3]);
  and and_9 (and_9_out, Q[4], ~not_1_out);  // AND_Gate
  and and_10 (and_10_out, not_1_out, D[4]);
  and and_11 (and_11_out, Q[5], ~not_1_out);  // AND_Gate
  and and_12 (and_12_out, not_1_out, D[5]);
  and and_13 (and_13_out, Q[6], ~not_1_out);  // AND_Gate
  and and_14 (and_14_out, not_1_out, D[6]);
  and and_15 (and_15_out, Q[7], ~not_1_out);  // AND_Gate
  and and_16 (and_16_out, not_1_out, D[7]);
  or or_1 (or_1_out, and_1_out, and_2_out);
  or or_2 (or_2_out, and_3_out, and_4_out);
  or or_3 (or_3_out, and_5_out, and_6_out);
  or or_4 (or_4_out, and_7_out, and_8_out);
  or or_5 (or_5_out, and_9_out, and_10_out);
  or or_6 (or_6_out, and_11_out, and_12_out);
  or or_7 (or_7_out, and_13_out, and_14_out);
  or or_8 (or_8_out, and_15_out, and_16_out);
  D_Flip_Flop #(.trigger("falling")) d_ff_1 (.clk(not_2_out), .D(or_1_out), .Q(Q[0]));  // open: Qn, preset, reset
  D_Flip_Flop #(.trigger("falling")) d_ff_2 (.clk(not_2_out), .D(or_2_out), .Q(Q[1]));  // open: Qn, preset, reset
  D_Flip_Flop #(.trigger("falling")) d_ff_3 (.clk(not_2_out), .D(or_3_out), .Q(Q[2]));  // open: Qn, preset, reset
  D_Flip_Flop #(.trigger("falling")) d_ff_4 (.clk(not_2_out), .D(or_4_out), .Q(Q[3]));  // open: Qn, preset, reset
  D_Flip_Flop #(.trigger("falling")) d_ff_5 (.clk(not_2_out), .D(or_5_out), .Q(Q[4]));  // open: Qn, preset, reset
  D_Flip_Flop #(.trigger("falling")) d_ff_6 (.clk(not_2_out), .D(or_6_out), .Q(Q[5]));  // open: Qn, preset, reset
  D_Flip_Flop #(.trigger("falling")) d_ff_7 (.clk(not_2_out), .D(or_7_out), .Q(Q[6]));  // open: Qn, preset, reset
  D_Flip_Flop #(.trigger("falling")) d_ff_8 (.clk(not_2_out), .D(or_8_out), .Q(Q[7]));  // open: Qn, preset, reset
endmodule

module HCT244 (
  input  [7:0] A,
  input  nOE,
  output [7:0] Y
);

  wire not_1_out;

  not not_1 (not_1_out, nOE);
  assign Y[0] = not_1_out ? A[0] : 1'bz;  // Controlled_Buffer controlled_buffer_1
  assign Y[1] = not_1_out ? A[1] : 1'bz;  // Controlled_Buffer controlled_buffer_2
  assign Y[2] = not_1_out ? A[2] : 1'bz;  // Controlled_Buffer controlled_buffer_3
  assign Y[3] = not_1_out ? A[3] : 1'bz;  // Controlled_Buffer controlled_buffer_4
  assign Y[4] = not_1_out ? A[4] : 1'bz;  // Controlled_Buffer controlled_buffer_5
  assign Y[5] = not_1_out ? A[5] : 1'bz;  // Controlled_Buffer controlled_buffer_6
  assign Y[6] = not_1_out ? A[6] : 1'bz;  // Controlled_Buffer controlled_buffer_7
  assign Y[7] = not_1_out ? A[7] : 1'bz;  // Controlled_Buffer controlled_buffer_8
endmodule

module HCT193 (
  input  CPU,
  input  CPD,
  input  nPL,
  input  MR,
  input  D0,
  input  D1,
  input  D2,
  input  in_8,
  output Q2,
  output Q3,
  output Q0,
  output Q1,
  output nTCU,
  output nTCD
);

  wire and_1_out, and_2_out, and_3_out, and_4_out, and_5_out, and_6_out, buffer_1_out, buffer_2_out,
       buffer_3_out, buffer_4_out, buffer_5_out, buffer_6_out, nand_1_out, nand_2_out, nand_3_out,
       nand_4_out, nand_5_out, nand_6_out, nand_7_out, nand_8_out, nor_1_out, nor_2_out, nor_3_out,
       nor_4_out, not_1_out, not_2_out, not_3_out, not_4_out, not_5_out, not_6_out, not_7_out, not_8_out,
       or_1_out, or_2_out, or_3_out, or_4_out, t_ff_1_qn, t_ff_2_qn, t_ff_3_qn, t_ff_4_qn;

  not not_1 (not_1_out, CPU);
  not not_2 (not_2_out, CPD);
  not not_3 (not_3_out, nPL);
  not not_4 (not_4_out, MR);
  buf buffer_1 (buffer_1_out, not_1_out);
  nor nor_1 (nor_1_out, buffer_1_out, buffer_2_out);
  buf buffer_2 (buffer_2_out, not_2_out);
  not not_5 (not_5_out, nand_1_out);
  nand nand_1 (nand_1_out, not_3_out, not_4_out, buffer_3_out);
  buf buffer_3 (buffer_3_out, D0);
  T_Flip_Flop t_ff_1 (.clk(nor_1_out), .T(1'b1), .Q(Q0), .Qn(t_ff_1_qn), .preset(not_5_out), .reset(or_1_out));
  nand nand_2 (nand_2_out, nand_1_out, not_3_out);
  or or_1 (or_1_out, ~nand_2_out, ~not_4_out);  // OR_Gate
  and and_1 (and_1_out, not_1_out, Q0);
  and and_2 (and_2_out, t_ff_1_qn, not_2_out);
  nor nor_2 (nor_2_out, and_1_out, and_2_out);
  not not_6 (not_6_out, nand_3_out);
  nand nand_3 (nand_3_out, not_3_out, not_4_out, buffer_4_out);
  buf buffer_4 (buffer_4_out, D1);
  T_Flip_Flop t_ff_2 (.clk(nor_2_out), .T(1'b1), .Q(Q1), .Qn(t_ff_2_qn), .preset(not_6_out), .reset(or_2_out));
  nand nand_4 (nand_4_out, nand_3_out, not_3_out);
  or or_2 (or_2_out, ~nand_4_out, ~not_4_out);  // OR_Gate
  and and_3 (and_3_out, not_1_out, Q0, Q1);
  nor nor_3 (nor_3_out, and_3_out, and_4_out);
  and and_4 (and_4_out, not_2_out, t_ff_2_qn, t_ff_1_qn);
  not not_7 (not_7_out, nand_5_out);
  T_Flip_Flop t_ff_3 (.clk(nor_3_out), .T(1'b1), .Q(Q2), .Qn(t_ff_3_qn), .preset(not_7_out), .reset(or_3_out));
  nand nand_5 (nand_5_out, not_3_out, not_4_out, buffer_5_out);
  nand nand_6 (nand_6_out, nand_5_out, not_3_out);
  buf buffer_5 (buffer_5_out, D2);
  or or_3 (or_3_out, ~nand_6_out, ~not_4_out);  // OR_Gate
  and and_5 (and_5_out, not_1_out, Q0, Q1, Q2);
  and and_6 (and_6_out, not_2_out, t_ff_3_qn, t_ff_2_qn, t_ff_1_qn);
  nor nor_4 (nor_4_out, and_5_out, and_6_out);
  T_Flip_Flop t_ff_4 (.clk(nor_4_out), .T(1'b1), .Q(Q3), .Qn(t_ff_4_qn), .preset(not_8_out), .reset(or_4_out));
  not not_8 (not_8_out, nand_7_out);
  nand nand_7 (nand_7_out, not_3_out, not_4_out, buffer_6_out);
  buf buffer_6 (buffer_6_out, in_8);
  nand nand_8 (nand_8_out, nand_7_out, not_3_out);
  or or_4 (or_4_out, ~nand_8_out, ~not_4_out);  // OR_Gate
  nand nand_9 (nTCU, Q2, Q1, Q0, not_1_out, Q3);
  nand nand_10 (nTCD, t_ff_4_qn, t_ff_3_qn, t_ff_2_qn, t_ff_1_qn, not_2_out);
endmodule

module HCT299 (
  input  DSR,
  input  [7:0] O,
  input  S0,
  input  S1,
  input  CP,
  input  nOE1,
  input  nOE2,
  input  DSL,
  input  nMR,
  output [7:0] I,
  output Q0,
  output Q7
);

  wire and_1_out, and_2_out, and_3_out, and_4_out, and_5_out, and_6_out, and_7_out, and_8_out, and_9_out,
       and_10_out, and_11_out, and_12_out, and_13_out, and_14_out, and_15_out, and_16_out, and_17_out,
       and_18_out, and_19_out, and_20_out, and_21_out, and_22_out, and_23_out, and_24_out, and_25_out,
       and_26_out, and_27_out, and_28_out, and_29_out, and_30_out, and_31_out, and_32_out, buffer_2_out,
       buffer_3_out, buffer_4_out, buffer_6_out, buffer_7_out, buffer_8_out, buffer_9_out, buffer_10_out,
       buffer_11_out, buffer_12_out, buffer_13_out, buffer_14_out, buffer_15_out, nand_1_out, nand_2_out,
       not_1_out, not_2_out, not_3_out, not_4_out, not_5_out, not_6_out, not_7_out, not_8_out, not_9_out,
       not_10_out, not_11_out, not_12_out, not_13_out, not_14_out, not_15_out, not_16_out, not_17_out,
       or_1_out, or_2_out, or_3_out, or_4_out, or_5_out, or_6_out, or_7_out, or_8_out;
  wire [7:0] d_ff_1_q;

  buf buffer_1 (Q7, d_ff_1_q[7]);
  buf buffer_2 (buffer_2_out, DSR);
  buf buffer_3 (buffer_3_out, S0);
  buf buffer_4 (buffer_4_out, S1);
  nand nand_1 (nand_1_out, buffer_4_out, buffer_3_out);
  not not_1 (not_1_out, CP);
  buf buffer_5 (Q0, d_ff_1_q[0]);
  not not_2 (not_2_out, nOE1);
  not not_3 (not_3_out, nOE2);
  buf buffer_6 (buffer_6_out, DSL);
  buf buffer_7 (buffer_7_out, nMR);
  not not_4 (not_4_out, buffer_3_out);
  not not_5 (not_5_out, buffer_4_out);
  nand nand_2 (nand_2_out, nand_1_out, not_2_out, not_3_out);
  not not_6 (not_6_out, not_4_out);
  not not_7 (not_7_out, not_5_out);
  not not_8 (not_8_out, not_1_out);
  not not_9 (not_9_out, nand_2_out);
  and and_1 (and_1_out, buffer_2_out, not_6_out, not_5_out);
  and and_2 (and_2_out, not_7_out, not_4_out, d_ff_1_q[1]);
  and and_3 (and_3_out, not_7_out, not_6_out, buffer_8_out);
  and and_4 (and_4_out, not_5_out, not_4_out, d_ff_1_q[0]);
  and and_5 (and_5_out, d_ff_1_q[0], not_6_out, not_5_out);
  and and_6 (and_6_out, not_7_out, not_4_out, d_ff_1_q[2]);
  and and_7 (and_7_out, not_7_out, not_6_out, buffer_9_out);
  and and_8 (and_8_out, not_5_out, not_4_out, d_ff_1_q[1]);
  and and_9 (and_9_out, d_ff_1_q[1], not_6_out, not_5_out);
  and and_10 (and_10_out, not_7_out, not_4_out, d_ff_1_q[3]);
  and and_11 (and_11_out, not_7_out, not_6_out, buffer_10_out);
  and and_12 (and_12_out, not_5_out, not_4_out, d_ff_1_q[2]);
  and and_13 (and_13_out, d_ff_1_q[2], not_6_out, not_5_out);
  and and_14 (and_14_out, not_7_out, not_4_out, d_ff_1_q[4]);
  and and_15 (and_15_out, not_7_out, not_6_out, buffer_11_out);
  and and_16 (and_16_out, not_5_out, not_4_out, d_ff_1_q[3]);
  and and_17 (and_17_out, d_ff_1_q[3], not_6_out, not_5_out);
  and and_18 (and_18_out, not_7_out, not_4_out, d_ff_1_q[5]);
  and and_19 (and_19_out, not_7_out, not_6_out, buffer_12_out);
  and and_20 (and_20_out, not_5_out, not_4_out, d_ff_1_q[4]);
  and and_21 (and_21_out, d_ff_1_q[4], not_6_out, not_5_out);
  and and_22 (and_22_out, not_7_out, not_4_out, d_ff_1_q[6]);
  and and_23 (and_23_out, not_7_out, not_6_out, buffer_13_out);
  and and_24 (and_24_out, not_5_out, not_4_out, d_ff_1_q[5]);
  and and_25 (and_25_out, d_ff_1_q[5], not_6_out, not_5_out);
  and and_26 (and_26_out, not_7_out, not_4_out, d_ff_1_q[7]);
  and and_27 (and_27_out, not_7_out, not_6_out, buffer_14_out);
  and and_28 (and_28_out, not_5_out, not_4_out, d_ff_1_q[6]);
  and and_29 (and_29_out, d_ff_1_q[6], not_6_out, not_5_out);
  and and_30 (and_30_out, not_7_out, not_4_out, buffer_6_out);
  and and_31 (and_31_out, not_7_out, not_6_out, buffer_15_out);
  and and_32 (and_32_out, not_5_out, not_4_out, d_ff_1_q[7]);
  D_Flip_Flop d_ff_1 (.D(or_1_out), .clk(not_8_out), .Q(d_ff_1_q[0]), .reset(not_10_out));  // open: Qn, preset
  or or_1 (or_1_out, and_1_out, and_2_out, and_3_out, and_4_out);
  D_Flip_Flop d_ff_2 (.D(or_2_out), .clk(not_8_out), .Q(d_ff_1_q[1]), .reset(not_11_out));  // open: Qn, preset
  or or_2 (or_2_out, and_5_out, and_6_out, and_7_out, and_8_out);
  D_Flip_Flop d_ff_3 (.D(or_3_out), .clk(not_8_out), .Q(d_ff_1_q[2]), .reset(not_12_out));  // open: Qn, preset
  or or_3 (or_3_out, and_9_out, and_10_out, and_11_out, and_12_out);
  D_Flip_Flop d_ff_4 (.D(or_4_out), .clk(not_8_out), .Q(d_ff_1_q[3]), .reset(not_13_out));  // open: Qn, preset
  or or_4 (or_4_out, and_13_out, and_14_out, and_15_out, and_16_out);
  D_Flip_Flop d_ff_5 (.D(or_5_out), .clk(not_8_out), .Q(d_ff_1_q[4]), .reset(not_14_out));  // open: Qn, preset
  or or_5 (or_5_out, and_17_out, and_18_out, and_19_out, and_20_out);
  D_Flip_Flop d_ff_6 (.D(or_6_out), .clk(not_8_out), .Q(d_ff_1_q[5]), .reset(not_15_out));  // open: Qn, preset
  or or_6 (or_6_out, and_21_out, and_22_out, and_23_out, and_24_out);
  D_Flip_Flop d_ff_7 (.D(or_7_out), .clk(not_8_out), .Q(d_ff_1_q[6]), .reset(not_16_out));  // open: Qn, preset
  or or_7 (or_7_out, and_25_out, and_26_out, and_27_out, and_28_out);
  D_Flip_Flop d_ff_8 (.D(or_8_out), .clk(not_8_out), .Q(d_ff_1_q[7]), .reset(not_17_out));  // open: Qn, preset
  or or_8 (or_8_out, and_29_out, and_30_out, and_31_out, and_32_out);
  not not_10 (not_10_out, buffer_7_out);
  not not_11 (not_11_out, buffer_7_out);
  not not_12 (not_12_out, buffer_7_out);
  not not_13 (not_13_out, buffer_7_out);
  not not_14 (not_14_out, buffer_7_out);
  not not_15 (not_15_out, buffer_7_out);
  not not_16 (not_16_out, buffer_7_out);
  not not_17 (not_17_out, buffer_7_out);
  Register #(.trigger("high")) register_1 (.D(d_ff_1_q), .clk(1'b1));  // open: en, Q, clr
  buf buffer_8 (buffer_8_out, O[0]);
  assign I[0] = not_9_out ? d_ff_1_q[0] : 1'bz;  // Controlled_Buffer controlled_buffer_1
  buf buffer_9 (buffer_9_out, O[1]);
  assign I[1] = not_9_out ? d_ff_1_q[1] : 1'bz;  // Controlled_Buffer controlled_buffer_2
  buf buffer_10 (buffer_10_out, O[2]);
  assign I[2] = not_9_out ? d_ff_1_q[2] : 1'bz;  // Controlled_Buffer controlled_buffer_3
  buf buffer_11 (buffer_11_out, O[3]);
  assign I[3] = not_9_out ? d_ff_1_q[3] : 1'bz;  // Controlled_Buffer controlled_buffer_4
  buf buffer_12 (buffer_12_out, O[4]);
  assign I[4] = not_9_out ? d_ff_1_q[4] : 1'bz;  // Controlled_Buffer controlled_buffer_5
  buf buffer_13 (buffer_13_out, O[5]);
  assign I[5] = not_9_out ? d_ff_1_q[5] : 1'bz;  // Controlled_Buffer controlled_buffer_6
  buf buffer_14 (buffer_14_out, O[6]);
  assign I[6] = not_9_out ? d_ff_1_q[6] : 1'bz;  // Controlled_Buffer controlled_buffer_7
  buf buffer_15 (buffer_15_out, O[7]);
  assign I[7] = not_9_out ? d_ff_1_q[7] : 1'bz;  // Controlled_Buffer controlled_buffer_8
endmodule

module HCT163 (
  input  D0,
  input  D1,
  input  D2,
  input  D3,
  input  CET,
  input  CEP,
  input  nPE,
  input  nMR,
  input  CP,
  output Q0,
  output Q1,
  output Q2,
  output Q3,
  output TC
);

  wire and_1_out, and_2_out, and_3_out, and_4_out, and_5_out, and_6_out, and_7_out, and_8_out, and_9_out,
       buffer_1_out, buffer_2_out, buffer_3_out, buffer_4_out, d_ff_1_q, d_ff_1_qn, d_ff_2_q, d_ff_2_qn,
       d_ff_3_q, d_ff_3_qn, d_ff_4_q, d_ff_4_qn, nand_1_out, nand_2_out, nor_1_out, nor_2_out, nor_3_out,
       nor_4_out, nor_5_out, nor_6_out, not_1_out, not_2_out, or_1_out, or_2_out, or_3_out, or_4_out,
       or_5_out, xnor_1_out, xnor_2_out, xnor_3_out;

  buf buffer_1 (buffer_1_out, nPE);
  not not_1 (not_1_out, nMR);
  buf buffer_2 (buffer_2_out, CET);
  buf buffer_3 (buffer_3_out, CEP);
  nor nor_1 (nor_1_out, buffer_1_out, not_1_out);
  buf buffer_4 (buffer_4_out, CP);
  nand nand_1 (nand_1_out, buffer_2_out, buffer_3_out);
  nor nor_2 (nor_2_out, nor_1_out, not_1_out);
  not not_2 (not_2_out, nand_1_out);
  xnor xnor_1 (xnor_1_out, not_2_out, d_ff_1_qn);
  and and_1 (and_1_out, D0, nor_1_out);
  and and_2 (and_2_out, xnor_1_out, nor_2_out);
  or or_1 (or_1_out, and_1_out, and_2_out);
  D_Flip_Flop d_ff_1 (.clk(buffer_4_out), .D(or_1_out), .Q(d_ff_1_q), .Qn(d_ff_1_qn));  // open: preset, reset
  not not_3 (Q0, d_ff_1_qn);
  nor nor_3 (nor_3_out, nand_1_out, d_ff_1_qn);
  xnor xnor_2 (xnor_2_out, nor_3_out, d_ff_2_qn);
  and and_3 (and_3_out, D1, nor_1_out);
  and and_4 (and_4_out, xnor_2_out, nor_2_out);
  or or_2 (or_2_out, and_3_out, and_4_out);
  D_Flip_Flop d_ff_2 (.clk(buffer_4_out), .D(or_2_out), .Q(d_ff_2_q), .Qn(d_ff_2_qn));  // open: preset, reset
  nor nor_4 (nor_4_out, nand_1_out, d_ff_2_qn, d_ff_1_qn);
  and and_5 (and_5_out, D2, nor_1_out);
  or or_3 (or_3_out, and_5_out, and_6_out);
  not not_4 (Q1, d_ff_2_qn);
  xnor xnor_3 (xnor_3_out, nor_4_out, d_ff_3_qn);
  and and_6 (and_6_out, xnor_3_out, nor_2_out);
  D_Flip_Flop d_ff_3 (.clk(buffer_4_out), .D(or_3_out), .Q(d_ff_3_q), .Qn(d_ff_3_qn));  // open: preset, reset
  not not_5 (Q2, d_ff_3_qn);
  nor nor_5 (nor_5_out, nand_1_out, d_ff_3_qn, d_ff_2_qn, d_ff_1_qn);
  and and_7 (and_7_out, nor_5_out, d_ff_4_qn);
  or or_4 (or_4_out, and_7_out, nor_6_out);
  and and_8 (and_8_out, D3, nor_1_out);
  and and_9 (and_9_out, nor_2_out, or_4_out);
  or or_5 (or_5_out, and_8_out, and_9_out);
  nor nor_6 (nor_6_out, nor_5_out, d_ff_4_qn);
  D_Flip_Flop d_ff_4 (.clk(buffer_4_out), .D(or_5_out), .Q(d_ff_4_q), .Qn(d_ff_4_qn));  // open: preset, reset
  not not_6 (Q3, d_ff_4_qn);
  nand nand_2 (nand_2_out, d_ff_4_q, d_ff_3_q, d_ff_2_q, d_ff_1_q, buffer_2_out);
  not not_7 (TC, nand_2_out);
endmodule
