// Logisim project HCT6526blocks.circ as structural Verilog: 16 circuits, main circuit regDecoder
module regDecoder (
  input  RS0,
  input  RS1,
  input  RS2,
  input  RS3,
  input  nCS,
  input  PHI2,
  input  nPHI2,
  output EN0,
  output EN1,
  output EN2,
  output EN3,
  output EN4,
  output EN5,
  output EN6,
  output EN7,
  output EN8,
  output EN9,
  output EN10,
  output EN11,
  output EN12,
  output EN13,
  output EN14,
  output EN15
);

  HCT138 hct138_1 (
    .Y0(EN0), .Y1(EN1), .Y2(EN2), .Y3(EN3), .Y4(EN4), .Y5(EN5), .Y6(EN6), .Y7(EN7), .A(RS0), .G1(PHI2),
    .nG2A(RS3), .B(RS1), .nG2B(nCS), .C(RS2));
  HCT138 hct138_2 (
    .Y0(EN8), .Y1(EN9), .Y2(EN10), .Y3(EN11), .Y4(EN12), .Y5(EN13), .Y6(EN14), .Y7(EN15), .A(RS0), .G1(RS3),
    .nG2A(nPHI2), .B(RS1), .nG2B(nCS), .C(RS2));
endmodule

module ddra (
  input  [7:0] D,
  input  nPHI2,
  input  nRES,
  input  ENAND,
  input  EN,
  output [7:0] DDR,
  output [7:0] Q
);

  wire nand_1_out, nand_2_out, not_1_out, not_2_out, or_1_out;

  nand nand_1 (nand_1_out, EN, nRES);
  or or_1 (or_1_out, ENAND, EN);
  nand nand_2 (nand_2_out, nand_1_out, ENAND);
  Register ddra (.D(D), .en(not_1_out), .Q(DDR), .clk(nPHI2));  // open: clr
  not not_1 (not_1_out, nand_2_out);
  assign Q = not_2_out ? DDR : 8'bz;  // Controlled_Buffer controlled_buffer_1
  not not_2 (not_2_out, or_1_out);
endmodule

module ddrb (
  input  [7:0] D,
  input  nPHI2,
  input  nRES,
  input  ENAND,
  input  EN,
  output [7:0] DDR,
  output [7:0] Q
);

  wire nand_1_out, nand_2_out, not_1_out, not_2_out, or_1_out;

  nand nand_1 (nand_1_out, EN, nRES);
  nand nand_2 (nand_2_out, nand_1_out, ENAND);
  or or_1 (or_1_out, ENAND, EN);
  Register ddrb (.D(D), .en(not_1_out), .Q(DDR), .clk(nPHI2));  // open: clr
  not not_1 (not_1_out, nand_2_out);
  not not_2 (not_2_out, or_1_out);
  assign Q = not_2_out ? DDR : 8'bz;  // Controlled_Buffer controlled_buffer_1
endmodule

module porta (
  input  [7:0] DDR,
  input  [7:0] D,
  input  nPHI2,
  input  nRES,
  input  ENAND,
  input  EN,
  input  [7:0] PORTI,
  output [7:0] PORTO,
  output [7:0] Q
);

  wire nand_1_out, nand_2_out, not_1_out, not_2_out, or_1_out;
  wire [7:0] and_1_out, not_3_out, PORTA_q;

  nand nand_1 (nand_1_out, nRES, EN);
  or or_1 (or_1_out, ENAND, EN);
  nand nand_2 (nand_2_out, nand_1_out, ENAND);
  Pull_Resistor #(.pull(1)) pull_resistor_1 (.node(PORTI));
  not not_1 (not_1_out, nand_2_out);
  assign PORTI[7] = and_1_out[7] ? 1'b0 : 1'bz;  // Controlled_Buffer controlled_buffer_1
  assign PORTI[6] = and_1_out[6] ? 1'b0 : 1'bz;  // Controlled_Buffer controlled_buffer_2
  assign Q = not_2_out ? PORTI : 8'bz;  // Controlled_Buffer controlled_buffer_3
  not not_2 (not_2_out, or_1_out);
  Register PORTA (.D(D), .en(not_1_out), .Q(PORTA_q), .clk(nPHI2));  // open: clr
  assign PORTI[5] = and_1_out[5] ? 1'b0 : 1'bz;  // Controlled_Buffer controlled_buffer_4
  assign PORTI[4] = and_1_out[4] ? 1'b0 : 1'bz;  // Controlled_Buffer controlled_buffer_5
  assign PORTI[3] = and_1_out[3] ? 1'b0 : 1'bz;  // Controlled_Buffer controlled_buffer_6
  assign not_3_out = ~PORTA_q;  // NOT_Gate not_3, 8 bits wide
  assign PORTI[2] = and_1_out[2] ? 1'b0 : 1'bz;  // Controlled_Buffer controlled_buffer_7
  assign PORTI[1] = and_1_out[1] ? 1'b0 : 1'bz;  // Controlled_Buffer controlled_buffer_8
  assign PORTI[0] = and_1_out[0] ? 1'b0 : 1'bz;  // Controlled_Buffer controlled_buffer_9
  assign and_1_out = DDR & not_3_out;  // AND_Gate and_1, 8 bits wide

  assign PORTO = PORTI;
endmodule

module portb (
  input  [7:0] DDR,
  input  [7:0] D,
  input  nPHI2,
  input  nRES,
  input  TAOUT,
  input  PB6ON,
  input  TBOUT,
  input  PB7ON,
  input  ENAND,
  input  EN,
  input  [7:0] PORTI,
  output nPC,
  output [7:0] PORTO,
  output [7:0] Q
);

  wire nand_1_out, nand_2_out, not_1_out, not_2_out, or_1_out;
  wire [7:0] and_1_out, not_3_out, PORTB_q;
  wire [7:6] multiplexer_1_out, or_2_out;

  nand nand_1 (nand_1_out, nRES, EN);
  or or_1 (or_1_out, ENAND, EN);
  D_Flip_Flop d_ff_1 (.clk(nPHI2), .D(EN), .Q(nPC));  // open: Qn, preset, reset
  nand nand_2 (nand_2_out, nand_1_out, ENAND);
  not not_1 (not_1_out, nand_2_out);
  assign PORTI[7] = and_1_out[7] ? 1'b0 : 1'bz;  // Controlled_Buffer controlled_buffer_1
  assign PORTI[6] = and_1_out[6] ? 1'b0 : 1'bz;  // Controlled_Buffer controlled_buffer_2
  Pull_Resistor #(.pull(1)) pull_resistor_1 (.node(PORTI));
  assign Q = not_2_out ? PORTI : 8'bz;  // Controlled_Buffer controlled_buffer_3
  not not_2 (not_2_out, or_1_out);
  Register PORTB (.D(D), .en(not_1_out), .Q(PORTB_q), .clk(nPHI2));  // open: clr
  assign PORTI[5] = and_1_out[5] ? 1'b0 : 1'bz;  // Controlled_Buffer controlled_buffer_4
  assign PORTI[4] = and_1_out[4] ? 1'b0 : 1'bz;  // Controlled_Buffer controlled_buffer_5
  Multiplexer #(.enable("false")) multiplexer_1 (
    .in0(PORTB_q[6]), .in1(TAOUT), .out(multiplexer_1_out[6]), .sel(PB6ON));
  Multiplexer #(.enable("false")) multiplexer_2 (
    .in0(PORTB_q[7]), .in1(TBOUT), .out(multiplexer_1_out[7]), .sel(PB7ON));
  assign PORTI[3] = and_1_out[3] ? 1'b0 : 1'bz;  // Controlled_Buffer controlled_buffer_6
  assign PORTI[2] = and_1_out[2] ? 1'b0 : 1'bz;  // Controlled_Buffer controlled_buffer_7
  assign PORTI[1] = and_1_out[1] ? 1'b0 : 1'bz;  // Controlled_Buffer controlled_buffer_8
  or or_2 (or_2_out[6], DDR[6], PB6ON);
  or or_3 (or_2_out[7], DDR[7], PB7ON);
  assign PORTI[0] = and_1_out[0] ? 1'b0 : 1'bz;  // Controlled_Buffer controlled_buffer_9
  assign and_1_out = {or_2_out, DDR[5:0]} & not_3_out;  // AND_Gate and_1, 8 bits wide
  assign not_3_out = ~{multiplexer_1_out, PORTB_q[5:0]};  // NOT_Gate not_3, 8 bits wide

  assign PORTO = PORTI;
endmodule

module timera (
  input  PHI2,
  input  [7:0] D,
  input  nPHI2,
  input  START,
  input  INMODE,
  input  CNT,
  input  nRES,
  input  ENLO,
  input  ENAND,
  input  LOAD,
  input  ENHI,
  input  OUTMODE,
  output [7:0] Q,
  output UNDERFLOW,
  output PULSEOUT,
  output TOUT
);

  wire and_1_out, and_2_out, d_ff_1_qn, d_ff_2_q, d_ff_3_qn, d_ff_4_q, d_ff_5_q, d_ff_6_qn, d_ff_7_q,
       d_ff_8_qn, multiplexer_1_out, nand_1_out, nand_2_out, nand_5_out, nor_1_out, nor_2_out, not_1_out,
       not_2_out, not_3_out, not_4_out, not_5_out, not_6_out, not_7_out, not_8_out, not_9_out, OEHI, OELO,
       timer16_1_p10, timerpulse_1_phi8, WEHI, WELO;
  wire [7:0] register_1_q, register_2_q;

  timerpulse timerpulse_1 (.PHI8(timerpulse_1_phi8), .in_1(PHI2));  // open: PHI6, PHI4, PHI2
  buf and_1 (and_1_out, PHI2);  // AND_Gate
  D_Flip_Flop d_ff_1 (.clk(CNT), .D(1'b1), .Qn(d_ff_1_qn), .reset(not_1_out));  // open: Q, preset
  not not_1 (not_1_out, d_ff_1_qn);
  nand nand_1 (nand_1_out, nRES, ENLO);
  nand nand_2 (nand_2_out, nRES, ENHI);
  or or_1 (OELO, ENLO, ENAND);
  or or_2 (OEHI, ENHI, ENAND);
  not not_2 (not_2_out, WELO);
  not not_3 (not_3_out, WEHI);
  D_Flip_Flop d_ff_2 (.clk(timerpulse_1_phi8), .D(1'b0), .Q(d_ff_2_q), .preset(not_4_out));  // open: Qn, reset
  not not_4 (not_4_out, d_ff_1_qn);
  nand nand_3 (WELO, nand_1_out, ENAND);
  nand nand_4 (WEHI, ENAND, nand_2_out);
  Register register_1 (.D(D), .en(not_2_out), .Q(register_1_q), .clk(nPHI2));  // open: clr
  Register register_2 (.D(D), .en(not_3_out), .Q(register_2_q), .clk(nPHI2));  // open: clr
  D_Flip_Flop d_ff_3 (.clk(timerpulse_1_phi8), .D(d_ff_2_q), .Qn(d_ff_3_qn));  // open: Q, preset, reset
  D_Flip_Flop d_ff_4 (.clk(nPHI2), .D(1'b1), .Q(d_ff_4_q), .reset(not_5_out));  // open: Qn, preset
  not not_5 (not_5_out, nor_1_out);
  and and_2 (and_2_out, START, nand_5_out);
  nand nand_5 (nand_5_out, INMODE, d_ff_3_qn);
  D_Flip_Flop d_ff_5 (.clk(timerpulse_1_phi8), .D(and_2_out), .Q(d_ff_5_q), .reset(not_6_out));  // open: Qn, preset
  not not_6 (not_6_out, nor_1_out);
  and and_3 (UNDERFLOW, d_ff_5_q, timer16_1_p10);
  nor nor_1 (nor_1_out, UNDERFLOW, LOAD, nor_2_out);
  nor nor_2 (nor_2_out, START, WEHI, 1'b0);
  // timer16 timer16_1: pin names not known; wires that end beside it: and_1_out, d_ff_5_q, OELO, OEHI, register_1_q, register_2_q, d_ff_4_q, nRES, Q, timer16_1_p10
  not not_7 (not_7_out, UNDERFLOW);
  D_Flip_Flop d_ff_6 (.clk(PHI2), .D(1'b0), .Q(PULSEOUT), .Qn(d_ff_6_qn), .preset(not_8_out));  // open: reset
  not not_8 (not_8_out, not_7_out);
  D_Flip_Flop d_ff_7 (.clk(START), .D(1'b1), .Q(d_ff_7_q), .reset(PHI2));  // open: Qn, preset
  D_Flip_Flop d_ff_8 (.clk(PULSEOUT), .D(d_ff_8_qn), .Qn(d_ff_8_qn), .preset(d_ff_7_q), .reset(not_9_out));  // open: Q
  not not_9 (not_9_out, nRES);
  Multiplexer #(.enable("false")) multiplexer_1 (
    .in0(d_ff_6_qn), .in1(d_ff_8_qn), .out(multiplexer_1_out), .sel(OUTMODE));
  not not_10 (TOUT, multiplexer_1_out);

  // Notes on the sheet:
  //   PHI_8
endmodule

module timerb (
  input  PHI2,
  input  [7:0] D,
  input  nPHI2,
  input  INMODE0,
  input  START,
  input  INMODE1,
  input  CNT,
  input  PULSEA,
  input  nRES,
  input  LOAD,
  input  ENLO,
  input  ENAND,
  input  ENHI,
  input  OUTMODE,
  output [7:0] Q,
  output UNDERFLOW,
  output PULSEOUT,
  output TOUT
);

  wire and_1_out, and_2_out, and_3_out, d_ff_1_q, d_ff_2_qn, d_ff_3_q, d_ff_4_q, d_ff_5_q, d_ff_6_q,
       d_ff_7_qn, d_ff_8_q, d_ff_9_qn, multiplexer_1_out, multiplexer_2_out, nand_1_out, nand_2_out,
       nor_1_out, nor_2_out, not_1_out, not_2_out, not_3_out, not_4_out, not_5_out, not_6_out, not_7_out,
       not_8_out, not_9_out, OEHI, OELO, timer16_1_p10, timerpulse_1_phi8, WEHI, WELO;
  wire [7:0] register_1_q, register_2_q;

  timerpulse timerpulse_1 (.PHI8(timerpulse_1_phi8), .PHI4(PHI2), .in_1(PHI2));  // open: PHI6, PHI2
  D_Flip_Flop d_ff_1 (.clk(PHI2), .D(PULSEA), .Q(d_ff_1_q));  // open: Qn, preset, reset
  buf and_1 (and_1_out, PHI2);  // AND_Gate
  D_Flip_Flop d_ff_2 (.clk(CNT), .D(1'b1), .Qn(d_ff_2_qn), .reset(not_1_out));  // open: Q, preset
  not not_1 (not_1_out, d_ff_2_qn);
  not not_2 (not_2_out, d_ff_2_qn);
  nand nand_1 (nand_1_out, nRES, ENLO);
  nand nand_2 (nand_2_out, nRES, ENHI);
  or or_1 (OELO, ENLO, ENAND);
  or or_2 (OEHI, ENHI, ENAND);
  Register register_1 (.D(D), .en(not_3_out), .Q(register_1_q), .clk(nPHI2));  // open: clr
  not not_3 (not_3_out, WELO);
  Register register_2 (.D(D), .en(not_4_out), .Q(register_2_q), .clk(nPHI2));  // open: clr
  not not_4 (not_4_out, WEHI);
  D_Flip_Flop d_ff_3 (.clk(timerpulse_1_phi8), .D(1'b0), .Q(d_ff_3_q), .preset(not_2_out));  // open: Qn, reset
  nand nand_3 (WELO, nand_1_out, ENAND);
  nand nand_4 (WEHI, ENAND, nand_2_out);
  D_Flip_Flop d_ff_4 (.clk(timerpulse_1_phi8), .D(d_ff_3_q), .Q(d_ff_4_q));  // open: Qn, preset, reset
  and and_2 (and_2_out, d_ff_1_q, CNT);
  Multiplexer #(.enable("false"), .select(2)) multiplexer_1 (
    .in0(1'b1), .in1(d_ff_4_q), .in2(d_ff_1_q), .in3(and_2_out), .out(multiplexer_1_out),
    .sel({INMODE1, INMODE0}));
  D_Flip_Flop d_ff_5 (.clk(nPHI2), .D(1'b1), .Q(d_ff_5_q), .reset(not_5_out));  // open: Qn, preset
  not not_5 (not_5_out, nor_1_out);
  and and_3 (and_3_out, START, multiplexer_1_out);
  D_Flip_Flop d_ff_6 (.clk(timerpulse_1_phi8), .D(and_3_out), .Q(d_ff_6_q), .reset(not_6_out));  // open: Qn, preset
  not not_6 (not_6_out, nor_1_out);
  and and_4 (UNDERFLOW, d_ff_6_q, timer16_1_p10);
  nor nor_1 (nor_1_out, UNDERFLOW, LOAD, nor_2_out);
  nor nor_2 (nor_2_out, START, WEHI, 1'b0);
  // timer16 timer16_1: pin names not known; wires that end beside it: and_1_out, d_ff_6_q, OELO, OEHI, register_1_q, register_2_q, d_ff_5_q, nRES, Q, timer16_1_p10
  not not_7 (not_7_out, UNDERFLOW);
  D_Flip_Flop d_ff_7 (.clk(PHI2), .D(1'b0), .Q(PULSEOUT), .Qn(d_ff_7_qn), .preset(not_8_out));  // open: reset
  not not_8 (not_8_out, not_7_out);
  D_Flip_Flop d_ff_8 (.clk(START), .D(1'b1), .Q(d_ff_8_q), .reset(PHI2));  // open: Qn, preset
  D_Flip_Flop d_ff_9 (.clk(PULSEOUT), .D(d_ff_9_qn), .Qn(d_ff_9_qn), .preset(d_ff_8_q), .reset(not_9_out));  // open: Q
  not not_9 (not_9_out, nRES);
  Multiplexer #(.enable("false")) multiplexer_2 (
    .in0(d_ff_7_qn), .in1(d_ff_9_qn), .out(multiplexer_2_out), .sel(OUTMODE));
  not not_10 (TOUT, multiplexer_2_out);

  // Notes on the sheet:
  //   PHI_8
endmodule

module timer16 (
  input  PULSE,
  input  nOELO,
  input  [7:0] LO,
  input  [7:0] HI,
  input  FORCELOAD,
  input  nOEHI,
  input  nRES,
  output [7:0] Q,
  output UNDERFLOW,
  output [15:0] TIMER
);

  wire and_1_out, hct193_1_ntcd, hct193_2_ntcd, hct193_3_ntcd, not_1_out, not_2_out;

  and and_1 (and_1_out, FORCELOAD, nRES);
  HCT193 hct193_1 (
    .Q3(TIMER[3]), .nTCD(hct193_1_ntcd), .Q0(TIMER[0]), .Q1(TIMER[1]), .Q2(TIMER[2]), .in_8(LO[3]),
    .D0(LO[0]), .D1(LO[1]), .CPU(1'b1), .CPD(PULSE), .nPL(and_1_out), .MR(1'b0), .D2(LO[2]));  // open: nTCU
  HCT193 hct193_2 (
    .Q3(TIMER[7]), .nTCD(hct193_2_ntcd), .Q0(TIMER[4]), .Q1(TIMER[5]), .Q2(TIMER[6]), .in_8(LO[7]),
    .D0(LO[4]), .D1(LO[5]), .CPU(1'b1), .CPD(hct193_1_ntcd), .nPL(and_1_out), .MR(1'b0), .D2(LO[6]));  // open: nTCU
  HCT193 hct193_3 (
    .Q3(TIMER[11]), .nTCD(hct193_3_ntcd), .Q0(TIMER[8]), .Q1(TIMER[9]), .Q2(TIMER[10]), .in_8(HI[3]),
    .D0(HI[0]), .D1(HI[1]), .CPU(1'b1), .CPD(hct193_2_ntcd), .nPL(and_1_out), .MR(1'b0), .D2(HI[2]));  // open: nTCU
  HCT193 hct193_4 (
    .Q3(TIMER[15]), .Q0(TIMER[12]), .Q1(TIMER[13]), .Q2(TIMER[14]), .in_8(HI[7]), .D0(HI[4]), .D1(HI[5]),
    .CPU(1'b1), .CPD(hct193_3_ntcd), .nPL(and_1_out), .MR(1'b0), .D2(HI[6]));  // open: nTCU, nTCD
  not not_1 (not_1_out, nOELO);
  not not_2 (not_2_out, nOEHI);
  assign Q = not_1_out ? TIMER[7:0] : 8'bz;  // Controlled_Buffer controlled_buffer_1
  assign Q = not_2_out ? TIMER[15:8] : 8'bz;  // Controlled_Buffer controlled_buffer_2
  Register #(.trigger("high"), .width(16)) register_1 (.D(TIMER), .clk(1'b1));  // open: en, Q, clr
  nor nor_1 (UNDERFLOW, TIMER[0], TIMER[1], TIMER[2], TIMER[3], TIMER[4], TIMER[5], TIMER[6], TIMER[7], TIMER[8], TIMER[9], TIMER[10], TIMER[11], TIMER[12], TIMER[13], TIMER[14], TIMER[15]);
endmodule

module timerpulse (
  input  in_1,
  output PHI8,
  output PHI6,
  output PHI4,
  output PHI2
);

  wire not_1_out, not_3_out, not_5_out, not_7_out;

  not not_1 (not_1_out, in_1);
  not not_2 (PHI2, not_1_out);
  not not_3 (not_3_out, PHI2);
  not not_4 (PHI4, not_3_out);
  not not_5 (not_5_out, PHI4);
  not not_6 (PHI6, not_5_out);
  not not_7 (not_7_out, PHI6);
  not not_8 (PHI8, not_7_out);
endmodule

module creg (
  input  [7:0] D,
  input  nRES,
  input  ENAND,
  input  nPHI2,
  input  EN,
  input  UNDERFLOW,
  output [7:0] Q,
  output START,
  output PBON,
  output OUTMODE,
  output RUNMODE,
  output LOAD,
  output CR5,
  output CR6,
  output CR7
);

  wire and_1_out, and_2_out, d_ff_2_q, d_ff_3_q, nand_1_out, nand_2_out, not_1_out, not_2_out, not_3_out,
       not_4_out, or_1_out, or_2_out;
  wire [4:0] register_1_q;

  nand nand_1 (nand_1_out, EN, nRES);
  or or_1 (or_1_out, ENAND, EN);
  nand nand_2 (nand_2_out, nand_1_out, ENAND);
  not not_1 (not_1_out, nand_2_out);
  and and_1 (and_1_out, not_1_out, nPHI2);
  not not_2 (not_2_out, nPHI2);
  Register register_1 (
    .D({D[7:5], 1'b0, D[3:1], 1'b0}), .en(not_3_out),
    .Q({CR7, CR6, CR5, register_1_q[4], RUNMODE, OUTMODE, PBON, register_1_q[0]}), .clk(nPHI2));  // open: clr
  not not_3 (not_3_out, nand_2_out);
  D_Flip_Flop d_ff_1 (.clk(and_1_out), .D(D[0]), .Q(START), .reset(and_2_out));  // open: Qn, preset
  D_Flip_Flop d_ff_2 (.clk(and_1_out), .D(D[4]), .Q(d_ff_2_q), .reset(not_2_out));  // open: Qn, preset
  D_Flip_Flop d_ff_3 (.clk(not_2_out), .D(RUNMODE), .Q(d_ff_3_q));  // open: Qn, preset, reset
  D_Flip_Flop d_ff_4 (.clk(not_2_out), .D(d_ff_2_q), .Q(LOAD));  // open: Qn, preset, reset
  or or_2 (or_2_out, d_ff_3_q, RUNMODE);
  and and_2 (and_2_out, or_2_out, UNDERFLOW);
  assign Q = not_4_out ? {CR7, CR6, CR5, register_1_q[4], RUNMODE, OUTMODE, PBON, START} : 8'bz;  // Controlled_Buffer controlled_buffer_1
  not not_4 (not_4_out, or_1_out);
  Register #(.trigger("high")) creg (
    .D({CR7, CR6, CR5, LOAD, RUNMODE, OUTMODE, PBON, START}), .clk(1'b1));  // open: en, Q, clr
endmodule

module tod (
  input  [7:0] D,
  input  nRES,
  input  TODIN,
  input  ENAND,
  input  EN8,
  input  EN9,
  input  EN10,
  input  EN11,
  input  ALARM,
  input  nPHI2,
  input  TOD,
  output [7:0] Q,
  output [31:0] ALARMBUS,
  output TODIRQ,
  output [31:0] TODBUS
);

  wire AMPM_FL, and_1_out, and_2_out, and_3_out, and_4_out, and_5_out, and_6_out, and_7_out, and_8_out,
       and_9_out, and_15_out, and_17_out, d_ff_1_qn, d_ff_2_qn, d_ff_3_q, d_ff_5_q, HOUHI_FL, HOULO_CN,
       HOULO_LD, HOULO_MR, HOUR_LD, LATCH, MIN_LD, MINHI_CN, MINLO_CN, nand_1_out, nand_2_out, nand_3_out,
       nand_4_out, nand_5_out, nand_6_out, nand_7_out, nand_8_out, not_1_out, not_2_out, not_3_out,
       not_4_out, not_5_out, not_6_out, not_7_out, not_8_out, not_9_out, not_10_out, not_11_out, not_12_out,
       not_13_out, not_14_out, not_15_out, OEH, OEM, OES, OET, or_1_out, or_2_out, SEC_LD, SECHI_CN,
       SECLO_CN, TENTH_CN, TENTH_LD, TICKR_CN, WEAH, WEAM, WEAS, WEAT;
  wire [6:5] register_4_q;
  wire [7:0] register_5_q, register_6_q, register_7_q, register_8_q;
  wire [7:4] register_1_q;
  wire [7:7] register_2_q, register_3_q;
  wire [31:0] xor_1_out;

  not not_1 (not_1_out, WEAT);
  not not_2 (not_2_out, WEAS);
  not not_3 (not_3_out, WEAM);
  not not_4 (not_4_out, WEAH);
  not not_5 (not_5_out, nRES);
  Register register_1 (
    .D({4'b0000, D[3:0]}), .en(not_1_out), .Q({register_1_q, ALARMBUS[7:4]}), .clk(nPHI2), .clr(not_5_out));
  Register register_2 (
    .D({1'b0, D[6:0]}), .en(not_2_out), .Q({register_2_q[7], ALARMBUS[14:8]}), .clk(nPHI2), .clr(not_5_out));
  Register register_3 (
    .D({1'b0, D[6:0]}), .en(not_3_out), .Q({register_3_q[7], ALARMBUS[22:16]}), .clk(nPHI2), .clr(not_5_out));
  Register register_4 (
    .D({D[7], 2'b00, D[4:0]}), .en(not_4_out), .Q({ALARMBUS[31], register_4_q, ALARMBUS[28:24]}),
    .clk(nPHI2), .clr(not_5_out));
  not not_6 (not_6_out, or_1_out);
  or or_1 (or_1_out, ~nRES, HOUR_LD);  // OR_Gate
  or or_2 (or_2_out, or_1_out, D[0]);
  and and_1 (and_1_out, not_6_out, D[1]);
  and and_2 (and_2_out, not_6_out, D[2]);
  and and_3 (and_3_out, not_6_out, D[3]);
  and and_4 (and_4_out, not_6_out, D[4], nPHI2);
  and and_5 (and_5_out, not_6_out, ~D[4], nPHI2);  // AND_Gate
  and and_6 (and_6_out, not_6_out, D[7], nPHI2);
  and and_7 (and_7_out, not_6_out, ~D[7], nPHI2);  // AND_Gate
  D_Flip_Flop d_ff_1 (
    .clk(HOUHI_FL), .D(d_ff_1_qn), .Q(TODBUS[28]), .Qn(d_ff_1_qn), .preset(and_4_out), .reset(and_5_out));
  D_Flip_Flop d_ff_2 (
    .clk(AMPM_FL), .D(d_ff_2_qn), .Q(TODBUS[31]), .Qn(d_ff_2_qn), .preset(and_6_out), .reset(and_7_out));
  HCT193 TICKER (
    .Q3(TODBUS[3]), .Q0(TODBUS[0]), .Q1(TODBUS[1]), .Q2(TODBUS[2]), .in_8(1'b0), .D0(1'b0), .D1(1'b0),
    .CPU(TICKR_CN), .CPD(1'b1), .nPL(1'b1), .MR(TENTH_CN), .D2(1'b0));  // open: nTCU, nTCD
  HCT193 TENTHS (
    .Q3(TODBUS[7]), .Q0(TODBUS[4]), .Q1(TODBUS[5]), .Q2(TODBUS[6]), .in_8(D[3]), .D0(D[0]), .D1(D[1]),
    .CPU(TENTH_CN), .CPD(1'b1), .nPL(TENTH_LD), .MR(SECLO_CN), .D2(D[2]));  // open: nTCU, nTCD
  HCT193 SECLO (
    .Q3(TODBUS[11]), .Q0(TODBUS[8]), .Q1(TODBUS[9]), .Q2(TODBUS[10]), .in_8(D[3]), .D0(D[0]), .D1(D[1]),
    .CPU(SECLO_CN), .CPD(1'b1), .nPL(SEC_LD), .MR(SECHI_CN), .D2(D[2]));  // open: nTCU, nTCD
  HCT193 SECHI (
    .Q3(TODBUS[15]), .Q0(TODBUS[12]), .Q1(TODBUS[13]), .Q2(TODBUS[14]), .in_8(D[7]), .D0(D[4]), .D1(D[5]),
    .CPU(SECHI_CN), .CPD(1'b1), .nPL(SEC_LD), .MR(MINLO_CN), .D2(D[6]));  // open: nTCU, nTCD
  HCT193 MINLO (
    .Q3(TODBUS[19]), .Q0(TODBUS[16]), .Q1(TODBUS[17]), .Q2(TODBUS[18]), .in_8(D[3]), .D0(D[0]), .D1(D[1]),
    .CPU(MINLO_CN), .CPD(1'b1), .nPL(MIN_LD), .MR(MINHI_CN), .D2(D[2]));  // open: nTCU, nTCD
  HCT193 MINHI (
    .Q3(TODBUS[23]), .Q0(TODBUS[20]), .Q1(TODBUS[21]), .Q2(TODBUS[22]), .in_8(D[7]), .D0(D[4]), .D1(D[5]),
    .CPU(MINHI_CN), .CPD(1'b1), .nPL(MIN_LD), .MR(HOULO_CN), .D2(D[6]));  // open: nTCU, nTCD
  HCT193 HOURLO (
    .Q3(TODBUS[27]), .Q0(TODBUS[24]), .Q1(TODBUS[25]), .Q2(TODBUS[26]), .in_8(and_3_out), .D0(or_2_out),
    .D1(and_1_out), .CPU(HOULO_CN), .CPD(1'b1), .nPL(HOULO_LD), .MR(HOULO_MR), .D2(and_2_out));  // open: nTCU, nTCD
  and and_8 (and_8_out, ~TODIN, TODBUS[1], TODBUS[2]);  // AND_Gate
  and and_9 (and_9_out, TODIN, TODBUS[2], TODBUS[0]);
  and and_10 (SECLO_CN, TODBUS[5], TODBUS[7]);
  and and_11 (SECHI_CN, TODBUS[9], TODBUS[11]);
  and and_12 (MINLO_CN, TODBUS[13], TODBUS[14]);
  and and_13 (MINHI_CN, TODBUS[17], TODBUS[19]);
  and and_14 (HOULO_CN, TODBUS[21], TODBUS[22]);
  and and_15 (and_15_out, TODBUS[28], ~TODBUS[27], TODBUS[25]);  // AND_Gate
  or or_3 (TENTH_CN, and_8_out, and_9_out);
  and and_16 (HOULO_MR, TODBUS[25], TODBUS[27], ~TODBUS[28]);  // AND_Gate
  and and_17 (and_17_out, TODBUS[28], TODBUS[24], TODBUS[25]);
  D_Flip_Flop d_ff_3 (.clk(nPHI2), .D(1'b1), .Q(d_ff_3_q), .reset(and_17_out));  // open: Qn, preset
  D_Flip_Flop d_ff_4 (.clk(nPHI2), .D(1'b0), .Q(AMPM_FL), .preset(and_15_out), .reset(not_6_out));  // open: Qn
  or or_4 (HOUHI_FL, HOULO_MR, and_17_out);
  and and_18 (HOULO_LD, d_ff_3_q, HOUR_LD);
  not not_7 (not_7_out, TENTH_LD);
  not not_8 (not_8_out, OET);
  nand nand_1 (nand_1_out, EN8, nRES);
  nand nand_2 (nand_2_out, EN9, nRES);
  nand nand_3 (nand_3_out, EN10, nRES);
  nand nand_4 (nand_4_out, EN11, nRES);
  or or_5 (OET, EN8, ENAND);
  or or_6 (OEM, EN10, ENAND);
  assign xor_1_out = {TODBUS[31], 2'b00, TODBUS[28:0]} ^ {ALARMBUS[31], 2'b00, ALARMBUS[28:24], 1'b0, ALARMBUS[22:16], 1'b0, ALARMBUS[14:4], 4'b0000};  // XOR_Gate xor_1, 32 bits wide
  D_Flip_Flop d_ff_5 (.clk(nRES), .D(1'b0), .Q(d_ff_5_q), .preset(not_7_out), .reset(not_9_out));  // open: Qn
  not not_9 (not_9_out, HOUR_LD);
  D_Flip_Flop d_ff_6 (.clk(nRES), .D(1'b1), .Q(LATCH), .preset(not_8_out), .reset(not_10_out));  // open: Qn
  not not_10 (not_10_out, OEH);
  nand nand_5 (nand_5_out, nand_1_out, ENAND);
  nand nand_6 (nand_6_out, nand_2_out, ENAND);
  nand nand_7 (nand_7_out, nand_3_out, ENAND);
  not not_11 (not_11_out, ALARM);
  nand nand_8 (nand_8_out, nand_4_out, ENAND);
  or or_7 (OES, EN9, ENAND);
  or or_8 (OEH, EN11, ENAND);
  and and_19 (TICKR_CN, TOD, d_ff_5_q);
  or or_9 (TENTH_LD, nand_5_out, ALARM);
  or or_10 (SEC_LD, nand_6_out, ALARM);
  or or_11 (MIN_LD, nand_7_out, ALARM);
  or or_12 (HOUR_LD, nand_8_out, ALARM);
  or or_13 (WEAT, nand_5_out, not_11_out);
  or or_14 (WEAS, nand_6_out, not_11_out);
  or or_15 (WEAM, nand_7_out, not_11_out);
  or or_16 (WEAH, nand_8_out, not_11_out);
  nor nor_1 (TODIRQ, xor_1_out[0], xor_1_out[1], xor_1_out[2], xor_1_out[3], xor_1_out[4], xor_1_out[5], xor_1_out[6], xor_1_out[7], xor_1_out[8], xor_1_out[9], xor_1_out[10], xor_1_out[11], xor_1_out[12], xor_1_out[13], xor_1_out[14], xor_1_out[15], xor_1_out[17], xor_1_out[18], xor_1_out[19], xor_1_out[20], xor_1_out[21], xor_1_out[22], xor_1_out[23], xor_1_out[24], xor_1_out[25], xor_1_out[26], xor_1_out[27], xor_1_out[28], xor_1_out[29], xor_1_out[30], xor_1_out[31], xor_1_out[16]);
  assign Q = not_12_out ? register_5_q : 8'bz;  // Controlled_Buffer controlled_buffer_1
  Register #(.trigger("high")) register_5 (.D({4'b0000, TODBUS[7:4]}), .Q(register_5_q), .clk(LATCH));  // open: en, clr
  not not_12 (not_12_out, OET);
  assign Q = not_13_out ? register_6_q : 8'bz;  // Controlled_Buffer controlled_buffer_2
  Register #(.trigger("high")) register_6 (.D(TODBUS[15:8]), .Q(register_6_q), .clk(LATCH));  // open: en, clr
  not not_13 (not_13_out, OES);
  assign Q = not_14_out ? register_7_q : 8'bz;  // Controlled_Buffer controlled_buffer_3
  Register #(.trigger("high")) register_7 (.D(TODBUS[23:16]), .Q(register_7_q), .clk(LATCH));  // open: en, clr
  not not_14 (not_14_out, OEM);
  assign Q = not_15_out ? register_8_q : 8'bz;  // Controlled_Buffer controlled_buffer_4
  Register #(.trigger("high")) register_8 (
    .D({TODBUS[31], 2'b00, TODBUS[28:24]}), .Q(register_8_q), .clk(LATCH));  // open: en, clr
  not not_15 (not_15_out, OEH);

  assign {ALARMBUS[30:29], ALARMBUS[23], ALARMBUS[15], ALARMBUS[3:0]} = {8{1'b0}};
  assign TODBUS[30:29] = 2'b00;

  // Other names for the same wires on the sheet: MINHI_MR = HOULO_CN; MINLO_MR = MINHI_CN; SECHI_MR = MINLO_CN;
  //   SECLO_MR = SECHI_CN; TENTH_MR = SECLO_CN; TICKR_MR = TENTH_CN
endmodule

module clockdivider (
  input  in_1,
  output out_2
);

  wire counter_1_carry;

  Counter #(.max('hf), .width(4)) counter_1 (.carry(counter_1_carry), .clk(in_1));  // open: load, D, count, Q, clr
  T_Flip_Flop t_ff_1 (.clk(counter_1_carry), .T(1'b1), .Q(out_2));  // open: Qn, preset, reset
endmodule

module sdr (
  input  nPHI,
  input  [7:0] D,
  input  nRES,
  input  EN,
  input  ENAND,
  input  TARUNMODE,
  input  TASTART,
  input  iCNT,
  input  iSP,
  input  TAPULSE,
  input  SPMODE,
  output [7:0] Q,
  output oSP,
  output SERIRQ,
  output oCNT
);

  wire and_1_out, and_2_out, and_3_out, and_4_out, and_5_out, and_6_out, and_7_out, and_8_out, and_9_out,
       and_10_out, and_11_out, d_ff_1_q, d_ff_2_q, d_ff_2_qn, d_ff_3_q, d_ff_3_qn, hct193_1_q3, hct193_2_q3,
       hct299_2_q0, hct299_2_q7, LOAD, nand_1_out, nand_2_out, nCOUNT, not_1_out, not_2_out, not_3_out,
       not_4_out, or_1_out, or_2_out, or_3_out, or_4_out, or_5_out, S0, S0_q, S0_qn, S1, S1_q, S2, S2_qn;
  wire [7:0] controlled_buffer_1_out, register_1_q;

  nand nand_1 (nand_1_out, nRES, EN);
  or or_1 (or_1_out, ENAND, EN);
  and and_1 (and_1_out, nand_1_out, ENAND);
  or or_2 (or_2_out, ~nRES, ~d_ff_2_qn, SPMODE);  // OR_Gate
  assign controlled_buffer_1_out = and_2_out ? D : 8'bz;  // Controlled_Buffer controlled_buffer_1
  and and_2 (and_2_out, and_1_out, d_ff_2_qn);
  HCT299 hct299_1 (
    .I(controlled_buffer_1_out), .DSL(nRES), .nMR(nRES), .DSR(iSP), .S0(1'b1), .S1(1'b0), .CP(iCNT),
    .nOE1(d_ff_2_qn), .nOE2(d_ff_2_qn));  // open: Q7, Q0, O
  HCT193 hct193_1 (
    .Q3(hct193_1_q3), .in_8(1'b0), .D0(1'b0), .D1(1'b0), .CPU(iCNT), .CPD(1'b1), .nPL(1'b1), .MR(or_2_out),
    .D2(1'b0));  // open: nTCU, nTCD, Q0, Q1, Q2
  D_Flip_Flop d_ff_1 (.clk(hct193_1_q3), .D(1'b1), .Q(d_ff_1_q), .reset(d_ff_1_q));  // open: Qn, preset
  or or_3 (or_3_out, d_ff_2_q, and_1_out);
  D_Flip_Flop d_ff_2 (.clk(nPHI), .D(1'b0), .Q(d_ff_2_q), .Qn(d_ff_2_qn), .preset(d_ff_1_q));  // open: reset
  Register register_1 (.D(controlled_buffer_1_out), .en(or_3_out), .Q(register_1_q), .clk(nPHI));  // open: clr
  and and_3 (and_3_out, d_ff_3_q, ~LOAD);  // AND_Gate
  nand nand_2 (nand_2_out, SPMODE, nRES);
  HCT299 hct299_2 (
    .Q7(hct299_2_q7), .Q0(hct299_2_q0), .DSL(1'b1), .nMR(1'b1), .DSR(hct299_2_q0), .S0(1'b1), .S1(LOAD),
    .CP(and_3_out), .nOE1(1'b1), .nOE2(1'b1), .O(register_1_q));  // open: I
  D_Flip_Flop d_ff_3 (.clk(TAPULSE), .D(d_ff_3_qn), .Q(d_ff_3_q), .Qn(d_ff_3_qn), .preset(nCOUNT), .reset(nand_2_out));
  assign Q = not_1_out ? register_1_q : 8'bz;  // Controlled_Buffer controlled_buffer_2
  not not_1 (not_1_out, or_1_out);
  or or_4 (or_4_out, d_ff_3_qn, nCOUNT);
  or or_5 (or_5_out, nand_2_out, LOAD);
  not not_2 (not_2_out, hct299_2_q7);
  assign oSP = not_2_out ? 1'b0 : 1'bz;  // Controlled_Buffer controlled_buffer_3
  not not_3 (not_3_out, or_4_out);
  and and_4 (and_4_out, and_1_out, ~TARUNMODE, TASTART);  // AND_Gate
  HCT193 hct193_2 (
    .Q3(hct193_2_q3), .in_8(1'b0), .D0(1'b0), .D1(1'b0), .CPU(or_4_out), .CPD(1'b1), .nPL(1'b1),
    .MR(or_5_out), .D2(1'b0));  // open: nTCU, nTCD, Q0, Q1, Q2
  assign oCNT = not_3_out ? 1'b0 : 1'bz;  // Controlled_Buffer controlled_buffer_4
  D_Flip_Flop u_S0 (.clk(nPHI), .D(S0), .Q(S0_q), .Qn(S0_qn), .reset(nand_2_out));  // open: preset
  D_Flip_Flop u_S1 (.clk(nPHI), .D(S1), .Q(S1_q), .Qn(nCOUNT), .reset(nand_2_out));  // open: preset
  D_Flip_Flop u_S2 (.clk(nPHI), .D(S2), .Q(LOAD), .Qn(S2_qn), .reset(nand_2_out));  // open: preset
  not not_4 (not_4_out, hct193_2_q3);
  and and_5 (and_5_out, S0_q, not_4_out);
  or or_6 (S0, and_5_out, and_6_out);
  and and_6 (and_6_out, S1_q, and_4_out, not_4_out);
  or or_7 (S1, LOAD, and_7_out);
  and and_7 (and_7_out, not_4_out, S1_q);
  and and_8 (and_8_out, S0_q, hct193_2_q3);
  and and_9 (and_9_out, hct193_2_q3, and_4_out);
  or or_8 (S2, and_8_out, and_9_out, and_10_out);
  and and_10 (and_10_out, and_4_out, nCOUNT);
  and and_11 (and_11_out, S2_qn, S1_q, S0_qn, hct193_2_q3, ~and_4_out);  // AND_Gate
  or or_9 (SERIRQ, and_11_out, d_ff_2_q);

  // Other names for the same wires on the sheet: nPHI2 = nPHI
endmodule

module icr (
  input  [7:0] D,
  input  EN,
  input  nRES,
  input  ENAND,
  input  nPHI2,
  input  TAPULSE,
  input  TBPULSE,
  input  TODIRQ,
  input  SPIRQ,
  input  FLAG,
  output [7:0] Q,
  output nIRQ
);

  wire d_ff_1_q, d_ff_2_q, ICR7_qn, nand_1_out, nand_4_out, nand_5_out, not_2_out, not_3_out, or_1_out,
       or_2_out;
  wire [4:0] and_1_out, and_2_out, ICR0_q, nand_2_out, nand_3_out, nand_6_out, not_1_out, register_1_q;
  wire [7:5] register_1_q_2;
  wire [7:7] ICR7_q;

  D_Flip_Flop d_ff_1 (.clk(nPHI2), .D(nand_1_out), .Q(d_ff_1_q));  // open: Qn, preset, reset
  assign not_1_out = ~D[4:0];  // NOT_Gate not_1, 5 bits wide
  or or_1 (or_1_out, ENAND, EN);
  nand nand_1 (nand_1_out, nRES, or_1_out);
  D_Flip_Flop d_ff_2 (.clk(nPHI2), .D(d_ff_1_q), .Q(d_ff_2_q));  // open: Qn, preset, reset
  assign nand_2_out = ~(register_1_q & not_1_out);  // NAND_Gate nand_2, 5 bits wide
  assign nand_3_out = ~(D[4:0] & {5{D[7]}});  // NAND_Gate nand_3, 5 bits wide
  nand nand_4 (nand_4_out, EN, nRES);
  nand nand_5 (nand_5_out, nand_4_out, ENAND);
  assign nand_6_out = ~(nand_2_out & nand_3_out);  // NAND_Gate nand_6, 5 bits wide
  not not_2 (not_2_out, nand_5_out);
  D_Flip_Flop ICR0 (.Q(ICR0_q[0]), .preset(TAPULSE), .reset(d_ff_2_q));  // open: clk, D, Qn
  D_Flip_Flop ICR1 (.Q(ICR0_q[1]), .preset(TBPULSE), .reset(d_ff_2_q));  // open: clk, D, Qn
  D_Flip_Flop ICR2 (.Q(ICR0_q[2]), .preset(TODIRQ), .reset(d_ff_2_q));  // open: clk, D, Qn
  D_Flip_Flop ICR3 (.Q(ICR0_q[3]), .preset(SPIRQ), .reset(d_ff_2_q));  // open: clk, D, Qn
  D_Flip_Flop ICR4 (.clk(FLAG), .D(1'b1), .Q(ICR0_q[4]), .reset(d_ff_2_q));  // open: Qn, preset
  D_Flip_Flop ICR7 (.Q(ICR7_q[7]), .Qn(ICR7_qn), .preset(or_2_out), .reset(d_ff_2_q));  // open: clk, D
  assign and_1_out = nand_6_out & {5{nRES}};  // AND_Gate and_1, 5 bits wide
  Register register_1 (
    .D({3'b000, and_1_out}), .en(not_2_out), .Q({register_1_q_2, register_1_q}), .clk(nPHI2));  // open: clr
  assign and_2_out = register_1_q & ICR0_q;  // AND_Gate and_2, 5 bits wide
  D_Flip_Flop d_ff_3 (.clk(nPHI2), .D(ICR7_qn), .Q(nIRQ));  // open: Qn, preset, reset
  or or_2 (or_2_out, and_2_out[0], and_2_out[1], and_2_out[2], and_2_out[3], and_2_out[4]);
  Register #(.trigger("high")) register_2 (.D({ICR7_q[7], 2'b00, ICR0_q}), .clk(1'b1));  // open: en, Q, clr
  not not_3 (not_3_out, or_1_out);
  assign Q = not_3_out ? {ICR7_q[7], 2'b00, ICR0_q} : 8'bz;  // Controlled_Buffer controlled_buffer_1
endmodule

module timer16_163 (
  input  PULSE,
  input  DECREMENT,
  input  nOELO,
  input  [7:0] LO,
  input  [7:0] HI,
  input  FORCELOAD,
  input  nOEHI,
  input  nRES,
  output [7:0] Q,
  output UNDERFLOW,
  output [15:0] TIMER
);

  wire and_1_out, hct163_1_q0, hct163_1_q1, hct163_1_q2, hct163_1_q3, hct163_1_tc, hct163_2_q0, hct163_2_q1,
       hct163_2_q2, hct163_2_q3, hct163_2_tc, hct163_3_q0, hct163_3_q1, hct163_3_q2, hct163_3_q3,
       hct163_3_tc, hct163_4_q0, hct163_4_q1, hct163_4_q2, hct163_4_q3, not_1_out, not_2_out, not_3_out,
       not_4_out, not_5_out, not_6_out, not_7_out, not_8_out, not_9_out, not_10_out, not_11_out, not_12_out,
       not_13_out, not_14_out, not_15_out, not_16_out, not_33_out, not_34_out;

  and and_1 (and_1_out, FORCELOAD, nRES);
  not not_1 (not_1_out, LO[0]);
  not not_2 (not_2_out, LO[1]);
  not not_3 (not_3_out, LO[2]);
  not not_4 (not_4_out, LO[3]);
  not not_5 (not_5_out, LO[4]);
  not not_6 (not_6_out, LO[5]);
  not not_7 (not_7_out, LO[6]);
  not not_8 (not_8_out, LO[7]);
  not not_9 (not_9_out, HI[0]);
  not not_10 (not_10_out, HI[1]);
  not not_11 (not_11_out, HI[2]);
  not not_12 (not_12_out, HI[3]);
  not not_13 (not_13_out, HI[4]);
  not not_14 (not_14_out, HI[5]);
  not not_15 (not_15_out, HI[6]);
  not not_16 (not_16_out, HI[7]);
  HCT163 hct163_1 (
    .D0(not_1_out), .D1(not_2_out), .D2(not_3_out), .D3(not_4_out), .CET(1'b1), .CEP(DECREMENT),
    .nPE(and_1_out), .nMR(1'b1), .CP(PULSE), .Q0(hct163_1_q0), .Q1(hct163_1_q1), .Q2(hct163_1_q2),
    .Q3(hct163_1_q3), .TC(hct163_1_tc));
  HCT163 hct163_2 (
    .D0(not_5_out), .D1(not_6_out), .D2(not_7_out), .D3(not_8_out), .CET(hct163_1_tc), .CEP(DECREMENT),
    .nPE(and_1_out), .nMR(1'b1), .CP(PULSE), .Q0(hct163_2_q0), .Q1(hct163_2_q1), .Q2(hct163_2_q2),
    .Q3(hct163_2_q3), .TC(hct163_2_tc));
  HCT163 hct163_3 (
    .D0(not_9_out), .D1(not_10_out), .D2(not_11_out), .D3(not_12_out), .CET(hct163_2_tc), .CEP(DECREMENT),
    .nPE(and_1_out), .nMR(1'b1), .CP(PULSE), .Q0(hct163_3_q0), .Q1(hct163_3_q1), .Q2(hct163_3_q2),
    .Q3(hct163_3_q3), .TC(hct163_3_tc));
  HCT163 hct163_4 (
    .D0(not_13_out), .D1(not_14_out), .D2(not_15_out), .D3(not_16_out), .CET(hct163_3_tc), .CEP(DECREMENT),
    .nPE(and_1_out), .nMR(1'b1), .CP(PULSE), .Q0(hct163_4_q0), .Q1(hct163_4_q1), .Q2(hct163_4_q2),
    .Q3(hct163_4_q3));  // open: TC
  not not_17 (TIMER[0], hct163_1_q0);
  not not_18 (TIMER[1], hct163_1_q1);
  not not_19 (TIMER[2], hct163_1_q2);
  not not_20 (TIMER[3], hct163_1_q3);
  not not_21 (TIMER[4], hct163_2_q0);
  not not_22 (TIMER[5], hct163_2_q1);
  not not_23 (TIMER[6], hct163_2_q2);
  not not_24 (TIMER[7], hct163_2_q3);
  not not_25 (TIMER[8], hct163_3_q0);
  not not_26 (TIMER[9], hct163_3_q1);
  not not_27 (TIMER[10], hct163_3_q2);
  not not_28 (TIMER[11], hct163_3_q3);
  not not_29 (TIMER[12], hct163_4_q0);
  not not_30 (TIMER[13], hct163_4_q1);
  not not_31 (TIMER[14], hct163_4_q2);
  not not_32 (TIMER[15], hct163_4_q3);
  assign Q = not_33_out ? TIMER[7:0] : 8'bz;  // Controlled_Buffer controlled_buffer_1
  not not_33 (not_33_out, nOELO);
  assign Q = not_34_out ? TIMER[15:8] : 8'bz;  // Controlled_Buffer controlled_buffer_2
  not not_34 (not_34_out, nOEHI);
  nor nor_1 (UNDERFLOW, TIMER[0], TIMER[1], TIMER[2], TIMER[3], TIMER[4], TIMER[5], TIMER[6], TIMER[7], TIMER[8], TIMER[9], TIMER[10], TIMER[11], TIMER[12], TIMER[13], TIMER[14], TIMER[15]);
  Register #(.trigger("high"), .width(16)) register_1 (.D(TIMER), .clk(1'b1));  // open: en, Q, clr
endmodule

module tod_working (
  input  TOD,
  input  TODIN,
  input  [7:0] D,
  input  nPHI2,
  output [7:0] Q,
  output TODIRQ,
  output [31:0] TODBUS
);

  wire AMPM_FL, and_1_out, and_2_out, and_3_out, and_4_out, and_5_out, and_6_out, and_7_out, and_8_out,
       and_9_out, and_10_out, and_16_out, and_18_out, COUNT, d_ff_1_qn, d_ff_2_qn, d_ff_3_q, HOUHI_FL,
       HOULO_CN, HOULO_LD, HOULO_MR, HOUR_LD, LATCH, MIN_LD, MINHI_CN, MINLO_CN, not_1_out, not_2_out,
       not_3_out, not_4_out, not_5_out, not_6_out, not_7_out, not_8_out, not_9_out, nRES, OEH, OEM, OES, OET,
       or_1_out, or_2_out, SEC_LD, SECHI_CN, SECLO_CN, TENTH_CN, TENTH_LD;
  wire [7:0] register_1_q, register_2_q, register_3_q, register_4_q;
  wire [31:0] ALARMBUS, xor_1_out;

  and and_1 (and_1_out, TOD, COUNT);
  not not_1 (not_1_out, or_1_out);
  or or_1 (or_1_out, ~nRES, HOUR_LD);  // OR_Gate
  or or_2 (or_2_out, or_1_out, D[0]);
  and and_2 (and_2_out, not_1_out, D[1]);
  and and_3 (and_3_out, not_1_out, D[2]);
  and and_4 (and_4_out, not_1_out, D[3]);
  and and_5 (and_5_out, not_1_out, D[4], nPHI2);
  and and_6 (and_6_out, not_1_out, ~D[4], nPHI2);  // AND_Gate
  and and_7 (and_7_out, not_1_out, D[7], nPHI2);
  and and_8 (and_8_out, not_1_out, ~D[7], nPHI2);  // AND_Gate
  D_Flip_Flop d_ff_1 (
    .clk(HOUHI_FL), .D(d_ff_1_qn), .Q(TODBUS[28]), .Qn(d_ff_1_qn), .preset(and_5_out), .reset(and_6_out));
  D_Flip_Flop d_ff_2 (
    .clk(AMPM_FL), .D(d_ff_2_qn), .Q(TODBUS[31]), .Qn(d_ff_2_qn), .preset(and_7_out), .reset(and_8_out));
  HCT193 TICKER (
    .Q3(TODBUS[3]), .Q0(TODBUS[0]), .Q1(TODBUS[1]), .Q2(TODBUS[2]), .in_8(1'b0), .D0(1'b0), .D1(1'b0),
    .CPU(and_1_out), .CPD(1'b1), .nPL(1'b1), .MR(TENTH_CN), .D2(1'b0));  // open: nTCU, nTCD
  HCT193 TENTHS (
    .Q3(TODBUS[7]), .Q0(TODBUS[4]), .Q1(TODBUS[5]), .Q2(TODBUS[6]), .in_8(D[3]), .D0(D[0]), .D1(D[1]),
    .CPU(TENTH_CN), .CPD(1'b1), .nPL(TENTH_LD), .MR(SECLO_CN), .D2(D[2]));  // open: nTCU, nTCD
  HCT193 SECLO (
    .Q3(TODBUS[11]), .Q0(TODBUS[8]), .Q1(TODBUS[9]), .Q2(TODBUS[10]), .in_8(D[3]), .D0(D[0]), .D1(D[1]),
    .CPU(SECLO_CN), .CPD(1'b1), .nPL(SEC_LD), .MR(SECHI_CN), .D2(D[2]));  // open: nTCU, nTCD
  HCT193 SECHI (
    .Q3(TODBUS[15]), .Q0(TODBUS[12]), .Q1(TODBUS[13]), .Q2(TODBUS[14]), .in_8(D[7]), .D0(D[4]), .D1(D[5]),
    .CPU(SECHI_CN), .CPD(1'b1), .nPL(SEC_LD), .MR(MINLO_CN), .D2(D[6]));  // open: nTCU, nTCD
  HCT193 MINLO (
    .Q3(TODBUS[19]), .Q0(TODBUS[16]), .Q1(TODBUS[17]), .Q2(TODBUS[18]), .in_8(D[3]), .D0(D[0]), .D1(D[1]),
    .CPU(MINLO_CN), .CPD(1'b1), .nPL(MIN_LD), .MR(MINHI_CN), .D2(D[2]));  // open: nTCU, nTCD
  HCT193 MINHI (
    .Q3(TODBUS[23]), .Q0(TODBUS[20]), .Q1(TODBUS[21]), .Q2(TODBUS[22]), .in_8(D[7]), .D0(D[4]), .D1(D[5]),
    .CPU(MINHI_CN), .CPD(1'b1), .nPL(MIN_LD), .MR(HOULO_CN), .D2(D[6]));  // open: nTCU, nTCD
  HCT193 HOURLO (
    .Q3(TODBUS[27]), .Q0(TODBUS[24]), .Q1(TODBUS[25]), .Q2(TODBUS[26]), .in_8(and_4_out), .D0(or_2_out),
    .D1(and_2_out), .CPU(HOULO_CN), .CPD(1'b1), .nPL(HOULO_LD), .MR(HOULO_MR), .D2(and_3_out));  // open: nTCU, nTCD
  and and_9 (and_9_out, ~TODIN, TODBUS[1], TODBUS[2]);  // AND_Gate
  and and_10 (and_10_out, TODIN, TODBUS[2], TODBUS[0]);
  and and_11 (SECLO_CN, TODBUS[5], TODBUS[7]);
  and and_12 (SECHI_CN, TODBUS[9], TODBUS[11]);
  and and_13 (MINLO_CN, TODBUS[13], TODBUS[14]);
  and and_14 (MINHI_CN, TODBUS[17], TODBUS[19]);
  and and_15 (HOULO_CN, TODBUS[21], TODBUS[22]);
  and and_16 (and_16_out, TODBUS[28], ~TODBUS[27], TODBUS[25]);  // AND_Gate
  or or_3 (TENTH_CN, and_9_out, and_10_out);
  and and_17 (HOULO_MR, TODBUS[25], TODBUS[27], ~TODBUS[28]);  // AND_Gate
  and and_18 (and_18_out, TODBUS[28], TODBUS[24], TODBUS[25]);
  D_Flip_Flop d_ff_3 (.clk(nPHI2), .D(1'b1), .Q(d_ff_3_q), .reset(and_18_out));  // open: Qn, preset
  D_Flip_Flop d_ff_4 (.clk(nPHI2), .D(1'b0), .Q(AMPM_FL), .preset(and_16_out), .reset(not_1_out));  // open: Qn
  or or_4 (HOUHI_FL, HOULO_MR, and_18_out);
  and and_19 (HOULO_LD, d_ff_3_q, HOUR_LD);
  not not_2 (not_2_out, TENTH_LD);
  not not_3 (not_3_out, OET);
  assign xor_1_out = {TODBUS[31], 2'b00, TODBUS[28:0]} ^ ALARMBUS;  // XOR_Gate xor_1, 32 bits wide
  D_Flip_Flop d_ff_5 (.clk(nRES), .D(1'b0), .Q(COUNT), .preset(not_2_out), .reset(not_4_out));  // open: Qn
  not not_4 (not_4_out, HOUR_LD);
  D_Flip_Flop d_ff_6 (.clk(nRES), .D(1'b1), .Q(LATCH), .preset(not_3_out), .reset(not_5_out));  // open: Qn
  not not_5 (not_5_out, OEH);
  nor nor_1 (TODIRQ, xor_1_out[0], xor_1_out[1], xor_1_out[2], xor_1_out[3], xor_1_out[4], xor_1_out[5], xor_1_out[6], xor_1_out[7], xor_1_out[8], xor_1_out[9], xor_1_out[10], xor_1_out[11], xor_1_out[12], xor_1_out[13], xor_1_out[14], xor_1_out[15], xor_1_out[17], xor_1_out[18], xor_1_out[19], xor_1_out[20], xor_1_out[21], xor_1_out[22], xor_1_out[23], xor_1_out[24], xor_1_out[25], xor_1_out[26], xor_1_out[27], xor_1_out[28], xor_1_out[29], xor_1_out[30], xor_1_out[31], xor_1_out[16]);
  assign Q = not_6_out ? register_1_q : 8'bz;  // Controlled_Buffer controlled_buffer_1
  Register #(.trigger("high")) register_1 (.D({4'b0000, TODBUS[7:4]}), .Q(register_1_q), .clk(LATCH));  // open: en, clr
  not not_6 (not_6_out, OET);
  assign Q = not_7_out ? register_2_q : 8'bz;  // Controlled_Buffer controlled_buffer_2
  Register #(.trigger("high")) register_2 (.D(TODBUS[15:8]), .Q(register_2_q), .clk(LATCH));  // open: en, clr
  not not_7 (not_7_out, OES);
  assign Q = not_8_out ? register_3_q : 8'bz;  // Controlled_Buffer controlled_buffer_3
  Register #(.trigger("high")) register_3 (.D(TODBUS[23:16]), .Q(register_3_q), .clk(LATCH));  // open: en, clr
  not not_8 (not_8_out, OEM);
  assign Q = not_9_out ? register_4_q : 8'bz;  // Controlled_Buffer controlled_buffer_4
  Register #(.trigger("high")) register_4 (
    .D({TODBUS[31], 2'b00, TODBUS[28:24]}), .Q(register_4_q), .clk(LATCH));  // open: en, clr
  not not_9 (not_9_out, OEH);

  assign TODBUS[30:29] = 2'b00;

  // Other names for the same wires on the sheet: MINHI_MR = HOULO_CN; MINLO_MR = MINHI_CN; SECHI_MR = MINLO_CN;
  //   SECLO_MR = SECHI_CN; TENTH_MR = SECLO_CN; TICKR_MR = TENTH_CN
endmodule
