// Logisim project hct6526.circ as structural Verilog: 1 circuit, main circuit 74hct6526
module _74hct6526 (
  input  TOD,
  input  CNT,
  input  [15:0] A,
  input  nCS,
  input  PHI2,
  input  iSP,
  input  RnW,
  input  nFLAG,
  input  nRES,
  input  [7:0] PAI,
  input  [7:0] iD,
  input  [7:0] PBI,
  output nIRQ,
  output oCNT,
  output oSP,
  output [7:0] PAO,
  output [7:0] oD,
  output [7:0] PBO,
  output nPC
);

  wire buffer_1_out, creg_1_cr5, creg_1_cr6, creg_1_cr7, creg_1_load, creg_1_outmode, creg_1_pbon,
       creg_1_runmode, creg_1_start, creg_2_cr5, creg_2_cr6, creg_2_cr7, creg_2_load, creg_2_outmode,
       creg_2_pbon, creg_2_start, EN0, EN1, EN2, EN3, EN4, EN5, EN6, EN7, EN8, EN9, EN10, EN11, EN12, EN13,
       EN14, EN15, ENABLE_NAND, nPHI2, nRES_t, PHI2_t, sdr_1_p15, timera_1_pulseout, timera_1_tout,
       timera_1_underflow, timerb_1_pulseout, timerb_1_tout, timerb_1_underflow, tod_1_todirq;
  wire [7:0] and_1_out, ddra_1_ddr, ddrb_1_ddr, or_1_out;
  wire [7:7] not_2_out;

  buf buffer_1 (buffer_1_out, PHI2);
  buf buffer_2 (nRES_t, nRES);
  buf buffer_3 (PHI2_t, buffer_1_out);
  not not_1 (nPHI2, buffer_1_out);
  nand nand_1 (ENABLE_NAND, RnW, nRES_t);
  not not_2 (not_2_out[7], nRES);
  assign and_1_out = {8{nRES_t}} & iD;  // AND_Gate and_1, 8 bits wide
  assign or_1_out = iD | {8{not_2_out[7]}};  // OR_Gate or_1, 8 bits wide
  regDecoder regdecoder_1 (
    .EN0(EN0), .EN1(EN1), .EN2(EN2), .EN3(EN3), .EN4(EN4), .EN5(EN5), .EN6(EN6), .EN7(EN7), .EN8(EN8),
    .EN9(EN9), .EN10(EN10), .EN11(EN11), .EN12(EN12), .EN13(EN13), .EN14(EN14), .EN15(EN15), .RS0(A[0]),
    .RS1(A[1]), .RS2(A[2]), .RS3(A[3]), .nCS(nCS), .PHI2(PHI2_t), .nPHI2(nPHI2));
  ddra ddra_1 (.Q(oD), .DDR(ddra_1_ddr), .D(and_1_out), .nRES(nRES_t), .ENAND(ENABLE_NAND), .EN(EN2), .nPHI2(nPHI2));
  porta porta_1 (
    .PORTO(PAO), .Q(oD), .nRES(nRES_t), .ENAND(ENABLE_NAND), .EN(EN0), .D(and_1_out), .nPHI2(nPHI2),
    .PORTI(PAI), .DDR(ddra_1_ddr));
  ddrb ddrb_1 (.Q(oD), .DDR(ddrb_1_ddr), .D(and_1_out), .nRES(nRES_t), .ENAND(ENABLE_NAND), .EN(EN3), .nPHI2(nPHI2));
  portb portb_1 (
    .nPC(nPC), .PORTO(PBO), .Q(oD), .nPHI2(nPHI2), .nRES(nRES_t), .ENAND(ENABLE_NAND), .EN(EN1),
    .D(and_1_out), .PB6ON(creg_1_pbon), .PB7ON(creg_2_pbon), .TAOUT(timera_1_tout), .TBOUT(timerb_1_tout),
    .PORTI(PBI), .DDR(ddrb_1_ddr));
  creg creg_1 (
    .Q(oD), .START(creg_1_start), .PBON(creg_1_pbon), .OUTMODE(creg_1_outmode), .RUNMODE(creg_1_runmode),
    .LOAD(creg_1_load), .CR5(creg_1_cr5), .CR6(creg_1_cr6), .CR7(creg_1_cr7), .D(and_1_out), .nRES(nRES_t),
    .ENAND(ENABLE_NAND), .nPHI2(nPHI2), .EN(EN14), .UNDERFLOW(timera_1_underflow));
  creg creg_2 (
    .Q(oD), .START(creg_2_start), .PBON(creg_2_pbon), .OUTMODE(creg_2_outmode), .LOAD(creg_2_load),
    .CR5(creg_2_cr5), .CR6(creg_2_cr6), .CR7(creg_2_cr7), .D(and_1_out), .nRES(nRES_t), .ENAND(ENABLE_NAND),
    .nPHI2(nPHI2), .EN(EN15), .UNDERFLOW(timerb_1_underflow));  // open: RUNMODE
  timera timera_1 (
    .PULSEOUT(timera_1_pulseout), .TOUT(timera_1_tout), .UNDERFLOW(timera_1_underflow), .Q(oD),
    .nRES(nRES_t), .OUTMODE(creg_1_outmode), .CNT(CNT), .ENLO(EN4), .ENHI(EN5), .D(or_1_out),
    .START(creg_1_start), .INMODE(creg_1_cr5), .LOAD(creg_1_load), .nPHI2(nPHI2), .PHI2(PHI2_t),
    .ENAND(ENABLE_NAND));
  timerb timerb_1 (
    .PULSEOUT(timerb_1_pulseout), .TOUT(timerb_1_tout), .UNDERFLOW(timerb_1_underflow), .Q(oD),
    .nRES(nRES_t), .OUTMODE(creg_2_outmode), .CNT(CNT), .ENLO(EN6), .ENHI(EN7), .nPHI2(nPHI2), .D(or_1_out),
    .INMODE0(creg_2_cr5), .INMODE1(creg_2_cr6), .START(creg_2_start), .LOAD(creg_2_load),
    .PULSEA(timera_1_pulseout), .PHI2(PHI2_t), .ENAND(ENABLE_NAND));
  // sdr sdr_1: pin names not known; wires that end beside it: oD, and_1_out, ENABLE_NAND, nPHI2, nRES_t, creg_1_start, creg_1_runmode, timera_1_pulseout, creg_1_cr6, EN12, CNT, oCNT, iSP, oSP, sdr_1_p15
  tod tod_1 (
    .TODIRQ(tod_1_todirq), .Q(oD), .TODIN(creg_1_cr7), .D(and_1_out), .EN8(EN8), .EN9(EN9), .EN10(EN10),
    .EN11(EN11), .ALARM(creg_2_cr7), .nRES(nRES_t), .ENAND(ENABLE_NAND), .TOD(TOD), .nPHI2(nPHI2));  // open: TODBUS, ALARMBUS
  icr icr_1 (
    .nIRQ(nIRQ), .Q(oD), .D(and_1_out), .EN(EN13), .nRES(nRES_t), .ENAND(ENABLE_NAND), .FLAG(nFLAG),
    .TAPULSE(timera_1_pulseout), .TBPULSE(timerb_1_pulseout), .TODIRQ(tod_1_todirq), .SPIRQ(sdr_1_p15),
    .nPHI2(nPHI2));

  // Notes on the sheet:
  //   DZ BUS
  //   DO BUS
  //   OUTPUT DATA BUS
endmodule
