// Logisim project sbc6526.circ as structural Verilog: 2 circuits, main circuit sbc6526
module sbc6526 (
  input  RDY,
  input  BE,
  input  in_3,
  output [15:0] out_4,
  output [7:0] SYNC
);

  wire button_1_out, CIA_nirq, CIA_npc, CIAEXT_nirq, CIAEXT_npc, CIAEXT_ocnt, CIAEXT_osp, clock_1_out,
       controlled_buffer_1_out, memdecoder_1_ncia, memdecoder_1_nciaext, memdecoder_1_nciares,
       memdecoder_1_oe, memdecoder_1_we, n6502_1_phi2, n6502_1_r_w, not_1_out, not_2_out, not_3_out,
       not_4_out, TERM, undriven;
  wire [7:0] CIA_pao, CIA_pbo;

  Clock clock_1 (.out(clock_1_out));
  _6502 u_6502_1 (
    .A_BUS(out_4), .D_OUT(SYNC), .R_W(n6502_1_r_w), .PHI2(n6502_1_phi2), .PHI0(clock_1_out), .RDY(RDY),
    .BE(BE), .nRS(not_1_out), .nIRQ(controlled_buffer_1_out), .nNMI(not_2_out), .D_IN(SYNC));  // open: AX_OUT, PHI1, SYNC
  not not_1 (not_1_out, in_3);
  not not_2 (not_2_out, button_1_out);
  Button button_1 (.out(button_1_out));
  TTY #(.asciiwidth(8), .cols(20)) tty_1 (.data(SYNC[6:0]), .clk(TERM), .clr(in_3));  // open: we
  memDecoder memdecoder_1 (
    .A(out_4), .R_W(n6502_1_r_w), .PHI2(n6502_1_phi2), .OE(memdecoder_1_oe), .WE(memdecoder_1_we),
    .nCIA(memdecoder_1_ncia), .TERM(TERM), .nCIARES(memdecoder_1_nciares), .nCIAEXT(memdecoder_1_nciaext));
  _74hct6526 CIA (
    .oD(SYNC), .nIRQ(CIA_nirq), .PAO(CIA_pao), .PBO(CIA_pbo), .nPC(CIA_npc), .iD(SYNC), .A(out_4),
    .iSP(CIAEXT_ocnt), .nFLAG(CIAEXT_npc), .nCS(memdecoder_1_ncia), .PHI2(n6502_1_phi2), .TOD(undriven),
    .RnW(n6502_1_r_w), .nRES(memdecoder_1_nciares), .CNT(CIAEXT_osp));  // open: oCNT, oSP, PAI, PBI
  _74hct6526 CIAEXT (
    .oD(SYNC), .oCNT(CIAEXT_ocnt), .oSP(CIAEXT_osp), .nIRQ(CIAEXT_nirq), .nPC(CIAEXT_npc), .iD(SYNC),
    .A(out_4), .iSP(CIAEXT_osp), .nFLAG(CIA_npc), .PAI(CIA_pao), .PBI(CIA_pbo), .nCS(memdecoder_1_nciaext),
    .PHI2(n6502_1_phi2), .TOD(undriven), .RnW(n6502_1_r_w), .nRES(memdecoder_1_nciares), .CNT(CIAEXT_ocnt));  // open: PAO, PBO
  RAM #(.addrWidth(16), .databus("bidir"), .trigger("high"), .\type ("nonvolatile")) ram_1 (
    .addr(out_4), .data(SYNC));  // open: we, oe, clk
  not not_3 (not_3_out, CIA_nirq);
  not not_4 (not_4_out, CIAEXT_nirq);
  assign controlled_buffer_1_out = not_3_out ? 1'b0 : 1'bz;  // Controlled_Buffer controlled_buffer_1
  Pull_Resistor #(.pull(1)) pull_resistor_1 (.node(controlled_buffer_1_out));
  assign controlled_buffer_1_out = not_4_out ? 1'b0 : 1'bz;  // Controlled_Buffer controlled_buffer_2
  // Pins of 7 and 8 bits meet at SYNC

  // Notes on the sheet:
  //   PHI0
  //   NMI
  //   addr
  //   PHI1
  //   PHI2
  //   R/W
  //   DATA
endmodule

module memDecoder (
  input  [15:0] A,
  input  R_W,
  input  PHI2,
  output OE,
  output WE,
  output nCIA,
  output TERM,
  output nCIARES,
  output nCIAEXT
);

  wire and_1_out, decoder_1_out2, decoder_2_out1, decoder_2_out3, not_2_out;
  wire [0:0] not_1_out;

  and and_1 (and_1_out, A[15], ~A[14]);  // AND_Gate
  not not_1 (not_1_out[0], PHI2);
  Decoder #(.enable("false"), .select(2)) decoder_1 (.out2(decoder_1_out2), .sel(A[15:14]));  // open: out0, out1, out3
  Decoder #(.select(3)) decoder_2 (
    .out1(decoder_2_out1), .out3(decoder_2_out3), .sel(A[13:11]), .en(and_1_out));  // open: out0, out2, out4, out5, out6, out7
  Decoder #(.select(2)) decoder_3 (
    .out0(WE), .out2(OE), .sel({R_W, not_1_out[0]}), .en(not_2_out));  // open: out1, out3
  nand nand_1 (nCIARES, WE, ~A[15], A[14], ~A[13], ~A[12]);  // NAND_Gate
  and u_TERM (TERM, WE, ~A[15], A[14], A[13], A[12]);  // AND_Gate
  not not_2 (not_2_out, decoder_1_out2);
  not not_3 (nCIA, decoder_2_out1);
  not not_4 (nCIAEXT, decoder_2_out3);
endmodule
