// Logisim project sbc6526_ex.circ as structural Verilog: 2 circuits, main circuit sbc6526
module sbc6526 (
  input  RDY,
  input  BE,
  output [7:0] out_3,
  output [7:0] out_4,
  output [7:0] out_5,
  output [7:0] out_6,
  output [7:0] out_7,
  output [7:0] out_8,
  output [7:0] out_9,
  output [7:0] out_10,
  output [7:0] out_11,
  output [7:0] out_12,
  output [7:0] out_13,
  output [7:0] out_14,
  output [15:0] out_15,
  output [7:0] out_16,
  output [7:0] out_17,
  output [7:0] out_18,
  output [7:0] out_19,
  output [7:0] out_20,
  output [7:0] out_21,
  output [7:0] out_22,
  output [15:0] out_23,
  output [15:0] out_24,
  output [7:0] out_25,
  output [7:0] out_26,
  output [7:0] out_27,
  output [7:0] out_28,
  output EN14,
  output [7:0] out_30,
  output [7:0] out_31,
  output [15:0] out_32,
  output [15:0] out_33,
  output _1_SP,
  output [7:0] out_35,
  output [7:0] out_36,
  output [31:0] out_37,
  output [31:0] out_38,
  output [31:0] out_39,
  output [31:0] out_40,
  output [15:0] out_41,
  output _1_CNT,
  output PRECOUNT,
  output [7:0] out_44,
  output [7:0] out_45,
  output [15:0] out_46,
  output [7:0] out_47,
  output TBLOAD,
  output [7:0] out_49,
  output _1__PC,
  output [7:0] out_51,
  output [15:0] out_52,
  output TBis0,
  output _1_EN1,
  output CP,
  output S1
);

  wire _1__CS, _1__IRQ, _1__PHI2, _1__RES, _1_EN0, _1_EN2, _1_EN3, _1_EN4, _1_EN5, _1_EN6, _1_EN7, _1_EN8,
       _1_EN9, _1_EN10, _1_EN11, _1_EN12, _1_EN13, _1_EN15, _1_ENABLE_NAND, _1_FLAG, _1_OETAHI, _1_OETALO,
       _1_OETBHI, _1_OETBLO, _1_PHI2, _1_SDRCOUNT, _1_SDRIRQ, _1_SDRLOAD, _1_SDRS0, _1_SDRS1, _1_SDRS2,
       _1_TADECREMENT, _1_TAFL, _1_TALOADPULSE, _1_TAOFDETECT, _1_TAOUT, _1_TAPULSE, _1_TAUNDERFLOW,
       _1_TBDECREMENT, _1_TBFL, _1_TBLOADPULSE, _1_TBOUT, _1_TBPULSE, _1_TBUNDERFLOW, _1_TOD, _1_TODIRQ,
       _1_WETAHI, _1_WETALO, _1_WETBHI, _1_WETBLO, _2__CS, _2__IRQ, _2__PHI2, _2__RES, _2__SDRCOUNT, _2_EN0,
       _2_EN1, _2_EN2, _2_EN3, _2_EN4, _2_EN5, _2_EN6, _2_EN7, _2_EN8, _2_EN9, _2_EN10, _2_EN11, _2_EN12,
       _2_EN13, _2_EN14, _2_EN15, _2_ENABLE_NAND, _2_OETAHI, _2_OETALO, _2_OETBHI, _2_OETBLO, _2_PHI2,
       _2_SDRCOUNT, _2_SDRIRQ, _2_SDRS0, _2_SDRS1, _2_TADECREMENT, _2_TAFL, _2_TALOADPULSE, _2_TAOFDETECT,
       _2_TAOUT, _2_TAPULSE, _2_TAUNDERFLOW, _2_TBDECREMENT, _2_TBFL, _2_TBLOADPULSE, _2_TBOFDETECT,
       _2_TBOUT, _2_TBPULSE, _2_TBUNDERFLOW, _2_TODIRQ, _2_WETAHI, _2_WETALO, _2_WETBHI, _2_WETBLO,
       and_6_out, and_8_out, and_9_out, and_11_out, and_13_out, and_14_out, and_17_out, and_18_out,
       and_19_out, and_20_out, and_22_out, and_23_out, and_25_out, and_26_out, and_29_out, and_30_out,
       and_31_out, and_32_out, and_33_out, and_34_out, and_35_out, and_36_out, and_37_out, and_38_out,
       and_39_out, and_40_out, and_42_out, and_43_out, and_44_out, buffer_1_out, buffer_4_out, buffer_5_out,
       buffer_6_out, buffer_7_out, buffer_8_out, buffer_9_out, buffer_10_out, buffer_11_out, buffer_13_out,
       buffer_15_out, buffer_16_out, buffer_17_out, buffer_18_out, buffer_19_out, buffer_20_out,
       buffer_21_out, buffer_22_out, buffer_23_out, buffer_24_out, buffer_25_out, buffer_26_out,
       buffer_27_out, buffer_28_out, buffer_29_out, buffer_30_out, buffer_31_out, buffer_32_out,
       buffer_33_out, buffer_34_out, buffer_35_out, buffer_36_out, buffer_37_out, buffer_38_out,
       buffer_39_out, buffer_40_out, buffer_41_out, buffer_42_out, buffer_43_out, buffer_44_out,
       buffer_45_out, buffer_46_out, buffer_47_out, buffer_48_out, buffer_49_out, buffer_50_out,
       buffer_51_out, buffer_52_out, buffer_53_out, buffer_54_out, buffer_55_out, buffer_56_out,
       buffer_57_out, buffer_58_out, buffer_59_out, button_2_out, button_3_out, clock_1_out, d_ff_3_qn,
       d_ff_4_q, d_ff_5_q, d_ff_6_q, d_ff_7_qn, d_ff_8_q, d_ff_9_qn, d_ff_11_qn, d_ff_12_qn, d_ff_15_q,
       d_ff_17_q, d_ff_18_q, d_ff_19_q, d_ff_20_q, d_ff_21_qn, d_ff_22_q, d_ff_23_qn, d_ff_25_qn, d_ff_28_q,
       d_ff_29_q, d_ff_30_q, d_ff_31_qn, d_ff_33_q, d_ff_34_q, d_ff_36_q, d_ff_37_q, d_ff_38_qn, d_ff_39_q,
       d_ff_40_q, d_ff_41_q, d_ff_42_qn, d_ff_43_qn, d_ff_47_q, d_ff_49_q, d_ff_50_q, d_ff_52_q, d_ff_53_q,
       d_ff_54_qn, d_ff_55_q, d_ff_56_qn, d_ff_59_q, d_ff_61_qn, d_ff_62_q, d_ff_63_q, d_ff_64_q, d_ff_65_q,
       d_ff_66_q, d_ff_66_qn, d_ff_67_q, d_ff_68_q, d_ff_69_q, d_ff_69_qn, d_ff_70_q, d_ff_71_q, d_ff_72_q,
       d_ff_72_qn, d_ff_73_qn, d_ff_74_q, d_ff_75_qn, d_ff_76_qn, hct193_1_q3, hct193_2_q3, hct193_3_q3,
       hct193_4_q3, hct299_2_q0, hct299_2_q7, hct299_4_q0, hct299_4_q7, ICR7_q, icr_1_nirq,
       multiplexer_5_out, multiplexer_6_out, multiplexer_7_out, multiplexer_8_out, multiplexer_9_out,
       multiplexer_10_out, nand_3_out, nand_4_out, nand_5_out, nand_6_out, nand_7_out, nand_8_out,
       nand_9_out, nand_10_out, nand_11_out, nand_12_out, nand_13_out, nand_14_out, nand_15_out, nand_16_out,
       nand_17_out, nand_18_out, nand_19_out, nand_20_out, nand_21_out, nand_22_out, nand_23_out,
       nand_24_out, nand_25_out, nand_26_out, nand_27_out, nand_28_out, nand_29_out, nand_30_out,
       nand_31_out, nand_32_out, nand_33_out, nand_34_out, nand_35_out, nand_36_out, nand_37_out,
       nand_38_out, nand_39_out, nand_40_out, nand_41_out, nand_42_out, nand_43_out, nand_44_out,
       nand_45_out, nand_46_out, nand_47_out, nand_48_out, nand_49_out, nand_50_out, nand_51_out,
       nand_52_out, nand_53_out, nand_54_out, nand_55_out, nand_56_out, nand_57_out, nand_59_out,
       nand_61_out, nand_62_out, nand_63_out, nand_64_out, nand_65_out, nand_68_out, nand_69_out,
       nand_70_out, nand_71_out, nand_72_out, nand_75_out, nand_76_out, nand_77_out, nand_78_out,
       nand_81_out, nand_82_out, nand_83_out, nand_84_out, nand_85_out, nand_86_out, nand_87_out,
       nand_88_out, nand_91_out, nand_93_out, nor_1_out, nor_3_out, nor_5_out, nor_7_out, not_1_out,
       not_5_out, not_6_out, not_7_out, not_8_out, not_9_out, not_10_out, not_11_out, not_12_out, not_13_out,
       not_14_out, not_16_out, not_17_out, not_18_out, not_19_out, not_20_out, not_21_out, not_22_out,
       not_23_out, not_24_out, not_25_out, not_26_out, not_27_out, not_28_out, not_29_out, not_31_out,
       not_32_out, not_33_out, not_34_out, not_36_out, not_37_out, not_38_out, not_39_out, not_40_out,
       not_42_out, not_43_out, not_44_out, not_45_out, not_46_out, not_47_out, not_48_out, not_50_out,
       not_51_out, not_52_out, not_53_out, not_54_out, not_55_out, not_56_out, not_57_out, not_59_out,
       not_60_out, not_61_out, not_62_out, not_63_out, not_64_out, not_65_out, not_66_out, not_68_out,
       not_69_out, not_70_out, not_71_out, not_72_out, not_73_out, not_74_out, not_75_out, not_76_out,
       not_77_out, not_79_out, not_80_out, not_81_out, not_82_out, not_83_out, not_84_out, not_85_out,
       not_86_out, not_87_out, not_88_out, not_89_out, not_91_out, not_92_out, not_93_out, not_94_out,
       not_95_out, not_96_out, not_97_out, not_98_out, not_99_out, not_100_out, not_101_out, not_102_out,
       not_103_out, not_104_out, not_105_out, not_107_out, not_108_out, not_109_out, not_110_out,
       not_111_out, not_112_out, not_113_out, not_114_out, not_116_out, not_117_out, not_118_out,
       not_119_out, not_120_out, not_121_out, not_122_out, not_123_out, not_124_out, not_125_out,
       not_126_out, not_127_out, not_128_out, nRESc, OE, or_35_out, or_36_out, or_37_out, or_38_out,
       or_41_out, or_42_out, or_43_out, or_44_out, or_45_out, or_50_out, or_51_out, or_54_out, or_55_out,
       or_60_out, or_61_out, or_62_out, or_63_out, or_64_out, or_65_out, or_66_out, or_67_out, or_68_out,
       or_69_out, or_70_out, or_71_out, or_72_out, or_73_out, or_74_out, or_79_out, or_82_out, PHI2c, R, R_W,
       S0_2_q, S0_q, S0_qn, S1_q, S2_qn, TERM, undriven, WE;
  wire [0:0] d_ff_10_q, d_ff_24_q, d_ff_35_q, d_ff_51_q;
  wire [4:0] and_41_out, and_45_out, ICR0_q, nand_89_out, nand_90_out, nand_92_out, not_115_out,
       register_1_q, register_4_q, register_7_q, register_10_q, register_15_q;
  wire [7:0] _1_DO, _1_DZ, _2_DO, _2_DZ, and_3_out, and_4_out, and_5_out, and_7_out,
       controlled_buffer_46_out, hct299_3_i, not_30_out, not_35_out, not_41_out, not_49_out;
  wire [7:5] register_15_q_2;
  wire [7:6] multiplexer_1_out, multiplexer_3_out, or_39_out, or_48_out;
  wire [7:7] d_ff_76_q, not_2_out, not_4_out;

  Clock clock_1 (.out(clock_1_out));
  _6502 u_6502_1 (
    .A_BUS(out_15), .D_OUT(out_16), .R_W(R_W), .PHI2(PHI2c), .PHI0(clock_1_out), .RDY(RDY), .BE(BE),
    .nRS(not_1_out), .nIRQ(_1__IRQ), .nNMI(_2__IRQ), .D_IN(out_16));  // open: AX_OUT, PHI1, SYNC
  not not_1 (not_1_out, R);
  Button button_1 (.out(R));
  RAM #(.addrWidth(16), .databus("bidir"), .trigger("high"), .\type ("nonvolatile")) ram_1 (
    .addr(out_15), .data(out_16));  // open: we, oe, clk
  memDecoder memdecoder_1 (
    .A(out_15), .PHI2(PHI2c), .R_W(R_W), .TOD(_1_TOD), .OE(OE), .WE(WE), .nCIA(_1__CS), .nCIAEXT(_2__CS),
    .TERM(TERM), .nCIARES(nRESc));
  TTY #(.asciiwidth(8), .cols(3), .rows(21)) tty_1 (.data({1'b1, out_16[5:0]}), .clk(TERM), .clr(R));  // open: we
  Pull_Resistor #(.pull(1)) pull_resistor_1 (.node(_1_SP));
  buf buffer_1 (buffer_1_out, PHI2c);
  buf buffer_2 (_1__RES, nRESc);
  not not_2 (not_2_out[7], _1__RES);
  buf buffer_3 (_1_PHI2, buffer_1_out);
  not not_3 (_1__PHI2, buffer_1_out);
  nand nand_1 (_1_ENABLE_NAND, R_W, _1__RES);
  assign _1_DZ = {8{_1__RES}} & out_16;  // AND_Gate and_1, 8 bits wide
  assign _1_DO = out_16 | {8{not_2_out[7]}};  // OR_Gate or_1, 8 bits wide
  buf buffer_4 (buffer_4_out, out_15[0]);
  buf buffer_5 (buffer_5_out, out_15[1]);
  buf buffer_6 (buffer_6_out, out_15[2]);
  buf buffer_7 (buffer_7_out, _1_PHI2);
  buf buffer_8 (buffer_8_out, out_15[0]);
  buf buffer_9 (buffer_9_out, out_15[1]);
  buf buffer_10 (buffer_10_out, out_15[2]);
  buf buffer_11 (buffer_11_out, PHI2c);
  buf buffer_12 (_2__RES, nRESc);
  not not_4 (not_4_out[7], _2__RES);
  not not_5 (not_5_out, buffer_4_out);
  not not_6 (not_6_out, buffer_5_out);
  not not_7 (not_7_out, buffer_6_out);
  not not_8 (not_8_out, out_15[3]);
  not not_9 (not_9_out, _1__CS);
  not not_10 (not_10_out, buffer_8_out);
  not not_11 (not_11_out, buffer_9_out);
  not not_12 (not_12_out, buffer_10_out);
  buf buffer_13 (buffer_13_out, out_15[3]);
  not not_13 (not_13_out, _1__PHI2);
  not not_14 (not_14_out, _1__CS);
  buf buffer_14 (_2_PHI2, buffer_11_out);
  not not_15 (_2__PHI2, buffer_11_out);
  nand nand_2 (_2_ENABLE_NAND, R_W, _2__RES);
  nand nand_3 (nand_3_out, buffer_7_out, not_8_out, not_9_out);
  nand nand_4 (nand_4_out, buffer_13_out, not_13_out, not_14_out);
  assign _2_DZ = {8{_2__RES}} & out_16;  // AND_Gate and_2, 8 bits wide
  assign _2_DO = out_16 | {8{not_4_out[7]}};  // OR_Gate or_2, 8 bits wide
  nand nand_5 (nand_5_out, not_5_out, not_6_out, not_7_out);
  nand nand_6 (nand_6_out, buffer_4_out, not_6_out, not_7_out);
  nand nand_7 (nand_7_out, not_5_out, buffer_5_out, not_7_out);
  nand nand_8 (nand_8_out, buffer_4_out, buffer_5_out, not_7_out);
  nand nand_9 (nand_9_out, not_5_out, not_6_out, buffer_6_out);
  nand nand_10 (nand_10_out, buffer_4_out, not_6_out, buffer_6_out);
  nand nand_11 (nand_11_out, not_5_out, buffer_5_out, buffer_6_out);
  nand nand_12 (nand_12_out, buffer_4_out, buffer_5_out, buffer_6_out);
  nand nand_13 (nand_13_out, not_10_out, not_11_out, not_12_out);
  nand nand_14 (nand_14_out, buffer_8_out, not_11_out, not_12_out);
  nand nand_15 (nand_15_out, not_10_out, buffer_9_out, not_12_out);
  nand nand_16 (nand_16_out, buffer_8_out, buffer_9_out, not_12_out);
  nand nand_17 (nand_17_out, not_10_out, not_11_out, buffer_10_out);
  nand nand_18 (nand_18_out, buffer_8_out, not_11_out, buffer_10_out);
  nand nand_19 (nand_19_out, not_10_out, buffer_9_out, buffer_10_out);
  nand nand_20 (nand_20_out, buffer_8_out, buffer_9_out, buffer_10_out);
  buf buffer_15 (buffer_15_out, out_15[0]);
  buf buffer_16 (buffer_16_out, out_15[1]);
  buf buffer_17 (buffer_17_out, out_15[2]);
  buf buffer_18 (buffer_18_out, _2_PHI2);
  not not_16 (not_16_out, out_15[3]);
  not not_17 (not_17_out, _2__CS);
  buf buffer_19 (buffer_19_out, out_15[0]);
  buf buffer_20 (buffer_20_out, out_15[1]);
  buf buffer_21 (buffer_21_out, out_15[2]);
  buf buffer_22 (buffer_22_out, out_15[3]);
  not not_18 (not_18_out, _2__PHI2);
  not not_19 (not_19_out, _2__CS);
  or or_3 (_1_EN0, nand_5_out, nand_3_out);
  or or_4 (_1_EN1, nand_6_out, nand_3_out);
  or or_5 (_1_EN2, nand_7_out, nand_3_out);
  or or_6 (_1_EN3, nand_8_out, nand_3_out);
  or or_7 (_1_EN4, nand_9_out, nand_3_out);
  or or_8 (_1_EN5, nand_10_out, nand_3_out);
  or or_9 (_1_EN6, nand_11_out, nand_3_out);
  or or_10 (_1_EN7, nand_12_out, nand_3_out);
  or or_11 (_1_EN8, nand_13_out, nand_4_out);
  or or_12 (_1_EN9, nand_14_out, nand_4_out);
  or or_13 (_1_EN10, nand_15_out, nand_4_out);
  or or_14 (_1_EN11, nand_16_out, nand_4_out);
  or or_15 (_1_EN12, nand_17_out, nand_4_out);
  or or_16 (_1_EN13, nand_18_out, nand_4_out);
  or or_17 (EN14, nand_19_out, nand_4_out);
  or or_18 (_1_EN15, nand_20_out, nand_4_out);
  not not_20 (not_20_out, buffer_15_out);
  not not_21 (not_21_out, buffer_16_out);
  not not_22 (not_22_out, buffer_17_out);
  not not_23 (not_23_out, buffer_19_out);
  not not_24 (not_24_out, buffer_20_out);
  not not_25 (not_25_out, buffer_21_out);
  nand nand_21 (nand_21_out, buffer_18_out, not_16_out, not_17_out);
  nand nand_22 (nand_22_out, buffer_22_out, not_18_out, not_19_out);
  nand nand_23 (nand_23_out, not_20_out, not_21_out, not_22_out);
  nand nand_24 (nand_24_out, buffer_15_out, not_21_out, not_22_out);
  nand nand_25 (nand_25_out, not_20_out, buffer_16_out, not_22_out);
  nand nand_26 (nand_26_out, buffer_15_out, buffer_16_out, not_22_out);
  nand nand_27 (nand_27_out, not_20_out, not_21_out, buffer_17_out);
  nand nand_28 (nand_28_out, buffer_15_out, not_21_out, buffer_17_out);
  nand nand_29 (nand_29_out, not_20_out, buffer_16_out, buffer_17_out);
  nand nand_30 (nand_30_out, buffer_15_out, buffer_16_out, buffer_17_out);
  nand nand_31 (nand_31_out, not_23_out, not_24_out, not_25_out);
  nand nand_32 (nand_32_out, buffer_19_out, not_24_out, not_25_out);
  nand nand_33 (nand_33_out, not_23_out, buffer_20_out, not_25_out);
  nand nand_34 (nand_34_out, buffer_19_out, buffer_20_out, not_25_out);
  nand nand_35 (nand_35_out, not_23_out, not_24_out, buffer_21_out);
  nand nand_36 (nand_36_out, buffer_19_out, not_24_out, buffer_21_out);
  nand nand_37 (nand_37_out, not_23_out, buffer_20_out, buffer_21_out);
  nand nand_38 (nand_38_out, buffer_19_out, buffer_20_out, buffer_21_out);
  or or_19 (_2_EN0, nand_23_out, nand_21_out);
  or or_20 (_2_EN1, nand_24_out, nand_21_out);
  or or_21 (_2_EN2, nand_25_out, nand_21_out);
  or or_22 (_2_EN3, nand_26_out, nand_21_out);
  or or_23 (_2_EN4, nand_27_out, nand_21_out);
  or or_24 (_2_EN5, nand_28_out, nand_21_out);
  or or_25 (_2_EN6, nand_29_out, nand_21_out);
  or or_26 (_2_EN7, nand_30_out, nand_21_out);
  or or_27 (_2_EN8, nand_31_out, nand_22_out);
  or or_28 (_2_EN9, nand_32_out, nand_22_out);
  or or_29 (_2_EN10, nand_33_out, nand_22_out);
  or or_30 (_2_EN11, nand_34_out, nand_22_out);
  or or_31 (_2_EN12, nand_35_out, nand_22_out);
  or or_32 (_2_EN13, nand_36_out, nand_22_out);
  or or_33 (_2_EN14, nand_37_out, nand_22_out);
  or or_34 (_2_EN15, nand_38_out, nand_22_out);
  nand nand_39 (nand_39_out, _1__RES, _1_EN0);
  or or_35 (or_35_out, _1_ENABLE_NAND, _1_EN0);
  nand nand_40 (nand_40_out, _1_EN3, _1__RES);
  nand nand_41 (nand_41_out, _1__RES, _1_EN1);
  nand nand_42 (nand_42_out, nand_41_out, _1_ENABLE_NAND);
  D_Flip_Flop d_ff_1 (.clk(_1__PHI2), .D(_1_EN1), .Q(_1__PC));  // open: Qn, preset, reset
  or or_36 (or_36_out, _1_ENABLE_NAND, _1_EN1);
  nand nand_43 (nand_43_out, _1_EN2, _1__RES);
  nand nand_44 (nand_44_out, nand_43_out, _1_ENABLE_NAND);
  or or_37 (or_37_out, _1_ENABLE_NAND, _1_EN2);
  Register PORTA (.D(_1_DZ), .en(not_26_out), .Q(out_5), .clk(_1__PHI2));  // open: clr
  not not_26 (not_26_out, nand_45_out);
  nand nand_45 (nand_45_out, nand_39_out, _1_ENABLE_NAND);
  assign out_7[7] = and_3_out[7] ? 1'b0 : 1'bz;  // Controlled_Buffer controlled_buffer_1
  Pull_Resistor #(.pull(1)) pull_resistor_2 (.node(out_7));
  not not_27 (not_27_out, or_35_out);
  nand nand_46 (nand_46_out, nand_40_out, _1_ENABLE_NAND);
  or or_38 (or_38_out, _1_ENABLE_NAND, _1_EN3);
  Register PORTB (.D(_1_DZ), .en(not_28_out), .Q(out_11), .clk(_1__PHI2));  // open: clr
  not not_28 (not_28_out, nand_42_out);
  Pull_Resistor #(.pull(1)) pull_resistor_3 (.node(out_13));
  Register ddra (.D(_1_DZ), .en(not_29_out), .Q(out_3), .clk(_1__PHI2));  // open: clr
  not not_29 (not_29_out, nand_44_out);
  assign not_30_out = ~out_5;  // NOT_Gate not_30, 8 bits wide
  assign out_7[6] = and_3_out[6] ? 1'b0 : 1'bz;  // Controlled_Buffer controlled_buffer_2
  assign out_7[5] = and_3_out[5] ? 1'b0 : 1'bz;  // Controlled_Buffer controlled_buffer_3
  assign out_7[4] = and_3_out[4] ? 1'b0 : 1'bz;  // Controlled_Buffer controlled_buffer_4
  assign out_16 = not_27_out ? out_7 : 8'bz;  // Controlled_Buffer controlled_buffer_5
  Register ddrb (.D(_1_DZ), .en(not_31_out), .Q(out_9), .clk(_1__PHI2));  // open: clr
  not not_31 (not_31_out, nand_46_out);
  assign out_13[7] = and_4_out[7] ? 1'b0 : 1'bz;  // Controlled_Buffer controlled_buffer_6
  assign out_13[6] = and_4_out[6] ? 1'b0 : 1'bz;  // Controlled_Buffer controlled_buffer_7
  assign out_13[5] = and_4_out[5] ? 1'b0 : 1'bz;  // Controlled_Buffer controlled_buffer_8
  assign out_16 = not_32_out ? out_13 : 8'bz;  // Controlled_Buffer controlled_buffer_9
  not not_32 (not_32_out, or_36_out);
  assign out_16 = not_33_out ? out_3 : 8'bz;  // Controlled_Buffer controlled_buffer_10
  not not_33 (not_33_out, or_37_out);
  assign and_3_out = out_3 & not_30_out;  // AND_Gate and_3, 8 bits wide
  assign out_7[3] = and_3_out[3] ? 1'b0 : 1'bz;  // Controlled_Buffer controlled_buffer_11
  assign out_7[2] = and_3_out[2] ? 1'b0 : 1'bz;  // Controlled_Buffer controlled_buffer_12
  assign out_16 = not_34_out ? out_9 : 8'bz;  // Controlled_Buffer controlled_buffer_13
  not not_34 (not_34_out, or_38_out);
  or or_39 (or_39_out[6], out_9[6], out_17[1]);
  or or_40 (or_39_out[7], out_9[7], out_25[1]);
  Multiplexer #(.enable("false")) multiplexer_1 (
    .in0(out_11[6]), .in1(_1_TAOUT), .out(multiplexer_1_out[6]), .sel(out_17[1]));
  Multiplexer #(.enable("false")) multiplexer_2 (
    .in0(out_11[7]), .in1(_1_TBOUT), .out(multiplexer_1_out[7]), .sel(out_25[1]));
  assign out_13[4] = and_4_out[4] ? 1'b0 : 1'bz;  // Controlled_Buffer controlled_buffer_14
  assign out_13[3] = and_4_out[3] ? 1'b0 : 1'bz;  // Controlled_Buffer controlled_buffer_15
  assign out_13[2] = and_4_out[2] ? 1'b0 : 1'bz;  // Controlled_Buffer controlled_buffer_16
  assign out_7[1] = and_3_out[1] ? 1'b0 : 1'bz;  // Controlled_Buffer controlled_buffer_17
  assign out_7[0] = and_3_out[0] ? 1'b0 : 1'bz;  // Controlled_Buffer controlled_buffer_18
  assign and_4_out = {or_39_out, out_9[5:0]} & not_35_out;  // AND_Gate and_4, 8 bits wide
  assign not_35_out = ~{multiplexer_1_out, out_11[5:0]};  // NOT_Gate not_35, 8 bits wide
  assign out_13[1] = and_4_out[1] ? 1'b0 : 1'bz;  // Controlled_Buffer controlled_buffer_19
  assign out_13[0] = and_4_out[0] ? 1'b0 : 1'bz;  // Controlled_Buffer controlled_buffer_20
  nand nand_47 (nand_47_out, _2__RES, _2_EN0);
  nand nand_48 (nand_48_out, nand_47_out, _2_ENABLE_NAND);
  or or_41 (or_41_out, _2_ENABLE_NAND, _2_EN0);
  nand nand_49 (nand_49_out, _2_EN3, _2__RES);
  or or_42 (or_42_out, _2_ENABLE_NAND, _2_EN3);
  nand nand_50 (nand_50_out, _2__RES, _2_EN1);
  D_Flip_Flop d_ff_2 (.clk(_2__PHI2), .D(_2_EN1), .Q(_1_FLAG));  // open: Qn, preset, reset
  or or_43 (or_43_out, _2_ENABLE_NAND, _2_EN1);
  nand nand_51 (nand_51_out, _2_EN2, _2__RES);
  nand nand_52 (nand_52_out, nand_51_out, _2_ENABLE_NAND);
  or or_44 (or_44_out, _2_ENABLE_NAND, _2_EN2);
  Register PORTA_2 (.D(_2_DZ), .en(not_36_out), .Q(out_6), .clk(_2__PHI2));  // open: clr
  not not_36 (not_36_out, nand_48_out);
  assign out_7[7] = and_5_out[7] ? 1'b0 : 1'bz;  // Controlled_Buffer controlled_buffer_21
  Pull_Resistor #(.pull(1)) pull_resistor_4 (.node(out_7));
  assign out_16 = not_37_out ? out_7 : 8'bz;  // Controlled_Buffer controlled_buffer_22
  not not_37 (not_37_out, or_41_out);
  not not_38 (not_38_out, nand_53_out);
  nand nand_53 (nand_53_out, nand_49_out, _2_ENABLE_NAND);
  not not_39 (not_39_out, nand_54_out);
  nand nand_54 (nand_54_out, nand_50_out, _2_ENABLE_NAND);
  Register ddra_2 (.D(_2_DZ), .en(not_40_out), .Q(out_4), .clk(_2__PHI2));  // open: clr
  not not_40 (not_40_out, nand_52_out);
  assign not_41_out = ~out_6;  // NOT_Gate not_41, 8 bits wide
  assign out_7[6] = and_5_out[6] ? 1'b0 : 1'bz;  // Controlled_Buffer controlled_buffer_23
  assign out_7[5] = and_5_out[5] ? 1'b0 : 1'bz;  // Controlled_Buffer controlled_buffer_24
  assign out_7[4] = and_5_out[4] ? 1'b0 : 1'bz;  // Controlled_Buffer controlled_buffer_25
  assign out_16 = not_42_out ? out_10 : 8'bz;  // Controlled_Buffer controlled_buffer_26
  Register ddrb_2 (.D(_2_DZ), .en(not_38_out), .Q(out_10), .clk(_2__PHI2));  // open: clr
  not not_42 (not_42_out, or_42_out);
  Register PORTB_2 (.D(_2_DZ), .en(not_39_out), .Q(out_12), .clk(_2__PHI2));  // open: clr
  assign out_13[7] = and_7_out[7] ? 1'b0 : 1'bz;  // Controlled_Buffer controlled_buffer_27
  assign out_13[6] = and_7_out[6] ? 1'b0 : 1'bz;  // Controlled_Buffer controlled_buffer_28
  Pull_Resistor #(.pull(1)) pull_resistor_5 (.node(out_13));
  assign out_16 = not_43_out ? out_13 : 8'bz;  // Controlled_Buffer controlled_buffer_29
  not not_43 (not_43_out, or_43_out);
  nand nand_55 (nand_55_out, EN14, _1__RES);
  nand nand_56 (nand_56_out, nand_55_out, _1_ENABLE_NAND);
  or or_45 (or_45_out, _1_ENABLE_NAND, EN14);
  or or_46 (_1_OETALO, _1_EN4, _1_ENABLE_NAND);
  or or_47 (_1_OETAHI, _1_EN5, _1_ENABLE_NAND);
  D_Flip_Flop d_ff_3 (.clk(_1_CNT), .D(1'b1), .Qn(d_ff_3_qn), .reset(not_44_out));  // open: Q, preset
  not not_44 (not_44_out, d_ff_3_qn);
  not not_45 (not_45_out, d_ff_3_qn);
  assign out_16 = not_46_out ? out_4 : 8'bz;  // Controlled_Buffer controlled_buffer_30
  not not_46 (not_46_out, or_44_out);
  assign and_5_out = out_4 & not_41_out;  // AND_Gate and_5, 8 bits wide
  assign out_7[3] = and_5_out[3] ? 1'b0 : 1'bz;  // Controlled_Buffer controlled_buffer_31
  assign out_7[2] = and_5_out[2] ? 1'b0 : 1'bz;  // Controlled_Buffer controlled_buffer_32
  assign out_7[1] = and_5_out[1] ? 1'b0 : 1'bz;  // Controlled_Buffer controlled_buffer_33
  or or_48 (or_48_out[6], out_10[6], out_18[1]);
  or or_49 (or_48_out[7], out_10[7], out_26[1]);
  Multiplexer #(.enable("false")) multiplexer_3 (
    .in0(out_12[6]), .in1(_2_TAOUT), .out(multiplexer_3_out[6]), .sel(out_18[1]));
  Multiplexer #(.enable("false")) multiplexer_4 (
    .in0(out_12[7]), .in1(_2_TBOUT), .out(multiplexer_3_out[7]), .sel(out_26[1]));
  assign out_13[5] = and_7_out[5] ? 1'b0 : 1'bz;  // Controlled_Buffer controlled_buffer_34
  assign out_13[4] = and_7_out[4] ? 1'b0 : 1'bz;  // Controlled_Buffer controlled_buffer_35
  assign out_13[3] = and_7_out[3] ? 1'b0 : 1'bz;  // Controlled_Buffer controlled_buffer_36
  buf buffer_23 (buffer_23_out, _1_DZ[0]);
  buf buffer_24 (buffer_24_out, buffer_23_out);
  buf buffer_25 (buffer_25_out, buffer_24_out);
  buf buffer_26 (buffer_26_out, buffer_25_out);
  buf buffer_27 (buffer_27_out, _1_DZ[4]);
  buf buffer_28 (buffer_28_out, buffer_27_out);
  buf buffer_29 (buffer_29_out, buffer_28_out);
  buf buffer_30 (buffer_30_out, buffer_29_out);
  not not_47 (not_47_out, nand_56_out);
  and and_6 (and_6_out, not_47_out, _1__PHI2);
  not not_48 (not_48_out, _1__PHI2);
  nand nand_57 (nand_57_out, _1__RES, _1_EN4);
  nand nand_58 (_1_WETALO, nand_57_out, _1_ENABLE_NAND);
  nand nand_59 (nand_59_out, _1__RES, _1_EN5);
  nand nand_60 (_1_WETAHI, _1_ENABLE_NAND, nand_59_out);
  D_Flip_Flop d_ff_4 (.clk(_1_PHI2), .D(1'b0), .Q(d_ff_4_q), .preset(not_45_out));  // open: Qn, reset
  assign out_7[0] = and_5_out[0] ? 1'b0 : 1'bz;  // Controlled_Buffer controlled_buffer_37
  assign and_7_out = {or_48_out, out_10[5:0]} & not_49_out;  // AND_Gate and_7, 8 bits wide
  assign not_49_out = ~{multiplexer_3_out, out_12[5:0]};  // NOT_Gate not_49, 8 bits wide
  assign out_13[2] = and_7_out[2] ? 1'b0 : 1'bz;  // Controlled_Buffer controlled_buffer_38
  assign out_13[1] = and_7_out[1] ? 1'b0 : 1'bz;  // Controlled_Buffer controlled_buffer_39
  assign out_13[0] = and_7_out[0] ? 1'b0 : 1'bz;  // Controlled_Buffer controlled_buffer_40
  D_Flip_Flop d_ff_5 (.clk(and_6_out), .D(buffer_30_out), .Q(d_ff_5_q), .reset(not_48_out));  // open: Qn, preset
  D_Flip_Flop d_ff_6 (.clk(not_48_out), .D(out_17[3]), .Q(d_ff_6_q));  // open: Qn, preset, reset
  D_Flip_Flop d_ff_7 (.clk(_1_PHI2), .D(1'b0), .Q(_1_TAPULSE), .Qn(d_ff_7_qn), .preset(_1_TAUNDERFLOW));  // open: reset
  D_Flip_Flop d_ff_8 (.clk(out_17[0]), .D(1'b1), .Q(d_ff_8_q), .reset(_1_PHI2));  // open: Qn, preset
  D_Flip_Flop d_ff_9 (.clk(_1_PHI2), .D(d_ff_4_q), .Qn(d_ff_9_qn));  // open: Q, preset, reset
  not not_50 (not_50_out, nand_56_out);
  D_Flip_Flop d_ff_10 (.clk(and_6_out), .D(buffer_26_out), .Q(d_ff_10_q[0]), .reset(and_8_out));  // open: Qn, preset
  D_Flip_Flop d_ff_11 (
    .clk(_1_TAPULSE), .D(d_ff_11_qn), .Qn(d_ff_11_qn), .preset(d_ff_8_q), .reset(not_51_out));  // open: Q
  not not_51 (not_51_out, _1__RES);
  nand nand_61 (nand_61_out, out_17[5], d_ff_9_qn);
  D_Flip_Flop d_ff_12 (.clk(_1_CNT), .D(1'b1), .Qn(d_ff_12_qn), .reset(not_52_out));  // open: Q, preset
  not not_52 (not_52_out, d_ff_12_qn);
  Register register_1 (
    .D({_1_DZ[7:5], 1'b0, _1_DZ[3:1], 1'b0}), .en(not_50_out),
    .Q({out_17[7:5], register_1_q[4], out_17[3:1], register_1_q[0]}), .clk(_1__PHI2));  // open: clr
  D_Flip_Flop d_ff_13 (.clk(_1__PHI2), .D(d_ff_10_q[0]), .Q(out_17[0]));  // open: Qn, preset, reset
  D_Flip_Flop d_ff_14 (.clk(_1_PHI2), .D(d_ff_5_q), .Q(out_17[4]));  // open: Qn, preset, reset
  or or_50 (or_50_out, d_ff_6_q, out_17[3]);
  and and_8 (and_8_out, or_50_out, _1_TAUNDERFLOW);
  not not_53 (not_53_out, _1_TAFL);
  Multiplexer #(.enable("false")) multiplexer_5 (
    .in0(d_ff_7_qn), .in1(d_ff_11_qn), .out(multiplexer_5_out), .sel(out_17[2]));
  and and_9 (and_9_out, out_17[0], nand_61_out);
  not not_54 (not_54_out, _1_TAFL);
  timer16 timer16_1 (
    .TIMER(out_23), .UNDERFLOW(_1_TAOFDETECT), .Q(out_16), .PULSE(_1_TADECREMENT),
    .FORCELOAD(_1_TALOADPULSE), .nRES(_1__RES), .LO(out_19), .HI(out_21), .nOELO(_1_OETALO), .nOEHI(_1_OETAHI));
  buf buffer_31 (buffer_31_out, _2_DZ[0]);
  buf buffer_32 (buffer_32_out, _2_DZ[4]);
  nand nand_62 (nand_62_out, _2_EN14, _2__RES);
  nand nand_63 (nand_63_out, nand_62_out, _2_ENABLE_NAND);
  or or_51 (or_51_out, _2_ENABLE_NAND, _2_EN14);
  nand nand_64 (nand_64_out, _2__RES, _2_EN4);
  nand nand_65 (nand_65_out, _2__RES, _2_EN5);
  or or_52 (_2_OETALO, _2_EN4, _2_ENABLE_NAND);
  or or_53 (_2_OETAHI, _2_EN5, _2_ENABLE_NAND);
  D_Flip_Flop d_ff_15 (.clk(_2_PHI2), .D(1'b0), .Q(d_ff_15_q), .preset(not_55_out));  // open: Qn, reset
  not not_55 (not_55_out, d_ff_12_qn);
  Register register_2 (.D(_1_DO), .en(not_56_out), .Q(out_19), .clk(_1__PHI2));  // open: clr
  not not_56 (not_56_out, _1_WETALO);
  Register register_3 (.D(_1_DO), .en(not_57_out), .Q(out_21), .clk(_1__PHI2));  // open: clr
  not not_57 (not_57_out, _1_WETAHI);
  D_Flip_Flop d_ff_16 (.clk(_1__PHI2), .D(1'b1), .Q(_1_TALOADPULSE), .reset(not_53_out));  // open: Qn, preset
  not not_58 (_1_TAOUT, multiplexer_5_out);
  D_Flip_Flop d_ff_17 (.clk(_1_PHI2), .D(and_9_out), .Q(d_ff_17_q), .reset(not_54_out));  // open: Qn, preset
  and and_10 (_1_TAUNDERFLOW, d_ff_17_q, _1_TAOFDETECT);
  nor nor_1 (nor_1_out, out_17[0], _1_WETAHI, 1'b0);
  buf buffer_33 (buffer_33_out, buffer_31_out);
  buf buffer_34 (buffer_34_out, buffer_33_out);
  buf buffer_35 (buffer_35_out, buffer_34_out);
  buf buffer_36 (buffer_36_out, buffer_32_out);
  buf buffer_37 (buffer_37_out, buffer_36_out);
  buf buffer_38 (buffer_38_out, buffer_37_out);
  not not_59 (not_59_out, nand_63_out);
  and and_11 (and_11_out, not_59_out, _2__PHI2);
  not not_60 (not_60_out, _2__PHI2);
  nand nand_66 (_2_WETALO, nand_64_out, _2_ENABLE_NAND);
  nand nand_67 (_2_WETAHI, _2_ENABLE_NAND, nand_65_out);
  assign out_16 = not_61_out ? {out_17[7:5], register_1_q[4], out_17[3:1], d_ff_10_q[0]} : 8'bz;  // Controlled_Buffer controlled_buffer_41
  not not_61 (not_61_out, or_45_out);
  D_Flip_Flop d_ff_18 (.clk(_1_PHI2), .D(d_ff_17_q), .Q(d_ff_18_q), .reset(buffer_39_out));  // open: Qn, preset
  not not_62 (not_62_out, d_ff_17_q);
  buf buffer_39 (buffer_39_out, not_62_out);
  nor nor_2 (_1_TAFL, _1_TAUNDERFLOW, out_17[4], nor_1_out);
  D_Flip_Flop d_ff_19 (.clk(and_11_out), .D(buffer_38_out), .Q(d_ff_19_q), .reset(not_60_out));  // open: Qn, preset
  D_Flip_Flop d_ff_20 (.clk(not_60_out), .D(out_18[3]), .Q(d_ff_20_q));  // open: Qn, preset, reset
  D_Flip_Flop d_ff_21 (
    .clk(_2_PHI2), .D(1'b0), .Q(_2_TAPULSE), .Qn(d_ff_21_qn), .preset(_2_TAUNDERFLOW));  // open: reset
  D_Flip_Flop d_ff_22 (.clk(out_18[0]), .D(1'b1), .Q(d_ff_22_q), .reset(_2_PHI2));  // open: Qn, preset
  D_Flip_Flop d_ff_23 (.clk(_2_PHI2), .D(d_ff_15_q), .Qn(d_ff_23_qn));  // open: Q, preset, reset
  and and_12 (_1_TADECREMENT, _1_PHI2, d_ff_18_q);
  Register register_4 (
    .D({_2_DZ[7:5], 1'b0, _2_DZ[3:1], 1'b0}), .en(not_63_out),
    .Q({out_18[7:5], register_4_q[4], out_18[3:1], register_4_q[0]}), .clk(_2__PHI2));  // open: clr
  not not_63 (not_63_out, nand_63_out);
  D_Flip_Flop d_ff_24 (.clk(and_11_out), .D(buffer_35_out), .Q(d_ff_24_q[0]), .reset(and_13_out));  // open: Qn, preset
  or or_54 (or_54_out, d_ff_20_q, out_18[3]);
  D_Flip_Flop d_ff_25 (
    .clk(_2_TAPULSE), .D(d_ff_25_qn), .Qn(d_ff_25_qn), .preset(d_ff_22_q), .reset(not_64_out));  // open: Q
  not not_64 (not_64_out, _2__RES);
  nand nand_68 (nand_68_out, out_18[5], d_ff_23_qn);
  timer16 timer16_2 (
    .TIMER(out_24), .UNDERFLOW(_2_TAOFDETECT), .Q(out_16), .PULSE(_2_TADECREMENT),
    .FORCELOAD(_2_TALOADPULSE), .nRES(_2__RES), .LO(out_20), .HI(out_22), .nOELO(_2_OETALO), .nOEHI(_2_OETAHI));
  D_Flip_Flop d_ff_26 (.clk(_2__PHI2), .D(d_ff_24_q[0]), .Q(out_18[0]));  // open: Qn, preset, reset
  D_Flip_Flop d_ff_27 (.clk(_2_PHI2), .D(d_ff_19_q), .Q(out_18[4]));  // open: Qn, preset, reset
  and and_13 (and_13_out, or_54_out, _2_TAUNDERFLOW);
  not not_65 (not_65_out, _2_WETALO);
  not not_66 (not_66_out, _2_WETAHI);
  not not_67 (_2_TAOUT, multiplexer_6_out);
  Multiplexer #(.enable("false")) multiplexer_6 (
    .in0(d_ff_21_qn), .in1(d_ff_25_qn), .out(multiplexer_6_out), .sel(out_18[2]));
  D_Flip_Flop d_ff_28 (.clk(_2_PHI2), .D(and_14_out), .Q(d_ff_28_q), .reset(_2_TAUNDERFLOW));  // open: Qn, preset
  and and_14 (and_14_out, out_18[0], nand_68_out);
  and and_15 (_2_TAUNDERFLOW, d_ff_28_q, _2_TAOFDETECT);
  nor nor_3 (nor_3_out, out_18[0], _2_WETAHI, 1'b0);
  D_Flip_Flop d_ff_29 (.clk(_1_PHI2), .D(_1_TAPULSE), .Q(d_ff_29_q));  // open: Qn, preset, reset
  not not_68 (not_68_out, or_51_out);
  Register register_5 (.D(_2_DO), .en(not_65_out), .Q(out_20), .clk(_2__PHI2));  // open: clr
  Register register_6 (.D(_2_DO), .en(not_66_out), .Q(out_22), .clk(_2__PHI2));  // open: clr
  D_Flip_Flop d_ff_30 (.clk(_2__PHI2), .D(1'b1), .Q(d_ff_30_q), .reset(not_69_out));  // open: Qn, preset
  not not_69 (not_69_out, _2_TAFL);
  not not_70 (not_70_out, d_ff_28_q);
  nor nor_4 (_2_TAFL, _2_TAUNDERFLOW, out_18[4], nor_3_out);
  D_Flip_Flop d_ff_31 (.clk(_1_CNT), .D(1'b1), .Qn(d_ff_31_qn), .reset(not_71_out));  // open: Q, preset
  not not_71 (not_71_out, d_ff_31_qn);
  assign out_16 = not_68_out ? {out_18[7:5], register_4_q[4], out_18[3:1], d_ff_24_q[0]} : 8'bz;  // Controlled_Buffer controlled_buffer_42
  D_Flip_Flop d_ff_32 (.clk(_2__PHI2), .D(d_ff_30_q), .Q(_2_TALOADPULSE), .reset(not_69_out));  // open: Qn, preset
  and and_16 (_2_TADECREMENT, _2_PHI2, d_ff_33_q);
  D_Flip_Flop d_ff_33 (.clk(_2_PHI2), .D(d_ff_28_q), .Q(d_ff_33_q), .reset(buffer_40_out));  // open: Qn, preset
  buf buffer_40 (buffer_40_out, not_70_out);
  Pull_Resistor #(.pull(1)) pull_resistor_6 (.node(_1_CNT));
  Button button_2 (.out(button_2_out));
  assign _1_CNT = button_2_out ? 1'b0 : 1'bz;  // Controlled_Buffer controlled_buffer_43
  nand nand_69 (nand_69_out, _1_EN15, _1__RES);
  nand nand_70 (nand_70_out, nand_69_out, _1_ENABLE_NAND);
  or or_55 (or_55_out, _1_ENABLE_NAND, _1_EN15);
  nand nand_71 (nand_71_out, _1__RES, _1_EN6);
  nand nand_72 (nand_72_out, _1__RES, _1_EN7);
  or or_56 (_1_OETBLO, _1_EN6, _1_ENABLE_NAND);
  or or_57 (_1_OETBHI, _1_EN7, _1_ENABLE_NAND);
  D_Flip_Flop d_ff_34 (.clk(_1_PHI2), .D(1'b0), .Q(d_ff_34_q), .preset(not_72_out));  // open: Qn, reset
  not not_72 (not_72_out, d_ff_31_qn);
  buf buffer_41 (buffer_41_out, _1_DZ[0]);
  buf buffer_42 (buffer_42_out, buffer_41_out);
  buf buffer_43 (buffer_43_out, buffer_42_out);
  buf buffer_44 (buffer_44_out, buffer_43_out);
  buf buffer_45 (buffer_45_out, _1_DZ[4]);
  buf buffer_46 (buffer_46_out, buffer_45_out);
  buf buffer_47 (buffer_47_out, buffer_46_out);
  buf buffer_48 (buffer_48_out, buffer_47_out);
  not not_73 (not_73_out, nand_70_out);
  and and_17 (and_17_out, not_73_out, _1__PHI2);
  not not_74 (not_74_out, _1__PHI2);
  nand nand_73 (_1_WETBLO, nand_71_out, _1_ENABLE_NAND);
  nand nand_74 (_1_WETBHI, _1_ENABLE_NAND, nand_72_out);
  D_Flip_Flop d_ff_35 (.clk(and_17_out), .D(buffer_44_out), .Q(d_ff_35_q[0]), .reset(and_19_out));  // open: Qn, preset
  D_Flip_Flop d_ff_36 (.clk(and_17_out), .D(buffer_48_out), .Q(d_ff_36_q), .reset(not_74_out));  // open: Qn, preset
  D_Flip_Flop d_ff_37 (.clk(not_74_out), .D(out_25[3]), .Q(d_ff_37_q));  // open: Qn, preset, reset
  D_Flip_Flop d_ff_38 (
    .clk(_1_PHI2), .D(1'b0), .Q(_1_TBPULSE), .Qn(d_ff_38_qn), .preset(_1_TBUNDERFLOW));  // open: reset
  D_Flip_Flop d_ff_39 (.clk(out_25[0]), .D(1'b1), .Q(d_ff_39_q), .reset(_1_PHI2));  // open: Qn, preset
  D_Flip_Flop d_ff_40 (.clk(_1_PHI2), .D(d_ff_34_q), .Q(d_ff_40_q));  // open: Qn, preset, reset
  and and_18 (and_18_out, d_ff_29_q, _1_CNT);
  D_Flip_Flop d_ff_41 (.clk(_2_PHI2), .D(_2_TAPULSE), .Q(d_ff_41_q));  // open: Qn, preset, reset
  not not_75 (not_75_out, nand_70_out);
  D_Flip_Flop d_ff_42 (
    .clk(_1_TBPULSE), .D(d_ff_42_qn), .Qn(d_ff_42_qn), .preset(d_ff_39_q), .reset(not_76_out));  // open: Q
  not not_76 (not_76_out, _1__RES);
  Multiplexer #(.enable("false"), .select(2)) multiplexer_7 (
    .in0(1'b1), .in1(d_ff_40_q), .in2(d_ff_29_q), .in3(and_18_out), .out(multiplexer_7_out), .sel(out_25[6:5]));
  nand nand_75 (nand_75_out, _2__RES, _2_EN6);
  nand nand_76 (nand_76_out, _2__RES, _2_EN7);
  or or_58 (_2_OETBLO, _2_EN6, _2_ENABLE_NAND);
  or or_59 (_2_OETBHI, _2_EN7, _2_ENABLE_NAND);
  D_Flip_Flop d_ff_43 (.clk(_1_CNT), .D(1'b1), .Qn(d_ff_43_qn), .reset(not_77_out));  // open: Q, preset
  not not_77 (not_77_out, d_ff_43_qn);
  Register register_7 (
    .D({_1_DZ[7:5], 1'b0, _1_DZ[3:1], 1'b0}), .en(not_75_out),
    .Q({out_25[7:5], register_7_q[4], out_25[3:1], register_7_q[0]}), .clk(_1__PHI2));  // open: clr
  D_Flip_Flop d_ff_44 (.clk(_1__PHI2), .D(d_ff_35_q[0]), .Q(out_25[0]));  // open: Qn, preset, reset
  D_Flip_Flop d_ff_45 (.clk(_1_PHI2), .D(d_ff_36_q), .Q(out_25[4]));  // open: Qn, preset, reset
  or or_60 (or_60_out, d_ff_37_q, out_25[3]);
  and and_19 (and_19_out, or_60_out, _1_TBUNDERFLOW);
  not not_78 (_1_TBOUT, multiplexer_8_out);
  Multiplexer #(.enable("false")) multiplexer_8 (
    .in0(d_ff_38_qn), .in1(d_ff_42_qn), .out(multiplexer_8_out), .sel(out_25[2]));
  D_Flip_Flop d_ff_46 (.clk(_1_PHI2), .D(and_20_out), .Q(PRECOUNT), .reset(not_79_out));  // open: Qn, preset
  and and_20 (and_20_out, multiplexer_7_out, out_25[0]);
  not not_79 (not_79_out, _1_TBFL);
  timer16 timer16_3 (
    .TIMER(out_32), .UNDERFLOW(TBis0), .Q(out_16), .PULSE(_1_TBDECREMENT), .FORCELOAD(_1_TBLOADPULSE),
    .nRES(_1__RES), .LO(out_27), .HI(out_30), .nOELO(_1_OETBLO), .nOEHI(_1_OETBHI));
  buf buffer_49 (buffer_49_out, _2_DZ[0]);
  buf buffer_50 (buffer_50_out, _2_DZ[4]);
  nand nand_77 (nand_77_out, _2_EN15, _2__RES);
  nand nand_78 (nand_78_out, nand_77_out, _2_ENABLE_NAND);
  or or_61 (or_61_out, _2_ENABLE_NAND, _2_EN15);
  nand nand_79 (_2_WETBLO, nand_75_out, _2_ENABLE_NAND);
  nand nand_80 (_2_WETBHI, _2_ENABLE_NAND, nand_76_out);
  D_Flip_Flop d_ff_47 (.clk(_2_PHI2), .D(1'b0), .Q(d_ff_47_q), .preset(not_80_out));  // open: Qn, reset
  not not_80 (not_80_out, d_ff_43_qn);
  Register register_8 (.D(_1_DO), .en(not_81_out), .Q(out_27), .clk(_1__PHI2));  // open: clr
  not not_81 (not_81_out, _1_WETBLO);
  Register register_9 (.D(_1_DO), .en(not_82_out), .Q(out_30), .clk(_1__PHI2));  // open: clr
  not not_82 (not_82_out, _1_WETBHI);
  D_Flip_Flop d_ff_48 (.clk(_1__PHI2), .D(1'b1), .Q(_1_TBLOADPULSE), .reset(not_83_out));  // open: Qn, preset
  not not_83 (not_83_out, _1_TBFL);
  and and_21 (_1_TBUNDERFLOW, PRECOUNT, TBis0);
  nor nor_5 (nor_5_out, out_25[0], _1_WETBHI, 1'b0);
  buf buffer_51 (buffer_51_out, buffer_49_out);
  buf buffer_52 (buffer_52_out, buffer_51_out);
  buf buffer_53 (buffer_53_out, buffer_52_out);
  buf buffer_54 (buffer_54_out, buffer_50_out);
  buf buffer_55 (buffer_55_out, buffer_54_out);
  buf buffer_56 (buffer_56_out, buffer_55_out);
  not not_84 (not_84_out, nand_78_out);
  and and_22 (and_22_out, not_84_out, _2__PHI2);
  not not_85 (not_85_out, _2__PHI2);
  D_Flip_Flop d_ff_49 (.clk(_2_PHI2), .D(d_ff_47_q), .Q(d_ff_49_q));  // open: Qn, preset, reset
  and and_23 (and_23_out, d_ff_41_q, _1_CNT);
  assign out_16 = not_86_out ? {out_25[7:5], register_7_q[4], out_25[3:1], d_ff_35_q[0]} : 8'bz;  // Controlled_Buffer controlled_buffer_44
  not not_86 (not_86_out, or_55_out);
  D_Flip_Flop d_ff_50 (.clk(_1_PHI2), .D(PRECOUNT), .Q(d_ff_50_q), .reset(buffer_57_out));  // open: Qn, preset
  not not_87 (not_87_out, PRECOUNT);
  buf buffer_57 (buffer_57_out, not_87_out);
  nor nor_6 (_1_TBFL, _1_TBUNDERFLOW, undriven, nor_5_out);
  D_Flip_Flop d_ff_51 (.clk(and_22_out), .D(buffer_53_out), .Q(d_ff_51_q[0]), .reset(and_26_out));  // open: Qn, preset
  D_Flip_Flop d_ff_52 (.clk(and_22_out), .D(buffer_56_out), .Q(d_ff_52_q), .reset(not_85_out));  // open: Qn, preset
  D_Flip_Flop d_ff_53 (.clk(not_85_out), .D(out_26[3]), .Q(d_ff_53_q));  // open: Qn, preset, reset
  D_Flip_Flop d_ff_54 (
    .clk(_2_PHI2), .D(1'b0), .Q(_2_TBPULSE), .Qn(d_ff_54_qn), .preset(_2_TBUNDERFLOW));  // open: reset
  D_Flip_Flop d_ff_55 (.clk(out_26[0]), .D(1'b1), .Q(d_ff_55_q), .reset(_2_PHI2));  // open: Qn, preset
  Multiplexer #(.enable("false"), .select(2)) multiplexer_9 (
    .in0(1'b1), .in1(d_ff_49_q), .in2(d_ff_41_q), .in3(and_23_out), .out(multiplexer_9_out), .sel(out_26[6:5]));
  and and_24 (_1_TBDECREMENT, _1_PHI2, d_ff_50_q);
  Register register_10 (
    .D({_2_DZ[7:5], 1'b0, _2_DZ[3:1], 1'b0}), .en(not_88_out),
    .Q({out_26[7:5], register_10_q[4], out_26[3:1], register_10_q[0]}), .clk(_2__PHI2));  // open: clr
  not not_88 (not_88_out, nand_78_out);
  or or_62 (or_62_out, d_ff_53_q, out_26[3]);
  D_Flip_Flop d_ff_56 (
    .clk(_2_TBPULSE), .D(d_ff_56_qn), .Qn(d_ff_56_qn), .preset(d_ff_55_q), .reset(not_89_out));  // open: Q
  not not_89 (not_89_out, _2__RES);
  and and_25 (and_25_out, multiplexer_9_out, out_26[0]);
  timer16 timer16_4 (
    .TIMER(out_33), .UNDERFLOW(_2_TBOFDETECT), .Q(out_16), .PULSE(_2_TBDECREMENT),
    .FORCELOAD(_2_TBLOADPULSE), .nRES(_2__RES), .LO(out_28), .HI(out_31), .nOELO(_2_OETBLO), .nOEHI(_2_OETBHI));
  D_Flip_Flop d_ff_57 (.clk(_2__PHI2), .D(d_ff_51_q[0]), .Q(out_26[0]));  // open: Qn, preset, reset
  D_Flip_Flop d_ff_58 (.clk(_2_PHI2), .D(d_ff_52_q), .Q(out_26[4]));  // open: Qn, preset, reset
  and and_26 (and_26_out, or_62_out, _2_TBUNDERFLOW);
  not not_90 (_2_TBOUT, multiplexer_10_out);
  Multiplexer #(.enable("false")) multiplexer_10 (
    .in0(d_ff_54_qn), .in1(d_ff_56_qn), .out(multiplexer_10_out), .sel(out_26[2]));
  D_Flip_Flop d_ff_59 (.clk(_2_PHI2), .D(and_25_out), .Q(d_ff_59_q), .reset(not_91_out));  // open: Qn, preset
  not not_91 (not_91_out, _2_TBFL);
  and and_27 (_2_TBUNDERFLOW, d_ff_59_q, _2_TBOFDETECT);
  nor nor_7 (nor_7_out, out_26[0], _2_WETBHI, 1'b0);
  not not_92 (not_92_out, d_ff_61_qn);
  not not_93 (not_93_out, or_61_out);
  Register register_11 (.D(_2_DO), .en(not_94_out), .Q(out_28), .clk(_2__PHI2));  // open: clr
  not not_94 (not_94_out, _2_WETBLO);
  Register register_12 (.D(_2_DO), .en(not_95_out), .Q(out_31), .clk(_2__PHI2));  // open: clr
  not not_95 (not_95_out, _2_WETBHI);
  D_Flip_Flop d_ff_60 (.clk(_2__PHI2), .D(1'b1), .Q(_2_TBLOADPULSE), .reset(not_96_out));  // open: Qn, preset
  not not_96 (not_96_out, _2_TBFL);
  not not_97 (not_97_out, d_ff_59_q);
  nor nor_8 (_2_TBFL, _2_TBUNDERFLOW, out_26[4], nor_7_out);
  nand nand_81 (nand_81_out, d_ff_66_qn, _1__RES);
  D_Flip_Flop d_ff_61 (.clk(_1_CNT), .D(1'b1), .Qn(d_ff_61_qn), .reset(not_92_out));  // open: Q, preset
  not not_98 (not_98_out, d_ff_61_qn);
  assign out_16 = not_93_out ? {out_26[7:5], register_10_q[4], out_26[3:1], d_ff_51_q[0]} : 8'bz;  // Controlled_Buffer controlled_buffer_45
  and and_28 (_2_TBDECREMENT, _2_PHI2, d_ff_62_q);
  D_Flip_Flop d_ff_62 (.clk(_2_PHI2), .D(d_ff_59_q), .Q(d_ff_62_q), .reset(buffer_58_out));  // open: Qn, preset
  buf buffer_58 (buffer_58_out, not_97_out);
  nand nand_82 (nand_82_out, _1__RES, _1_EN12);
  or or_63 (or_63_out, _1_ENABLE_NAND, _1_EN12);
  or or_64 (or_64_out, nand_81_out, out_17[6]);
  D_Flip_Flop d_ff_63 (.clk(_1__PHI2), .D(d_ff_64_q), .Q(d_ff_63_q));  // open: Qn, preset, reset
  D_Flip_Flop d_ff_64 (.clk(_1__PHI2), .D(1'b0), .Q(d_ff_64_q), .preset(not_98_out));  // open: Qn, reset
  assign controlled_buffer_46_out = not_99_out ? _1_DZ : 8'bz;  // Controlled_Buffer controlled_buffer_46
  not not_99 (not_99_out, or_65_out);
  or or_65 (or_65_out, nand_83_out, d_ff_66_q);
  nand nand_83 (nand_83_out, nand_82_out, _1_ENABLE_NAND);
  HCT299 hct299_1 (
    .I(controlled_buffer_46_out), .DSL(_1__RES), .nMR(_1__RES), .DSR(_1_SP), .S0(1'b1), .S1(1'b0),
    .CP(d_ff_63_q), .nOE1(d_ff_66_qn), .nOE2(d_ff_66_qn));  // open: Q7, Q0, O
  HCT193 hct193_1 (
    .Q3(hct193_1_q3), .in_8(1'b0), .D0(1'b0), .D1(1'b0), .CPU(d_ff_63_q), .CPD(1'b1), .nPL(1'b1),
    .MR(or_64_out), .D2(1'b0));  // open: nTCU, nTCD, Q0, Q1, Q2
  Button button_3 (.out(button_3_out));
  assign _1_CNT = button_3_out ? 1'b0 : 1'bz;  // Controlled_Buffer controlled_buffer_47
  D_Flip_Flop d_ff_65 (.clk(hct193_1_q3), .D(1'b1), .Q(d_ff_65_q), .reset(d_ff_65_q));  // open: Qn, preset
  Pull_Resistor #(.pull(1)) pull_resistor_7 (.node(_1_CNT));
  tod tod_1 (
    .TODBUS(out_37), .TODIRQ(_1_TODIRQ), .Q(out_16), .ALARMBUS(out_39), .TODIN(out_17[7]), .D(_1_DZ),
    .EN8(_1_EN8), .EN9(_1_EN9), .EN10(_1_EN10), .EN11(_1_EN11), .ALARM(out_25[7]), .nRES(_1__RES),
    .ENAND(_1_ENABLE_NAND), .TOD(_1_TOD), .nPHI2(_1__PHI2));
  or or_66 (or_66_out, d_ff_66_q, ~nand_83_out);  // OR_Gate
  D_Flip_Flop d_ff_66 (.clk(_1__PHI2), .D(1'b0), .Q(d_ff_66_q), .Qn(d_ff_66_qn), .preset(d_ff_65_q));  // open: reset
  Register register_13 (.D(controlled_buffer_46_out), .en(or_66_out), .Q(out_35), .clk(_1__PHI2));  // open: clr
  D_Flip_Flop d_ff_67 (.clk(_1_CNT), .D(1'b1), .Q(d_ff_67_q), .reset(d_ff_67_q));  // open: Qn, preset
  buf buffer_59 (buffer_59_out, _1_SP);
  or or_67 (or_67_out, ~_2__RES, d_ff_72_q);  // OR_Gate
  or or_68 (or_68_out, or_67_out, out_18[6]);
  and and_29 (and_29_out, d_ff_69_q, ~_1_SDRLOAD);  // AND_Gate
  nand nand_84 (nand_84_out, out_17[6], _1__RES);
  D_Flip_Flop d_ff_68 (.clk(_2__PHI2), .D(1'b0), .Q(d_ff_68_q), .preset(d_ff_67_q));  // open: Qn, reset
  HCT299 hct299_2 (
    .Q7(hct299_2_q7), .Q0(hct299_2_q0), .DSL(1'b1), .nMR(1'b1), .DSR(hct299_2_q0), .S0(1'b1),
    .S1(_1_SDRLOAD), .CP(and_29_out), .nOE1(1'b1), .nOE2(1'b1), .O(out_35));  // open: I
  D_Flip_Flop d_ff_69 (
    .clk(_1_TAPULSE), .D(d_ff_69_qn), .Q(d_ff_69_q), .Qn(d_ff_69_qn), .preset(_1_SDRCOUNT),
    .reset(nand_84_out));
  nand nand_85 (nand_85_out, _2__RES, _2_EN12);
  nand nand_86 (nand_86_out, nand_85_out, _2_ENABLE_NAND);
  or or_69 (or_69_out, _2_ENABLE_NAND, _2_EN12);
  D_Flip_Flop d_ff_70 (.clk(_2__PHI2), .D(d_ff_68_q), .Q(d_ff_70_q));  // open: Qn, preset, reset
  HCT299 hct299_3 (
    .I(hct299_3_i), .DSL(1'b1), .nMR(1'b1), .DSR(buffer_59_out), .S0(1'b1), .S1(1'b0), .CP(d_ff_70_q),
    .nOE1(d_ff_72_qn), .nOE2(d_ff_72_qn));  // open: Q7, Q0, O
  HCT193 hct193_2 (
    .Q3(hct193_2_q3), .in_8(1'b0), .D0(1'b0), .D1(1'b0), .CPU(d_ff_70_q), .CPD(1'b1), .nPL(1'b1),
    .MR(or_68_out), .D2(1'b0));  // open: nTCU, nTCD, Q0, Q1, Q2
  D_Flip_Flop d_ff_71 (.clk(hct193_2_q3), .D(1'b1), .Q(d_ff_71_q), .reset(d_ff_71_q));  // open: Qn, preset
  tod tod_2 (
    .TODBUS(out_38), .TODIRQ(_2_TODIRQ), .Q(out_16), .ALARMBUS(out_40), .TODIN(out_18[7]), .D(_2_DZ),
    .EN8(_2_EN8), .EN9(_2_EN9), .EN10(_2_EN10), .EN11(_2_EN11), .ALARM(out_26[7]), .nRES(_2__RES),
    .ENAND(_2_ENABLE_NAND), .TOD(_1_TOD), .nPHI2(_2__PHI2));
  assign out_16 = not_100_out ? out_35 : 8'bz;  // Controlled_Buffer controlled_buffer_48
  not not_100 (not_100_out, or_63_out);
  not not_101 (not_101_out, hct299_2_q7);
  and and_30 (and_30_out, not_101_out, out_17[6]);
  assign hct299_3_i = not_102_out ? _2_DZ : 8'bz;  // Controlled_Buffer controlled_buffer_49
  not not_102 (not_102_out, or_70_out);
  or or_70 (or_70_out, nand_86_out, d_ff_72_q);
  D_Flip_Flop d_ff_72 (.clk(_2__PHI2), .D(1'b0), .Q(d_ff_72_q), .Qn(d_ff_72_qn), .preset(d_ff_71_q));  // open: reset
  assign _1_SP = and_30_out ? 1'b0 : 1'bz;  // Controlled_Buffer controlled_buffer_50
  or or_71 (or_71_out, d_ff_69_qn, _1_SDRCOUNT);
  not not_103 (not_103_out, or_71_out);
  assign _1_CNT = not_103_out ? 1'b0 : 1'bz;  // Controlled_Buffer controlled_buffer_51
  and and_31 (and_31_out, nand_86_out, d_ff_72_qn);
  or or_72 (or_72_out, d_ff_73_qn, _2__SDRCOUNT);
  HCT193 hct193_3 (
    .Q3(hct193_3_q3), .in_8(1'b0), .D0(1'b0), .D1(1'b0), .CPU(or_71_out), .CPD(1'b1), .nPL(1'b1),
    .MR(_1_SDRLOAD), .D2(1'b0));  // open: nTCU, nTCD, Q0, Q1, Q2
  icr icr_1 (
    .nIRQ(icr_1_nirq), .Q(out_16), .D(_1_DZ), .EN(_1_EN13), .nRES(_1__RES), .ENAND(_1_ENABLE_NAND),
    .FLAG(_1_FLAG), .TAPULSE(_1_TAPULSE), .TBPULSE(_1_TBPULSE), .TODIRQ(_1_TODIRQ), .SPIRQ(_1_SDRIRQ),
    .nPHI2(_1__PHI2));
  not not_104 (not_104_out, icr_1_nirq);
  assign _1__IRQ = not_104_out ? 1'b0 : 1'bz;  // Controlled_Buffer controlled_buffer_52
  Pull_Resistor #(.pull(1)) pull_resistor_8 (.node(_1__IRQ));
  not not_105 (not_105_out, and_31_out);
  not not_106 (CP, or_72_out);
  buf buffer_60 (S1, _2__SDRCOUNT);
  not not_107 (not_107_out, hct193_3_q3);
  Register register_14 (.D(hct299_3_i), .en(not_105_out), .Q(out_36), .clk(_2__PHI2));  // open: clr
  HCT299 hct299_4 (
    .Q7(hct299_4_q7), .Q0(hct299_4_q0), .DSL(1'b1), .nMR(1'b1), .DSR(hct299_4_q0), .S0(1'b1), .S1(S1),
    .CP(CP), .nOE1(1'b1), .nOE2(1'b1), .O(out_36));  // open: I
  D_Flip_Flop d_ff_73 (
    .clk(_2_TAPULSE), .D(d_ff_73_qn), .Qn(d_ff_73_qn), .preset(not_108_out), .reset(not_109_out));  // open: Q
  not not_108 (not_108_out, _2_SDRCOUNT);
  not not_109 (not_109_out, not_110_out);
  nand nand_87 (nand_87_out, out_18[6], _2__RES);
  not not_110 (not_110_out, nand_87_out);
  D_Flip_Flop d_ff_74 (.clk(_2__PHI2), .D(nand_88_out), .Q(d_ff_74_q));  // open: Qn, preset, reset
  D_Flip_Flop S0 (.clk(_1__PHI2), .D(_1_SDRS0), .Q(S0_q), .Qn(S0_qn), .reset(nand_84_out));  // open: preset
  D_Flip_Flop u_S1 (.clk(_1__PHI2), .D(_1_SDRS1), .Q(S1_q), .Qn(_1_SDRCOUNT), .reset(nand_84_out));  // open: preset
  D_Flip_Flop S2 (.clk(_1__PHI2), .D(_1_SDRS2), .Q(_1_SDRLOAD), .Qn(S2_qn), .reset(nand_84_out));  // open: preset
  assign out_16 = not_111_out ? out_36 : 8'bz;  // Controlled_Buffer controlled_buffer_53
  not not_111 (not_111_out, or_69_out);
  not not_112 (not_112_out, out_18[6]);
  or or_73 (or_73_out, hct299_4_q7, not_112_out);
  not not_113 (not_113_out, or_73_out);
  assign _1_SP = not_113_out ? 1'b0 : 1'bz;  // Controlled_Buffer controlled_buffer_54
  not not_114 (not_114_out, d_ff_73_qn);
  assign _1_CNT = not_114_out ? 1'b0 : 1'bz;  // Controlled_Buffer controlled_buffer_55
  assign not_115_out = ~_2_DZ[4:0];  // NOT_Gate not_115, 5 bits wide
  or or_74 (or_74_out, _2_ENABLE_NAND, _2_EN13);
  nand nand_88 (nand_88_out, _2__RES, or_74_out);
  not not_116 (not_116_out, d_ff_75_qn);
  not not_117 (not_117_out, d_ff_75_qn);
  D_Flip_Flop d_ff_75 (.clk(_2__PHI2), .D(d_ff_74_q), .Qn(d_ff_75_qn));  // open: Q, preset, reset
  not not_118 (not_118_out, d_ff_75_qn);
  not not_119 (not_119_out, d_ff_75_qn);
  not not_120 (not_120_out, d_ff_75_qn);
  not not_121 (not_121_out, d_ff_75_qn);
  and and_32 (and_32_out, ~nand_83_out, ~out_17[3], out_17[0]);  // AND_Gate
  and and_33 (and_33_out, not_110_out, out_18[0]);
  HCT193 hct193_4 (
    .Q3(hct193_4_q3), .in_8(1'b0), .D0(1'b0), .D1(1'b0), .CPU(d_ff_73_qn), .CPD(1'b1), .nPL(1'b1),
    .MR(_2__SDRCOUNT), .D2(1'b0));  // open: nTCU, nTCD, Q0, Q1, Q2
  assign nand_89_out = ~(register_15_q & not_115_out);  // NAND_Gate nand_89, 5 bits wide
  assign nand_90_out = ~(_2_DZ[4:0] & {5{_2_DZ[7]}});  // NAND_Gate nand_90, 5 bits wide
  nand nand_91 (nand_91_out, _2__RES, _2_EN13);
  and and_34 (and_34_out, S0_q, not_107_out);
  and and_35 (and_35_out, S1_q, and_32_out, not_107_out);
  and and_36 (and_36_out, not_107_out, S1_q);
  and and_37 (and_37_out, S0_q, hct193_3_q3);
  and and_38 (and_38_out, hct193_3_q3, and_32_out);
  and and_39 (and_39_out, and_32_out, _1_SDRCOUNT);
  and and_40 (and_40_out, S2_qn, S1_q, S0_qn, hct193_3_q3, ~and_32_out);  // AND_Gate
  assign nand_92_out = ~(nand_89_out & nand_90_out);  // NAND_Gate nand_92, 5 bits wide
  nand nand_93 (nand_93_out, nand_91_out, _2_ENABLE_NAND);
  D_Flip_Flop ICR0 (.Q(ICR0_q[0]), .preset(_2_TAPULSE), .reset(not_116_out));  // open: clk, D, Qn
  D_Flip_Flop ICR1 (.Q(ICR0_q[1]), .preset(_2_TBPULSE), .reset(not_117_out));  // open: clk, D, Qn
  D_Flip_Flop ICR2 (.Q(ICR0_q[2]), .preset(_2_TODIRQ), .reset(not_118_out));  // open: clk, D, Qn
  D_Flip_Flop ICR3 (.Q(ICR0_q[3]), .preset(_2_SDRIRQ), .reset(not_119_out));  // open: clk, D, Qn
  D_Flip_Flop ICR4 (.clk(_1__PC), .D(1'b1), .Q(ICR0_q[4]), .reset(not_120_out));  // open: Qn, preset
  D_Flip_Flop ICR7 (.Q(ICR7_q), .preset(or_82_out), .reset(not_121_out));  // open: clk, D, Qn
  or or_75 (_1_SDRS0, and_34_out, and_35_out);
  or or_76 (_1_SDRS1, _1_SDRLOAD, and_36_out);
  or or_77 (_1_SDRS2, and_37_out, and_38_out, and_39_out);
  or or_78 (_1_SDRIRQ, and_40_out, d_ff_66_q);
  not not_122 (not_122_out, nand_86_out);
  D_Flip_Flop S0_2 (.clk(_2__PHI2), .D(_2_SDRS0), .Q(S0_2_q), .reset(not_123_out));  // open: Qn, preset
  not not_123 (not_123_out, and_33_out);
  D_Flip_Flop S1_2 (
    .clk(_2__PHI2), .D(_2_SDRS1), .Q(_2_SDRCOUNT), .Qn(_2__SDRCOUNT), .reset(not_124_out));  // open: preset
  not not_124 (not_124_out, and_33_out);
  not not_125 (not_125_out, hct193_4_q3);
  assign and_41_out = nand_92_out & {5{_2__RES}};  // AND_Gate and_41, 5 bits wide
  D_Flip_Flop d_ff_76 (.clk(_2__PHI2), .D(ICR7_q), .Q(d_ff_76_q[7]), .Qn(d_ff_76_qn));  // open: preset, reset
  and and_42 (and_42_out, _2_SDRCOUNT, S0_2_q);
  and and_43 (and_43_out, _2_SDRCOUNT, not_125_out);
  and and_44 (and_44_out, _2__SDRCOUNT, S0_2_q);
  or or_79 (or_79_out, not_122_out, _2__SDRCOUNT, S0_2_q, not_125_out);
  nand nand_94 (_2_SDRIRQ, or_79_out, d_ff_72_qn);
  Register register_15 (
    .D({3'b000, and_41_out}), .en(not_126_out), .Q({register_15_q_2, register_15_q}), .clk(_2__PHI2));  // open: clr
  not not_126 (not_126_out, nand_93_out);
  or or_80 (_2_SDRS0, and_42_out, not_122_out);
  or or_81 (_2_SDRS1, and_43_out, and_44_out);
  assign and_45_out = register_15_q & ICR0_q;  // AND_Gate and_45, 5 bits wide
  not not_127 (not_127_out, or_74_out);
  assign out_16 = not_127_out ? {d_ff_76_q[7], 2'b00, ICR0_q} : 8'bz;  // Controlled_Buffer controlled_buffer_56
  Register #(.trigger("high")) register_16 (.D({d_ff_76_q[7], 2'b00, ICR0_q}), .clk(1'b1));  // open: en, Q, clr
  not not_128 (not_128_out, d_ff_76_qn);
  assign _2__IRQ = not_128_out ? 1'b0 : 1'bz;  // Controlled_Buffer controlled_buffer_57
  Pull_Resistor #(.pull(1)) pull_resistor_9 (.node(_2__IRQ));
  or or_82 (or_82_out, and_45_out[0], and_45_out[1], and_45_out[2], and_45_out[3], and_45_out[4]);
  // Pins of 7 and 8 bits meet at {out_16[7], 1'b1, out_16[5:0]}

  assign out_8 = out_7;
  assign out_14 = out_13;
  assign out_41 = out_23;
  assign out_44 = out_19;
  assign out_45 = out_21;
  assign out_46 = out_23;
  assign out_47 = out_25;
  assign out_49 = out_27;
  assign out_51 = out_30;
  assign out_52 = out_32;
  assign TBLOAD = out_25[4];

  // Other names for the same wires on the sheet: D[7:0] = out_16; _1_DDRB[7:0] = out_9; _1_PORTBREG[7:0] = out_11;
  //   _2_DDRB[7:0] = out_10; _2_PORTBREG[7:0] = out_12; nCIA = _1__CS; nIRQ = _1__IRQ; _1_ALARMBUS[31:0] = out_39;
  //   _1_CREGA[7:0] = out_17; _1_TASTART = out_17[0]; _1_PB6ON = out_17[1]; _1_TAOUTMODE = out_17[2];
  //   _1_TARUNMODE = out_17[3]; _1_TALOAD = out_17[4]; _1_TAINMODE = out_17[5]; _1_SPMODE = out_17[6];
  //   _1_TODIN = out_17[7]; _1_CREGB[7:0] = out_25; _1_TBSTART = out_25[0]; _1_PB7ON = out_25[1];
  //   _1_TBOUTMODE = out_25[2]; _1_TBLOAD = out_25[4]; _1_TBINMODE0 = out_25[5]; _1_TBINMODE1 = out_25[6];
  //   _1_ALARM = out_25[7]; _1_DDRA[7:0] = out_3; _1_EN14 = EN14; _1_PORTAREG[7:0] = out_5; _1_SDRREG[7:0] = out_35;
  //   _1_TALATCHHI[7:0] = out_21; _1_TALATCHLO[7:0] = out_19; _1_TBLATCHHI[7:0] = out_30; _1_TBLATCHLO[7:0] = out_27;
  //   _1_TBOFDETECT = TBis0; _1_TIMERA[15:0] = out_23; _1_TIMERB[15:0] = out_32; _1_TODBUS[31:0] = out_37;
  //   nCIAEXT = _2__CS; nNMI = _2__IRQ; _2__PC = _1_FLAG; _2_ALARMBUS[31:0] = out_40; _2_CNT = _1_CNT;
  //   _2_CREGA[7:0] = out_18; _2_TASTART = out_18[0]; _2_PB6ON = out_18[1]; _2_TAOUTMODE = out_18[2];
  //   _2_TARUNMODE = out_18[3]; _2_TALOAD = out_18[4]; _2_TAINMODE = out_18[5]; _2_SPMODE = out_18[6];
  //   _2_TODIN = out_18[7]; _2_CREGB[7:0] = out_26; _2_TBSTART = out_26[0]; _2_PB7ON = out_26[1];
  //   _2_TBOUTMODE = out_26[2]; _2_TBLOAD = out_26[4]; _2_TBINMODE0 = out_26[5]; _2_TBINMODE1 = out_26[6];
  //   _2_ALARM = out_26[7]; _2_DDRA[7:0] = out_4; _2_FLAG = _1__PC; _1_PORTA[7:0] = out_7; _2_PORTA[7:0] = out_7;
  //   _2_PORTAREG[7:0] = out_6; _1_PORTB[7:0] = out_13; _2_PORTB[7:0] = out_13; _2_SDRREG[7:0] = out_36;
  //   _2_SP = _1_SP; _2_TALATCHHI[7:0] = out_22; _2_TALATCHLO[7:0] = out_20; _2_TBLATCHHI[7:0] = out_31;
  //   _2_TBLATCHLO[7:0] = out_28; _2_TIMERA[15:0] = out_24; _2_TIMERB[15:0] = out_33; _2_TODBUS[31:0] = out_38;
  //   _1_RS0 = out_15[0]; _2_RS0 = out_15[0]; A[15:0] = out_15; _1_RS1 = out_15[1]; _2_RS1 = out_15[1];
  //   _1_RS2 = out_15[2]; _2_RS2 = out_15[2]; _1_RS3 = out_15[3]; _2_RS3 = out_15[3]; _2_TOD = _1_TOD; TOD = _1_TOD

  // Notes on the sheet:
  //   PHI0
  //   addr
  //   PHI1
  //   PHI2
  //   R/W
  //   SYNC
  //   INPUT/OUTPUT
  //   INPUT/OUTPUT
  //   ADDR.DECODER
  //   ADDR.DECODER
  //   DDRA PORTA
  //   DDRB PORTB
  //   DDRA PORTA
  //   DDRB PORTB
  //   CREGA TIMERA
  //   CREGA TIMERA
  //   PHI_8
  //   CREGB TIMERB
  //   CREGB TIMERB
  //   TOD
  //   SDR
  //   TOD
  //   ICR
  //   SDR
  //   ICR
  //   LATCH
endmodule

module memDecoder (
  input  [15:0] A,
  input  PHI2,
  input  R_W,
  output TOD,
  output OE,
  output WE,
  output nCIA,
  output nCIAEXT,
  output TERM,
  output nCIARES
);

  wire and_1_out, and_3_out, decoder_1_out2, decoder_2_out1, decoder_2_out3, decoder_2_out4, decoder_3_out1,
       decoder_3_out3, nand_1_out, not_2_out;
  wire [0:0] not_1_out;

  and and_1 (and_1_out, A[15], ~A[14]);  // AND_Gate
  not not_1 (not_1_out[0], PHI2);
  Decoder #(.enable("false"), .select(2)) decoder_1 (.out2(decoder_1_out2), .sel(A[15:14]));  // open: out0, out1, out3
  Decoder #(.select(3)) decoder_2 (
    .out0(TOD), .out1(decoder_2_out1), .out3(decoder_2_out3), .out4(decoder_2_out4), .sel(A[13:11]),
    .en(and_1_out));  // open: out2, out5, out6, out7
  Decoder #(.select(2)) decoder_3 (
    .out0(WE), .out1(decoder_3_out1), .out2(OE), .out3(decoder_3_out3), .sel({R_W, not_1_out[0]}),
    .en(not_2_out));
  not not_2 (not_2_out, decoder_1_out2);
  not not_3 (nCIA, decoder_2_out1);
  not not_4 (nCIAEXT, decoder_2_out3);
  and and_2 (TERM, ~A[12], A[13], ~A[14], A[15], PHI2);  // AND_Gate
  and and_3 (and_3_out, A[12], A[13], ~A[14], A[15], PHI2);  // AND_Gate
  not not_5 (nCIARES, and_3_out);
  // AND_Gate and_4 has open pins: in0=A[0], in1=PHI2, in2=decoder_2_out4, out=open
  nand nand_1 (nand_1_out, A[0], decoder_2_out4);

  // Notes on the sheet:
  //   A0
  //   A0
endmodule
