// Logisim project tem.circ as structural Verilog: 2 circuits, main circuit sbc6526
module sbc6526 (
  output EN14
);

  wire _1__PHI2, _1__RES, _1_CNT, _1_EN4, _1_EN5, _1_ENABLE_NAND, _1_OETAHI, _1_OETALO, _1_PB6ON, _1_PHI2,
       _1_SPMODE, _1_TADECREMENT, _1_TAFL, _1_TAINMODE, _1_TALOAD, _1_TALOADPULSE, _1_TAOFDETECT, _1_TAOUT,
       _1_TAOUTMODE, _1_TAPULSE, _1_TARUNMODE, _1_TASTART, _1_TAUNDERFLOW, _1_TODIN, _1_WETAHI, _1_WETALO,
       and_1_out, and_2_out, and_3_out, buffer_1_out, buffer_2_out, buffer_3_out, buffer_4_out, buffer_5_out,
       buffer_6_out, buffer_7_out, buffer_8_out, buffer_10_out, d_ff_1_q, d_ff_2_q, d_ff_6_qn, d_ff_7_q,
       d_ff_8_qn, d_ff_9_qn, d_ff_10_q, d_ff_11_qn, multiplexer_1_out, nand_1_out, nand_2_out, nand_3_out,
       nand_4_out, nand_7_out, nor_1_out, not_1_out, not_2_out, not_3_out, not_4_out, not_5_out, not_6_out,
       not_7_out, not_8_out, not_9_out, not_10_out, not_11_out, nRESc, or_1_out, or_4_out, PHI2c;
  wire [4:0] register_1_q;
  wire [7:0] _1_DO, _1_DZ, _1_TALATCHHI, _1_TALATCHLO, D;
  wire [7:7] not_12_out;

  nand nand_1 (nand_1_out, EN14, _1__RES);
  or or_1 (or_1_out, _1_ENABLE_NAND, EN14);
  nand nand_2 (nand_2_out, _1__RES, _1_EN4);
  nand nand_3 (nand_3_out, _1__RES, _1_EN5);
  or or_2 (_1_OETALO, _1_EN4, _1_ENABLE_NAND);
  or or_3 (_1_OETAHI, _1_EN5, _1_ENABLE_NAND);
  buf buffer_1 (buffer_1_out, _1_DZ[0]);
  buf buffer_2 (buffer_2_out, buffer_1_out);
  buf buffer_3 (buffer_3_out, buffer_2_out);
  buf buffer_4 (buffer_4_out, buffer_3_out);
  buf buffer_5 (buffer_5_out, _1_DZ[4]);
  buf buffer_6 (buffer_6_out, buffer_5_out);
  buf buffer_7 (buffer_7_out, buffer_6_out);
  buf buffer_8 (buffer_8_out, buffer_7_out);
  nand nand_4 (nand_4_out, nand_1_out, _1_ENABLE_NAND);
  not not_1 (not_1_out, nand_4_out);
  and and_1 (and_1_out, not_1_out, _1__PHI2);
  not not_2 (not_2_out, _1__PHI2);
  nand nand_5 (_1_WETALO, nand_2_out, _1_ENABLE_NAND);
  nand nand_6 (_1_WETAHI, _1_ENABLE_NAND, nand_3_out);
  not not_3 (not_3_out, nand_4_out);
  D_Flip_Flop d_ff_1 (.clk(and_1_out), .D(buffer_8_out), .Q(d_ff_1_q), .reset(not_2_out));  // open: Qn, preset
  D_Flip_Flop d_ff_2 (.clk(not_2_out), .D(_1_TARUNMODE), .Q(d_ff_2_q));  // open: Qn, preset, reset
  Register register_1 (
    .D({_1_DZ[7:5], 1'b0, _1_DZ[3:1], 1'b0}), .en(not_3_out),
    .Q({_1_TODIN, _1_SPMODE, _1_TAINMODE, register_1_q[4], _1_TARUNMODE, _1_TAOUTMODE, _1_PB6ON, register_1_q[0]}),
    .clk(_1__PHI2));  // open: clr
  D_Flip_Flop d_ff_3 (.clk(and_1_out), .D(buffer_4_out), .Q(_1_TASTART), .reset(and_2_out));  // open: Qn, preset
  D_Flip_Flop d_ff_4 (.clk(not_2_out), .D(d_ff_1_q), .Q(_1_TALOAD));  // open: Qn, preset, reset
  or or_4 (or_4_out, d_ff_2_q, _1_TARUNMODE);
  and and_2 (and_2_out, or_4_out, _1_TAUNDERFLOW);
  not not_4 (not_4_out, _1_TAFL);
  assign D = not_5_out ? {_1_TODIN, _1_SPMODE, _1_TAINMODE, register_1_q[4], _1_TARUNMODE, _1_TAOUTMODE, _1_PB6ON, _1_TASTART} : 8'bz;  // Controlled_Buffer controlled_buffer_1
  not not_5 (not_5_out, or_1_out);
  Register register_2 (.D(_1_DO), .en(not_6_out), .Q(_1_TALATCHLO), .clk(_1__PHI2));  // open: clr
  not not_6 (not_6_out, _1_WETALO);
  Register register_3 (.D(_1_DO), .en(not_7_out), .Q(_1_TALATCHHI), .clk(_1__PHI2));  // open: clr
  not not_7 (not_7_out, _1_WETAHI);
  D_Flip_Flop d_ff_5 (.clk(_1__PHI2), .D(1'b1), .Q(_1_TALOADPULSE), .reset(not_4_out));  // open: Qn, preset
  D_Flip_Flop d_ff_6 (.clk(_1_CNT), .D(1'b1), .Qn(d_ff_6_qn), .reset(not_8_out));  // open: Q, preset
  not not_8 (not_8_out, d_ff_6_qn);
  not not_9 (not_9_out, d_ff_6_qn);
  D_Flip_Flop d_ff_7 (.clk(_1_PHI2), .D(1'b0), .Q(d_ff_7_q), .preset(not_9_out));  // open: Qn, reset
  D_Flip_Flop d_ff_8 (.clk(_1_PHI2), .D(d_ff_7_q), .Qn(d_ff_8_qn));  // open: Q, preset, reset
  D_Flip_Flop d_ff_9 (.clk(_1_PHI2), .D(1'b0), .Q(_1_TAPULSE), .Qn(d_ff_9_qn), .preset(_1_TAUNDERFLOW));  // open: reset
  D_Flip_Flop d_ff_10 (.clk(_1_TASTART), .D(1'b1), .Q(d_ff_10_q), .reset(_1_PHI2));  // open: Qn, preset
  nand nand_7 (nand_7_out, _1_TAINMODE, d_ff_8_qn);
  D_Flip_Flop d_ff_11 (
    .clk(_1_TAPULSE), .D(d_ff_11_qn), .Qn(d_ff_11_qn), .preset(d_ff_10_q), .reset(not_10_out));  // open: Q
  not not_10 (not_10_out, _1__RES);
  and and_3 (and_3_out, _1_TASTART, nand_7_out);
  not not_11 (not_11_out, _1_TAFL);
  timer16 timer16_1 (
    .UNDERFLOW(_1_TAOFDETECT), .Q(D), .PULSE(_1_PHI2), .DECREMENT(_1_TADECREMENT),
    .FORCELOAD(_1_TALOADPULSE), .nRES(_1__RES), .LO(_1_TALATCHLO), .HI(_1_TALATCHHI), .nOELO(_1_OETALO),
    .nOEHI(_1_OETAHI));  // open: TIMER
  Multiplexer #(.enable("false")) multiplexer_1 (
    .in0(d_ff_9_qn), .in1(d_ff_11_qn), .out(multiplexer_1_out), .sel(_1_TAOUTMODE));
  D_Flip_Flop d_ff_12 (.clk(_1_PHI2), .D(and_3_out), .Q(_1_TADECREMENT), .reset(not_11_out));  // open: Qn, preset
  and and_4 (_1_TAUNDERFLOW, _1_TADECREMENT, _1_TAOFDETECT);
  nor nor_1 (nor_1_out, _1_TASTART, _1_WETAHI, 1'b0);
  buf buffer_9 (_1__RES, nRESc);
  not not_12 (not_12_out[7], _1__RES);
  buf buffer_10 (buffer_10_out, PHI2c);
  not not_13 (_1__PHI2, buffer_10_out);
  not not_14 (_1_TAOUT, multiplexer_1_out);
  nor nor_2 (_1_TAFL, _1_TAUNDERFLOW, _1_TALOAD, nor_1_out);
  assign _1_DO = D | {8{not_12_out[7]}};  // OR_Gate or_5, 8 bits wide

  // Other names for the same wires on the sheet: _1_EN14 = EN14
endmodule

module memDecoder (
  input  [15:0] A,
  input  R_W,
  input  PHI2,
  output OE,
  output WE,
  output nCIA,
  output TERM,
  output nCIARES,
  output nCIAEXT
);

  wire and_1_out, decoder_1_out2, decoder_2_out1, decoder_2_out3, decoder_2_out4, decoder_3_out1,
       decoder_3_out3, not_2_out;
  wire [0:0] not_1_out;

  and and_1 (and_1_out, A[15], ~A[14]);  // AND_Gate
  not not_1 (not_1_out[0], PHI2);
  Decoder #(.enable("false"), .select(2)) decoder_1 (.out2(decoder_1_out2), .sel(A[15:14]));  // open: out0, out1, out3
  Decoder #(.select(3)) decoder_2 (
    .out1(decoder_2_out1), .out3(decoder_2_out3), .out4(decoder_2_out4), .sel(A[13:11]), .en(and_1_out));  // open: out0, out2, out5, out6, out7
  Decoder #(.select(2)) decoder_3 (
    .out0(WE), .out1(decoder_3_out1), .out2(OE), .out3(decoder_3_out3), .sel({R_W, not_1_out[0]}),
    .en(not_2_out));
  not not_2 (not_2_out, decoder_1_out2);
  not not_3 (nCIA, decoder_2_out1);
  not not_4 (nCIAEXT, decoder_2_out3);
  and and_2 (TERM, ~A[0], PHI2, decoder_2_out4);  // AND_Gate
  nand nand_1 (nCIARES, A[0], decoder_2_out4);
endmodule
